// Logisim project NSU-2023-T04L2e01.circ as structural Verilog: 1 circuit, main circuit OR3
module OR3 (
  input  A,
  input  B,
  input  C,
  output R
);

  wire transistor_1_out, transistor_2_out;

  Transistor transistor_1 (.in(1'b1), .out(transistor_1_out), .gate(A));
  Transistor transistor_2 (.in(transistor_1_out), .out(transistor_2_out), .gate(B));
  Transistor transistor_3 (.in(transistor_2_out), .out(R), .gate(C));
  Transistor #(.\type ("n")) transistor_4 (.in(1'b0), .out(transistor_1_out), .gate(A));
  Transistor #(.\type ("n")) transistor_5 (.in(1'b0), .out(transistor_2_out), .gate(B));
  Transistor #(.\type ("n")) transistor_6 (.in(1'b0), .out(R), .gate(C));
endmodule
