// Logisim project NSU-2023-T04L2e02.circ as structural Verilog: 1 circuit, main circuit formula
module formula (
  input  A,
  input  B,
  input  C,
  output R
);

  wire pull_resistor_1_node, pull_resistor_2_node;

  Pull_Resistor #(.pull(1)) pull_resistor_1 (.node(pull_resistor_1_node));
  Transistor transistor_1 (.in(C), .out(pull_resistor_1_node), .gate(B));
  Pull_Resistor pull_resistor_2 (.node(pull_resistor_2_node));
  Transistor #(.\type ("n")) transistor_2 (.in(pull_resistor_1_node), .out(pull_resistor_2_node), .gate(A));
  Pull_Resistor pull_resistor_3 (.node(R));
  Transistor transistor_3 (.in(1'b1), .out(R), .gate(pull_resistor_2_node));
endmodule
