// Logisim project NSU-2023-T05L2e03.circ as structural Verilog: 2 circuits, main circuit formula
module formula (
  input  [7:0] A,
  output [7:0] R,
  output OFL
);

  wire halfadder_1_out_of, halfadder_2_out_of, halfadder_3_out_of, halfadder_4_out_of, halfadder_5_out_of,
       halfadder_6_out_of, halfadder_7_out_of;

  // AND_Gate and_1 is placed but not wired
  halfadder halfadder_1 (.in_2(1'b0), .in_3(A[0]), .in_1(1'b0), .out_main(R[0]), .out_of(halfadder_1_out_of));
  halfadder halfadder_2 (
    .in_2(1'b0), .in_3(A[1]), .in_1(halfadder_1_out_of), .out_main(R[1]), .out_of(halfadder_2_out_of));
  halfadder halfadder_3 (
    .in_2(A[0]), .in_3(A[2]), .in_1(halfadder_2_out_of), .out_main(R[2]), .out_of(halfadder_3_out_of));
  halfadder halfadder_4 (
    .in_2(A[1]), .in_3(A[3]), .in_1(halfadder_3_out_of), .out_main(R[3]), .out_of(halfadder_4_out_of));
  halfadder halfadder_5 (
    .in_2(A[2]), .in_3(A[4]), .in_1(halfadder_4_out_of), .out_main(R[4]), .out_of(halfadder_5_out_of));
  halfadder halfadder_6 (
    .in_2(A[3]), .in_3(A[5]), .in_1(halfadder_5_out_of), .out_main(R[5]), .out_of(halfadder_6_out_of));
  halfadder halfadder_7 (
    .in_2(A[4]), .in_3(A[6]), .in_1(halfadder_6_out_of), .out_main(R[6]), .out_of(halfadder_7_out_of));
  halfadder halfadder_8 (.in_2(A[5]), .in_3(A[7]), .in_1(halfadder_7_out_of), .out_main(R[7]), .out_of(OFL));
endmodule

module halfadder (
  input  in_1,
  input  in_2,
  input  in_3,
  output out_main,
  output out_of
);

  wire and_1_out, and_2_out, and_3_out, xor_1_out;

  and and_1 (and_1_out, in_3, in_2);
  xor xor_1 (xor_1_out, in_2, in_3);
  and and_2 (and_2_out, in_3, in_1);
  or or_1 (out_of, and_1_out, and_2_out, and_3_out);
  xor xor_2 (out_main, in_1, xor_1_out);
  and and_3 (and_3_out, in_1, in_2);
endmodule
