// Logisim project NSU-2023-T05L2e04.circ as structural Verilog: 2 circuits, main circuit mult4x4
module mult4x4 (
  input  [3:0] A,
  input  [3:0] B,
  output [7:0] R
);

  wire [3:0] and_1_out, and_2_out, and_3_out, and_4_out;
  wire [7:0] summator_1_sum, summator_2_sum;

  assign and_1_out = A & {4{B[0]}};  // AND_Gate and_1, 4 bits wide
  assign and_2_out = A & {4{B[1]}};  // AND_Gate and_2, 4 bits wide
  assign and_3_out = A & {4{B[2]}};  // AND_Gate and_3, 4 bits wide
  assign and_4_out = A & {4{B[3]}};  // AND_Gate and_4, 4 bits wide
  summator summator_1 (.A({4'b0000, and_1_out}), .B({3'b000, and_2_out, 1'b0}), .sum(summator_1_sum));  // open: Cout
  summator summator_2 (.A(summator_1_sum), .B({2'b00, and_3_out, 2'b00}), .sum(summator_2_sum));  // open: Cout
  summator summator_3 (.A(summator_2_sum), .B({1'b0, and_4_out, 3'b000}), .sum(R));  // open: Cout
endmodule

module summator (
  input  [7:0] A,
  input  [7:0] B,
  output [7:0] sum,
  output Cout
);

  wire [6:0] or_1_out;
  wire [7:0] and_1_out, and_2_out, and_3_out;

  assign and_1_out = A & B;  // AND_Gate and_1, 8 bits wide
  assign and_2_out = B & {or_1_out, 1'b0};  // AND_Gate and_2, 8 bits wide
  assign and_3_out = A & {or_1_out, 1'b0};  // AND_Gate and_3, 8 bits wide
  assign {Cout, or_1_out} = and_1_out | and_2_out | and_3_out;  // OR_Gate or_1, 8 bits wide
  assign sum = A ^ {or_1_out, 1'b0} ^ B;  // XOR_Gate xor_1, 8 bits wide
endmodule
