// Logisim project NSU-2023-T05L3e01.circ as structural Verilog: 1 circuit, main circuit ALU
module ALU (
  input  Cin,
  input  [7:0] A,
  input  [7:0] B,
  input  [1:0] instr,
  output [7:0] R,
  output Cout,
  output V
);

  wire and_16_out, and_17_out, not_2_out, not_3_out, not_4_out, not_5_out, not_6_out, not_7_out, not_8_out,
       or_2_out, or_7_out, or_8_out, undriven, undriven_2, xnor_1_out, xor_2_out, xor_4_out, xor_5_out;
  wire [6:0] or_6_out;
  wire [7:0] and_2_out, and_7_out, and_8_out, and_9_out, and_10_out, and_11_out, and_12_out, and_13_out,
       and_14_out, not_1_out, or_1_out, or_3_out, or_4_out, xor_1_out, xor_3_out;
  wire [7:1] and_1_out;
  wire [7:7] and_1_out_2, and_3_out, and_4_out, and_5_out, and_6_out;

  // Probe on A
  // Probe on B
  assign not_1_out = ~B;  // NOT_Gate not_1, 8 bits wide
  // Probe on R
  // Probe on R
  not not_2 (not_2_out, instr[0]);
  not not_3 (not_3_out, instr[1]);
  assign {and_1_out_2[7], and_1_out} = {and_1_out, 1'b1} & not_1_out;  // AND_Gate and_1, 8 bits wide
  assign xor_1_out = not_1_out ^ {and_1_out, 1'b1};  // XOR_Gate xor_1, 8 bits wide
  assign and_2_out = A & B;  // AND_Gate and_2, 8 bits wide
  assign or_1_out = A | B;  // OR_Gate or_1, 8 bits wide
  and and_3 (and_3_out[7], not_2_out, not_3_out);
  and and_4 (and_4_out[7], not_3_out, instr[0]);
  and and_5 (and_5_out[7], not_2_out, instr[1]);
  and and_6 (and_6_out[7], instr[1], instr[0]);
  or or_2 (or_2_out, and_5_out[7], and_6_out[7]);
  assign and_7_out = {8{and_5_out[7]}} & B;  // AND_Gate and_7, 8 bits wide
  assign and_8_out = {8{and_6_out[7]}} & xor_1_out;  // AND_Gate and_8, 8 bits wide
  assign or_3_out = {8{and_6_out[7]}} | {8{and_5_out[7]}};  // OR_Gate or_3, 8 bits wide
  assign or_4_out = and_7_out | and_8_out;  // OR_Gate or_4, 8 bits wide
  xor xor_2 (xor_2_out, A[7], or_4_out[7]);
  assign and_9_out = A & or_4_out;  // AND_Gate and_9, 8 bits wide
  assign and_10_out = or_4_out & {or_6_out, Cin};  // AND_Gate and_10, 8 bits wide
  assign and_11_out = A & {or_6_out, Cin};  // AND_Gate and_11, 8 bits wide
  assign and_12_out = and_2_out & {8{and_3_out[7]}};  // AND_Gate and_12, 8 bits wide
  assign and_13_out = or_1_out & {8{and_4_out[7]}};  // AND_Gate and_13, 8 bits wide
  assign and_14_out = or_3_out & xor_3_out;  // AND_Gate and_14, 8 bits wide
  // Probe on R
  assign R = and_12_out | and_13_out | and_14_out;  // OR_Gate or_5, 8 bits wide
  assign xor_3_out = A ^ {or_6_out, Cin} ^ or_4_out;  // XOR_Gate xor_3, 8 bits wide
  assign {Cout, or_6_out} = and_9_out | and_10_out | and_11_out;  // OR_Gate or_6, 8 bits wide
  not not_4 (not_4_out, or_4_out[7]);
  not not_5 (not_5_out, A[7]);
  not xnor_1 (xnor_1_out, undriven);  // XNOR_Gate
  and and_15 (V, or_2_out, not_6_out, or_8_out);
  not not_6 (not_6_out, xor_2_out);
  not not_7 (not_7_out, or_6_out[6]);
  and and_16 (and_16_out, or_4_out[7], A[7]);
  and and_17 (and_17_out, not_4_out, not_5_out);
  or or_7 (or_7_out, xnor_1_out, not_8_out);
  xor xor_4 (xor_4_out, or_6_out[6], and_16_out);
  or or_8 (or_8_out, xor_4_out, xor_5_out);
  xor xor_5 (xor_5_out, not_7_out, and_17_out);
  not not_8 (not_8_out, undriven_2);

  // Notes on the sheet:
  //   00: and
  //   01: or
  //   10: add
  //   11: sub
endmodule
