// Logisim project NSU-2023-T06L1e01.circ as structural Verilog: 1 circuit, main circuit fib32
module fib32 (
  input  clock,
  output [31:0] a,
  output [5:0] k,
  output stop
);

  wire t_ff_1_q, t_ff_1_qn, undriven;
  wire [5:0] adder_2_out, bit_extender_1_out;
  wire [31:0] adder_1_out, bit_extender_2_out, controlled_buffer_1_out, register_2_q;

  T_Flip_Flop t_ff_1 (.clk(clock), .T(t_ff_1_qn), .Q(t_ff_1_q), .Qn(t_ff_1_qn), .reset(undriven));  // open: preset, en
  assign controlled_buffer_1_out = t_ff_1_qn ? bit_extender_2_out : 32'bz;  // Controlled_Buffer controlled_buffer_1
  assign controlled_buffer_1_out = t_ff_1_q ? adder_1_out : 32'bz;  // Controlled_Buffer controlled_buffer_2
  Register #(.width(32)) register_1 (.D(controlled_buffer_1_out), .Q(a), .clk(clock), .clr(undriven));  // open: en
  Register #(.width(32)) register_2 (.D(a), .Q(register_2_q), .clk(clock), .clr(undriven));  // open: en
  assign bit_extender_1_out = {{5{1'b0}}, 1'b1};  // Bit_Extender bit_extender_1
  Adder #(.width(32)) adder_1 (.a(a), .b(register_2_q), .out(adder_1_out));  // open: cin, cout
  Register #(.width(6)) register_3 (.D(adder_2_out), .Q(k), .clk(clock), .clr(undriven));  // open: en
  assign bit_extender_2_out = {{31{1'b0}}, 1'b1};  // Bit_Extender bit_extender_2
  Adder #(.width(6)) adder_2 (.a(bit_extender_1_out), .b(k), .out(adder_2_out));  // open: cin, cout
  // Probe on a
  // Probe on k

  assign stop = a[31];
endmodule
