// Logisim project NSU-2023-T06L1e02.circ as structural Verilog: 2 circuits, main circuit solution
module solution (
  input  [7:0] A,
  input  set,
  input  [7:0] B,
  input  clock,
  output [7:0] GCD,
  output done
);

  wire and_1_out, and_2_out, comparator_1_eq, comparator_1_gt, comparator_1_lt, nor_1_out, t_ff_1_q,
       t_ff_1_qn, t_ff_2_q, t_ff_2_qn;
  wire [7:0] bit_extender_1_out, multiplexer_1_out, multiplexer_2_out, multiplexer_3_out, multiplexer_4_out,
       or_1_out, register_1_q, register_2_q, subtractor_1_out, subtractor_2_out;

  // Probe on A
  // Probe on B
  T_Flip_Flop t_ff_1 (.clk(and_1_out), .T(t_ff_1_qn), .Q(t_ff_1_q), .Qn(t_ff_1_qn));  // open: preset, reset, en
  T_Flip_Flop t_ff_2 (.clk(set), .T(t_ff_2_qn), .Q(t_ff_2_q), .Qn(t_ff_2_qn));  // open: preset, reset, en
  Multiplexer #(.width(8)) multiplexer_1 (
    .in0(A), .in1(multiplexer_3_out), .out(multiplexer_1_out), .sel(t_ff_1_q));  // open: en
  Multiplexer #(.width(8)) multiplexer_2 (
    .in0(B), .in1(multiplexer_4_out), .out(multiplexer_2_out), .sel(t_ff_1_q));  // open: en
  and and_1 (and_1_out, t_ff_2_q, clock);
  Register register_1 (.D(multiplexer_1_out), .Q(register_1_q), .clk(clock));  // open: en, clr
  Register register_2 (.D(multiplexer_2_out), .Q(register_2_q), .clk(clock));  // open: en, clr
  // Probe on register_1_q
  // Probe on register_2_q
  Multiplexer #(.width(8)) multiplexer_3 (
    .in0(register_1_q), .in1(subtractor_1_out), .out(multiplexer_3_out), .sel(comparator_1_gt));  // open: en
  Comparator #(.mode("unsigned")) comparator_1 (
    .a(register_1_q), .b(register_2_q), .gt(comparator_1_gt), .eq(comparator_1_eq), .lt(comparator_1_lt));
  Multiplexer #(.width(8)) multiplexer_4 (
    .in0(register_2_q), .in1(subtractor_2_out), .out(multiplexer_4_out), .sel(comparator_1_lt));  // open: en
  assign or_1_out = register_2_q | register_1_q;  // OR_Gate or_1, 8 bits wide
  Subtractor subtractor_1 (.a(register_1_q), .b(register_2_q), .out(subtractor_1_out));  // open: bin, bout
  Subtractor subtractor_2 (.a(register_2_q), .b(register_1_q), .out(subtractor_2_out));  // open: bin, bout
  assign bit_extender_1_out = {{7{1'b0}}, 1'b1};  // Bit_Extender bit_extender_1
  and and_2 (and_2_out, comparator_1_eq, t_ff_1_q);
  Multiplexer #(.width(8)) multiplexer_5 (
    .in0(register_2_q), .in1(bit_extender_1_out), .out(GCD), .sel(nor_1_out));  // open: en
  nor nor_1 (nor_1_out, or_1_out[0], or_1_out[1], or_1_out[2], or_1_out[3], or_1_out[5], or_1_out[6], or_1_out[7], or_1_out[4]);
  // Probe on GCD
  or or_2 (done, and_2_out, t_ff_2_qn);
endmodule

module stopper (
  input  run_prime,
  input  stop,
  input  clock_in,
  output clock_out
);

  wire multiplexer_1_out, not_1_out, or_1_out, register_1_q;

  not not_1 (not_1_out, stop);
  Multiplexer #(.enable("false")) multiplexer_1 (
    .in0(not_1_out), .in1(run_prime), .out(multiplexer_1_out), .sel(run_prime));
  or or_1 (or_1_out, run_prime, register_1_q);
  Register #(.width(1), .trigger("falling")) register_1 (
    .D(multiplexer_1_out), .en(or_1_out), .Q(register_1_q), .clk(clock_in));  // open: clr
  and and_1 (clock_out, register_1_q, clock_in);
endmodule
