// Logisim project 022.main (add 3 presets).circ as structural Verilog: 26 circuits, main circuit main
// CDM8
module main (
  input  clock,
  input  [7:0] KeyBoard,
  output [15:0] i__row,
  output [15:0] j__column,
  output KB_lamp,
  output torus,
  output [1:0] state,
  output pause,
  output clear,
  output enable
);

  wire _0xFD, _0xFF, adr____0xF8_2_out, adr____0xF8_out, adr____0xFA_out, adr____0xFC_out, adr____0xFE_out,
       and_4_out, and_5_out, and_6_out, mem, noRAM, not_1_out, not_2_out, not_3_out, or_1_out, or_2_out, RAM,
       read, reset;
  wire [6:5] state_t;
  wire [7:0] addressBus, cdm_8_mark5_1_data_out, cdm_8_mark5_1_pc, cdm_8_mark5_1_ps, cdm_8_mark5_1_r0,
       cdm_8_mark5_1_r1, cdm_8_mark5_1_r2, cdm_8_mark5_1_r3, cdm_8_mark5_1_sp, controlled_buffer_2_out,
       dataBus, ram_1_data, RAMDataBus;
  wire [15:0] j, toRegi, toRegj;

  // Probe on cdm_8_mark5_1_r1
  // Probe on cdm_8_mark5_1_r0
  // Probe on cdm_8_mark5_1_pc
  // Probe on cdm_8_mark5_1_sp
  // Probe on cdm_8_mark5_1_r2
  // Probe on cdm_8_mark5_1_r3
  Button u_reset (.out(reset));
  // Probe on cdm_8_mark5_1_ps
  CdM_8_mark5 cdm_8_mark5_1 (
    .clock(clock), .addr(addressBus), .mem_read(read), .mem_cycle(mem), .data_out(cdm_8_mark5_1_data_out),
    .data_in(controlled_buffer_2_out), .r0(cdm_8_mark5_1_r0), .r1(cdm_8_mark5_1_r1), .r2(cdm_8_mark5_1_r2),
    .r3(cdm_8_mark5_1_r3), .PC(cdm_8_mark5_1_pc), .SP(cdm_8_mark5_1_sp), .PS(cdm_8_mark5_1_ps),
    .reset__by_Hom4ik(reset));  // open: data_inst, IAck, IRQ, vec
  assign dataBus = not_1_out ? cdm_8_mark5_1_data_out : 8'bz;  // Controlled_Buffer controlled_buffer_1
  not not_1 (not_1_out, read);
  assign controlled_buffer_2_out = read ? dataBus : 8'bz;  // Controlled_Buffer controlled_buffer_2
  reverse16Bits reverse16bits_1 (.in(j), .out(j__column));
  // Probe on dataBus
  // Probe on addressBus
  RAM ram_1 (.addr(addressBus), .data(ram_1_data), .sel(RAM), .clk(clock), .ld(read));  // open: clr
  and adr____0xF8 (adr____0xF8_out, addressBus[3], addressBus[4], addressBus[5], addressBus[6], addressBus[7]);
  assign RAMDataBus = read ? ram_1_data : 8'bz;  // Controlled_Buffer controlled_buffer_3
  assign ram_1_data = not_2_out ? dataBus : 8'bz;  // Controlled_Buffer controlled_buffer_4
  not not_2 (not_2_out, read);
  and and_1 (RAM, mem, ~adr____0xF8_out);  // AND_Gate
  and and_2 (noRAM, adr____0xF8_out, mem);
  and and_3 (KB_lamp, mem, adr____0xF8_2_out);
  and adr____0xF8_2 (adr____0xF8_2_out, ~addressBus[0], ~addressBus[1], ~addressBus[2], noRAM);  // AND_Gate
  and adr____0xFA (adr____0xFA_out, ~addressBus[0], addressBus[1], ~addressBus[2], noRAM);  // AND_Gate
  and adr____0xFC (adr____0xFC_out, ~addressBus[0], ~addressBus[1], addressBus[2], noRAM);  // AND_Gate
  or or_1 (or_1_out, adr____0xFC_out, _0xFD);
  and adr____0xFD (_0xFD, addressBus[0], ~addressBus[1], noRAM);  // AND_Gate
  and adr____0xFE (adr____0xFE_out, ~addressBus[0], addressBus[1], addressBus[2], noRAM);  // AND_Gate
  or or_2 (or_2_out, adr____0xFE_out, _0xFF);
  and adr____0xFF (_0xFF, addressBus[0], addressBus[1], addressBus[2], noRAM);
  Multiplexer #(.width(8)) multiplexer_1 (
    .in0(RAMDataBus), .in1(KeyBoard), .out(dataBus), .sel(adr____0xF8_2_out), .en(read));
  and and_4 (and_4_out, adr____0xFA_out, ~read);  // AND_Gate
  and and_5 (and_5_out, or_1_out, ~read);  // AND_Gate
  and and_6 (and_6_out, or_2_out, ~read);  // AND_Gate
  Register register_1 (
    .D(dataBus), .en(and_4_out), .Q({enable, state_t, clear, pause, state, torus}), .clk(clock), .clr(reset));
  Register #(.width(16)) register_2 (.D(toRegi), .en(and_5_out), .Q(i__row), .clk(clock), .clr(reset));
  Register #(.width(16), .trigger("falling")) register_3 (.D(toRegj), .en(and_6_out), .Q(j), .clk(clock), .clr(reset));
  // Probe on dataBus
  // Probe on dataBus
  // Probe on toRegi
  Multiplexer #(.width(16), .enable("false")) multiplexer_2 (
    .in0({dataBus, i__row[7:0]}), .in1({i__row[15:8], dataBus}), .out(toRegi), .sel(_0xFD));
  // Probe on toRegj
  Multiplexer #(.width(16), .enable("false")) multiplexer_3 (
    .in0({dataBus, j[7:0]}), .in1({j[15:8], dataBus}), .out(toRegj), .sel(_0xFF));
  not not_3 (not_3_out, not_3_out);

  // Other names for the same wires on the sheet: i[15:0] = i__row; KB_out[7:0] = KeyBoard;
  //   state_t (some bits) = {enable, clear, pause, state, torus}

  // Notes on the sheet:
  //   load STATE (from CPU)
  //   store KeyBoard's data to CPU
  //   if the "read" option is disabled (↑), plexer won't work
  //   load i-cursor (need x2 operations)
  //   load j-cursor (need x2 operations)
  //   load i-cursor (high part) from CPU
  //   load i-cursor (low part) from CPU
  //   load j-cursor (high part) from CPU
  //   load j-cursor (low part) from CPU
endmodule

module mainCDM16__not_used (
  input  [4:0] minus_2_line,
  input  [5:0] num_1,
  input  [5:0] num_1_2,
  input  [4:0] minus_1_line,
  input  [5:0] num_2,
  input  [5:0] num_2_2,
  input  [4:0] cur_line,
  input  [5:0] num_3,
  input  [5:0] num_3_2,
  input  [4:0] plus_1_line,
  input  [5:0] num_4,
  input  [5:0] num_4_2,
  input  [4:0] plus_2_line,
  input  [5:0] num_5,
  input  [5:0] num_5_2,
  input  [5:0] num_6,
  input  [5:0] num_6_2,
  input  [5:0] B__S
);

  wire cdm16_1_p1, cdm16_1_p2, cdm16_1_p4, cdm16_1_p5, cdm16_1_p6, cdm16_1_p7, cdm16_1_p8, cdm16_1_p9,
       cdm16_1_p10, cdm16_1_p11, cdm16_1_p12, clock, mem, not_1_out, read, word;
  wire [15:0] address_bus, cdm16_1_p17, cdm16_1_p18, data_bus;
  wire [29:0] birth, save;

  // Probe on cdm16_1_p1
  // Probe on cdm16_1_p2
  Clock clock_1 (.out(clock));
  // Probe on cdm16_1_p5
  // Probe on cdm16_1_p4
  // Probe on cdm16_1_p7
  // Probe on cdm16_1_p6
  // cdm16 cdm16_1: pin names not known; wires that end beside it: cdm16_1_p1, cdm16_1_p2, clock, cdm16_1_p4, cdm16_1_p5, cdm16_1_p6, cdm16_1_p7, cdm16_1_p8, cdm16_1_p9, cdm16_1_p10, cdm16_1_p11, cdm16_1_p12, mem, read, word, address_bus, cdm16_1_p17, cdm16_1_p18
  // Probe on cdm16_1_p8
  // Probe on cdm16_1_p9
  assign data_bus = not_1_out ? cdm16_1_p17 : 16'bz;  // Controlled_Buffer controlled_buffer_1
  not not_1 (not_1_out, read);
  assign cdm16_1_p18 = read ? data_bus : 16'bz;  // Controlled_Buffer controlled_buffer_2
  // Probe on cdm16_1_p10
  // Probe on cdm16_1_p11
  // Probe on cdm16_1_p12
  // Probe on birth[4:0]
  BS_helper bs_helper_1 (.input_6_bit(num_1), .output_5_bit(birth[4:0]));
  BS_helper bs_helper_2 (.input_6_bit(num_2), .output_5_bit(birth[9:5]));
  // Probe on birth[9:5]
  BS_helper bs_helper_3 (.input_6_bit(num_3), .output_5_bit(birth[14:10]));
  // Probe on birth[14:10]
  BS_helper bs_helper_4 (.input_6_bit(num_4), .output_5_bit(birth[19:15]));
  // Probe on birth[19:15]
  BS_helper bs_helper_5 (.input_6_bit(num_5), .output_5_bit(birth[24:20]));
  // Probe on birth[24:20]
  // Probe on birth[29:25]
  BS_helper bs_helper_6 (.input_6_bit(num_6), .output_5_bit(birth[29:25]));
  // RAM ram_1: pin names not known; wires that end beside it: address_bus, word, mem, clock, read, data_bus
  // Probe on save[4:0]
  BS_helper bs_helper_7 (.input_6_bit(num_1_2), .output_5_bit(save[4:0]));
  BS_helper bs_helper_8 (.input_6_bit(num_2_2), .output_5_bit(save[9:5]));
  // Probe on save[9:5]
  // Probe on save[14:10]
  BS_helper bs_helper_9 (.input_6_bit(num_3_2), .output_5_bit(save[14:10]));
  // Probe on save[19:15]
  BS_helper bs_helper_10 (.input_6_bit(num_4_2), .output_5_bit(save[19:15]));
  BS_helper bs_helper_11 (.input_6_bit(num_5_2), .output_5_bit(save[24:20]));
  // Probe on save[24:20]
  // Probe on save[29:25]
  BS_helper bs_helper_12 (.input_6_bit(num_6_2), .output_5_bit(save[29:25]));

  // Other names for the same wires on the sheet: lookAt[24:0] = {plus_2_line, plus_1_line, cur_line, minus_1_line, minus_2_line}

  // Notes on the sheet:
  //   look at
  //   Set up rules (not now :{ )
  //   birth
  //   if the number is >25, the rule is inactive
  //   You can choose up to 6 numbers from 0 to 25
  //   ↓ 0 – use number in rules, 1 — don't use
  //   ↑ ↑ ↑ ↑ ↑ binary number from 0 to 25
  //   save
endmodule

// ☀
module arrows__not_used (
  input  LEFT,
  input  DOWN,
  input  RIGHT,
  input  UP,
  output [2:0] out
);

  Multiplexer #(.select(4), .width(3)) multiplexer_1 (
    .in0(3'b000), .in1(3'b100), .in2(3'b011), .in3(3'b011), .in4(3'b010), .in5(3'b010), .in6(3'b010),
    .in7(3'b010), .in8(3'b001), .in9(3'b001), .in10(3'b001), .in11(3'b001), .in12(3'b001), .in13(3'b001),
    .in14(3'b001), .in15(3'b001), .out(out), .sel({UP, RIGHT, DOWN, LEFT}));  // open: en

  // Notes on the sheet:
  //   out: pull=down
endmodule

module KeyBoard (
  input  LEFT,
  input  DOWN,
  input  torus,
  input  RIGHT,
  input  UP,
  input  _1,
  input  INVERT,
  input  _0,
  input  CLEAR,
  input  SPACE,
  output [7:0] out
);

  wire [2:0] or_5_out;
  wire [3:0] arrows, or_1_out;

  or or_1 (or_1_out[0], LEFT, torus);
  or or_2 (or_1_out[1], DOWN, torus);
  or or_3 (or_1_out[2], RIGHT, torus);
  or or_4 (or_1_out[3], UP, torus);
  Multiplexer #(.select(4), .width(4)) multiplexer_1 (
    .in0(4'b0000), .in1(4'b0001), .in2(4'b0010), .in3(4'b0010), .in4(4'b0100), .in5(4'b0100), .in6(4'b0100),
    .in7(4'b0100), .in8(4'b1000), .in9(4'b1000), .in10(4'b1000), .in11(4'b1000), .in12(4'b1000),
    .in13(4'b1000), .in14(4'b1000), .in15(4'b1111), .out(arrows), .sel(or_1_out));  // open: en
  or or_5 (or_5_out[0], arrows[0], arrows[1], arrows[2], arrows[3]);
  // Probe on 2'b11
  or or_6 (or_5_out[1], _1, INVERT);
  or or_7 (or_5_out[2], INVERT, _0);
  // Probe on 2'b10
  // Probe on or_5_out[0]
  // Probe on 2'b01
  // Probe on 2'b00
  Multiplexer #(.select(5), .width(8)) multiplexer_2 (
    .in0({8{1'b0}}), .in1({4'b0000, arrows}), .in2(8'h30), .in3(8'h30), .in4(8'h20), .in5(8'h20),
    .in6(8'h10), .in7(8'h10), .in8(8'h40), .in9(8'h40), .in10(8'h40), .in11(8'h40), .in12(8'h40),
    .in13(8'h40), .in14(8'h40), .in15(8'h40), .in16(8'h80), .in17(8'h80), .in18(8'h80), .in19(8'h80),
    .in20(8'h80), .in21(8'h80), .in22(8'h80), .in23(8'h80), .in24(8'h80), .in25(8'h80), .in26(8'h80),
    .in27(8'h80), .in28(8'h80), .in29(8'h80), .in30(8'h80), .in31(8'h80), .out(out),
    .sel({SPACE, CLEAR, or_5_out}));  // open: en
  // Probe on 2'b00

  // Notes on the sheet:
  //   1 (set alive)
  //   state = 11
  //   0 (set dead)
  //   state = 10
  //   invert cell
  //   state = 01
  //   clear field
  //   state = 00
  //   space (pause)
  //   state = 00
endmodule

module aliveSTD___not_used (
  input  [8:0] neighbours,
  input  pause,
  input  [1:0] input_state,
  output alive
);

  wire _2_out, _3_out, multiplexer_1_out, multiplexer_2_out, or_1_out, xor_1_out;
  wire [3:0] newCnt;

  and _3 (_3_out, newCnt[0], newCnt[1], ~newCnt[2], ~newCnt[3]);  // AND_Gate
  and _2 (_2_out, ~newCnt[0], newCnt[1], ~newCnt[2], ~newCnt[3]);  // AND_Gate
  // Probe on newCnt
  BitAdder bitadder_1 (.in0({neighbours[8:5], neighbours[3:0]}), .out(newCnt));
  Multiplexer #(.disabled(0)) multiplexer_1 (
    .in0(_3_out), .in1(or_1_out), .out(multiplexer_1_out), .sel(neighbours[4]));  // open: en
  or or_1 (or_1_out, _3_out, _2_out);
  xor xor_1 (xor_1_out, neighbours[4], input_state[0]);
  Multiplexer #(.disabled(0)) multiplexer_2 (
    .in0(xor_1_out), .in1(input_state[0]), .out(multiplexer_2_out), .sel(input_state[1]));  // open: en
  Multiplexer #(.disabled(0)) multiplexer_3 (
    .in0(multiplexer_1_out), .in1(multiplexer_2_out), .out(alive), .sel(pause));  // open: en
  Pull_Resistor pull_resistor_1 (.node(alive));

  // Other names for the same wires on the sheet: cur = neighbours[4]

  // Notes on the sheet:
  //   neighbours: pull=down
  //   input_state: pull=down
  //   ▒ — look at
  //   ▓ — current cell
  //   floating → 0
  //   if cur cell is dead (= 0) try birth,
  //   alive (= 1) — try save
  //   ▒ ▒ ▒
  //   ▒ ▓ ▒
  //   ▒ ▒ ▒
  //   3 if dead
  //   2 or 3 if alive
  //   00 — old
  //   01 — invert
  //   10 — set DEAD
  //   11 — set ALIVE
  //   old or invert
  //   0 (low bit)
  //   1 (high bit)
  //   new
  //   by state
endmodule

module aliveSTD__old__not_used (
  input  [8:0] neighbours,
  input  pause,
  input  clock,
  input  [1:0] input_state,
  output alive
);

  wire _2_out, _3_out, multiplexer_1_out, multiplexer_2_out, multiplexer_3_out, not_1_out, or_1_out;
  wire [3:0] newCnt;

  and _3 (_3_out, newCnt[0], newCnt[1], ~newCnt[2], ~newCnt[3]);  // AND_Gate
  and _2 (_2_out, ~newCnt[0], newCnt[1], ~newCnt[2], ~newCnt[3]);  // AND_Gate
  // Probe on newCnt
  BitAdder bitadder_1 (.in0({neighbours[8:5], neighbours[3:0]}), .out(newCnt));
  Multiplexer #(.disabled(0)) multiplexer_1 (
    .in0(_3_out), .in1(or_1_out), .out(multiplexer_1_out), .sel(neighbours[4]));  // open: en
  or or_1 (or_1_out, _3_out, _2_out);
  Multiplexer #(.select(2), .disabled(0)) multiplexer_2 (
    .in0(alive), .in1(not_1_out), .in2(input_state[0]), .in3(input_state[0]), .out(multiplexer_2_out),
    .sel(input_state));  // open: en
  Multiplexer #(.disabled(0)) multiplexer_3 (
    .in0(multiplexer_1_out), .in1(multiplexer_2_out), .out(multiplexer_3_out), .sel(pause));  // open: en
  Pull_Resistor pull_resistor_1 (.node(alive));
  Register #(.width(1), .trigger("falling")) register_1 (
    .D(multiplexer_3_out), .Q(alive), .clk(clock));  // open: en, clr
  not not_1 (not_1_out, alive);

  // Other names for the same wires on the sheet: cur = neighbours[4]

  // Notes on the sheet:
  //   neighbours: pull=down
  //   input_state: pull=down
  //   ▒ — look at
  //   ▓ — current cell
  //   floating → 0
  //   if cur cell is dead (= 0) try birth,
  //   alive (= 1) — try save
  //   ▒ ▒ ▒
  //   ▒ ▓ ▒
  //   ▒ ▒ ▒
  //   3 if dead
  //   2 or 3 if alive
  //   00 — old
  //   01 — invert
  //   10 — set DEAD
  //   11 — set ALIVE
  //   0 (low bit)
  //   1 (high bit)
  //   new
  //   by state
endmodule

module alive (
  input  [24:0] neighbours,
  input  [24:0] look_at,
  input  [29:0] B1___birth,
  input  [29:0] S1___save,
  input  pause,
  input  [29:0] B2___birth,
  input  [1:0] input_state,
  input  [29:0] S2___save,
  output alive
);

  wire can_cell_born_out, can_cell_save_out, comparator_1_eq, comparator_2_eq, comparator_3_eq,
       comparator_4_eq, comparator_5_eq, comparator_6_eq, comparator_7_eq, comparator_8_eq, comparator_9_eq,
       comparator_10_eq, comparator_11_eq, comparator_12_eq, comparator_13_eq, comparator_14_eq,
       comparator_15_eq, comparator_16_eq, comparator_17_eq, comparator_18_eq, comparator_19_eq,
       comparator_20_eq, comparator_21_eq, comparator_22_eq, comparator_23_eq, comparator_24_eq,
       multiplexer_1_out, multiplexer_3_out, xor_1_out;
  wire [4:0] newCnt;
  wire [24:0] and_1_out, undriven;

  assign and_1_out = neighbours & look_at;  // AND_Gate and_1, 25 bits wide
  // Probe on newCnt
  BitAdder #(.width(25)) bitadder_1 (.in0(and_1_out), .out(newCnt));
  // Probe on undriven[4:0]
  // Probe on undriven[9:5]
  // Probe on undriven[14:10]
  // Probe on undriven[19:15]
  // Probe on undriven[24:20]
  Comparator #(.width(5), .mode("unsigned")) comparator_1 (
    .a(newCnt), .b(B1___birth[4:0]), .eq(comparator_1_eq));  // open: gt, lt
  Comparator #(.width(5), .mode("unsigned")) comparator_2 (
    .a(newCnt), .b(B1___birth[9:5]), .eq(comparator_2_eq));  // open: gt, lt
  Comparator #(.width(5), .mode("unsigned")) comparator_3 (
    .a(newCnt), .b(B1___birth[14:10]), .eq(comparator_3_eq));  // open: gt, lt
  Comparator #(.width(5), .mode("unsigned")) comparator_4 (
    .a(newCnt), .b(B1___birth[19:15]), .eq(comparator_4_eq));  // open: gt, lt
  Comparator #(.width(5), .mode("unsigned")) comparator_5 (
    .a(newCnt), .b(B1___birth[24:20]), .eq(comparator_5_eq));  // open: gt, lt
  Comparator #(.width(5), .mode("unsigned")) comparator_6 (
    .a(newCnt), .b(B1___birth[29:25]), .eq(comparator_6_eq));  // open: gt, lt
  Comparator #(.width(5), .mode("unsigned")) comparator_7 (
    .a(newCnt), .b(B2___birth[4:0]), .eq(comparator_7_eq));  // open: gt, lt
  Comparator #(.width(5), .mode("unsigned")) comparator_8 (
    .a(newCnt), .b(B2___birth[9:5]), .eq(comparator_8_eq));  // open: gt, lt
  Comparator #(.width(5), .mode("unsigned")) comparator_9 (
    .a(newCnt), .b(B2___birth[14:10]), .eq(comparator_9_eq));  // open: gt, lt
  Comparator #(.width(5), .mode("unsigned")) comparator_10 (
    .a(newCnt), .b(B2___birth[19:15]), .eq(comparator_10_eq));  // open: gt, lt
  Comparator #(.width(5), .mode("unsigned")) comparator_11 (
    .a(newCnt), .b(B2___birth[24:20]), .eq(comparator_11_eq));  // open: gt, lt
  Comparator #(.width(5), .mode("unsigned")) comparator_12 (
    .a(newCnt), .b(B2___birth[29:25]), .eq(comparator_12_eq));  // open: gt, lt
  Comparator #(.width(5), .mode("unsigned")) comparator_13 (
    .a(newCnt), .b(S1___save[4:0]), .eq(comparator_13_eq));  // open: gt, lt
  Comparator #(.width(5), .mode("unsigned")) comparator_14 (
    .a(newCnt), .b(S1___save[9:5]), .eq(comparator_14_eq));  // open: gt, lt
  Comparator #(.width(5), .mode("unsigned")) comparator_15 (
    .a(newCnt), .b(S1___save[14:10]), .eq(comparator_15_eq));  // open: gt, lt
  Comparator #(.width(5), .mode("unsigned")) comparator_16 (
    .a(newCnt), .b(S1___save[19:15]), .eq(comparator_16_eq));  // open: gt, lt
  Comparator #(.width(5), .mode("unsigned")) comparator_17 (
    .a(newCnt), .b(S1___save[24:20]), .eq(comparator_17_eq));  // open: gt, lt
  Comparator #(.width(5), .mode("unsigned")) comparator_18 (
    .a(newCnt), .b(S1___save[29:25]), .eq(comparator_18_eq));  // open: gt, lt
  Comparator #(.width(5), .mode("unsigned")) comparator_19 (
    .a(newCnt), .b(S2___save[4:0]), .eq(comparator_19_eq));  // open: gt, lt
  Comparator #(.width(5), .mode("unsigned")) comparator_20 (
    .a(newCnt), .b(S2___save[9:5]), .eq(comparator_20_eq));  // open: gt, lt
  Comparator #(.width(5), .mode("unsigned")) comparator_21 (
    .a(newCnt), .b(S2___save[14:10]), .eq(comparator_21_eq));  // open: gt, lt
  Comparator #(.width(5), .mode("unsigned")) comparator_22 (
    .a(newCnt), .b(S2___save[19:15]), .eq(comparator_22_eq));  // open: gt, lt
  Comparator #(.width(5), .mode("unsigned")) comparator_23 (
    .a(newCnt), .b(S2___save[24:20]), .eq(comparator_23_eq));  // open: gt, lt
  Comparator #(.width(5), .mode("unsigned")) comparator_24 (
    .a(newCnt), .b(S2___save[29:25]), .eq(comparator_24_eq));  // open: gt, lt
  or can_cell_born (can_cell_born_out, comparator_1_eq, comparator_2_eq, comparator_3_eq, comparator_4_eq, comparator_5_eq, comparator_6_eq, comparator_7_eq, comparator_8_eq, comparator_9_eq, comparator_10_eq, comparator_11_eq, comparator_12_eq);
  or can_cell_save (can_cell_save_out, comparator_13_eq, comparator_14_eq, comparator_15_eq, comparator_16_eq, comparator_17_eq, comparator_18_eq, comparator_19_eq, comparator_20_eq, comparator_21_eq, comparator_22_eq, comparator_23_eq, comparator_24_eq);
  Multiplexer #(.disabled(0)) multiplexer_1 (
    .in0(can_cell_born_out), .in1(can_cell_save_out), .out(multiplexer_1_out), .sel(neighbours[12]));  // open: en
  xor xor_1 (xor_1_out, neighbours[12], input_state[0]);
  Multiplexer #(.disabled(0)) multiplexer_2 (
    .in0(multiplexer_1_out), .in1(multiplexer_3_out), .out(alive), .sel(pause));  // open: en
  Pull_Resistor pull_resistor_1 (.node(alive));
  Multiplexer #(.disabled(0)) multiplexer_3 (
    .in0(xor_1_out), .in1(input_state[0]), .out(multiplexer_3_out), .sel(input_state[1]));  // open: en

  // Other names for the same wires on the sheet: B1[4:0] = B1___birth[4:0]; B2[4:0] = B1___birth[9:5];
  //   B3[4:0] = B1___birth[14:10]; B4[4:0] = B1___birth[19:15]; B5[4:0] = B1___birth[24:20];
  //   B6[4:0] = B1___birth[29:25]; B7[4:0] = B2___birth[4:0]; B8[4:0] = B2___birth[9:5]; B9[4:0] = B2___birth[14:10];
  //   B10[4:0] = B2___birth[19:15]; B11[4:0] = B2___birth[24:20]; B12[4:0] = B2___birth[29:25]; cur = neighbours[12];
  //   S1[4:0] = S1___save[4:0]; S2[4:0] = S1___save[9:5]; S3[4:0] = S1___save[14:10]; S4[4:0] = S1___save[19:15];
  //   S5[4:0] = S1___save[24:20]; S6[4:0] = S1___save[29:25]; S7[4:0] = S2___save[4:0]; S8[4:0] = S2___save[9:5];
  //   S9[4:0] = S2___save[14:10]; S10[4:0] = S2___save[19:15]; S11[4:0] = S2___save[24:20];
  //   S12[4:0] = S2___save[29:25]

  // Notes on the sheet:
  //   neighbours: pull=down
  //   S2___save: pull=up
  //   look_at: pull=down
  //   B1___birth: pull=up
  //   S1___save: pull=up
  //   input_state: pull=down
  //   B2___birth: pull=up
  //   floating → 0
  //   floating → 0
  //   floating → 1
  //   floating → 1
  //   floating → 1
  //   floating → 1
  //   DEBUG TOOLS
  //   ▒ — neighbours
  //   ▓ — current cell
  //   ▒ ▒ ▒ ▒ ▒
  //   ▒ ▒ ▒ ▒ ▒
  //   ▒ ▒ ▓ ▒ ▒
  //   ▒ ▒ ▒ ▒ ▒
  //   ▒ ▒ ▒ ▒ ▒
  //   if cur cell is dead (= 0) try birth
  //   alive (= 1) — try save
  //   new iteration
  //   by state
  //   old or invert
  //   new: 0 or 1
  //   00 — old
  //   01 — invert
  //   10 — set DEAD
  //   11 — set ALIVE
endmodule

module BS_helperSTD__not_used (
  input  [4:0] input_5_bit,
  output [3:0] output_4_bit
);

  Multiplexer #(.width(4)) multiplexer_1 (
    .in0(input_5_bit[3:0]), .in1(4'b1111), .out(output_4_bit), .sel(input_5_bit[4]));  // open: en
endmodule

module BS_helper (
  input  [5:0] input_6_bit,
  output [4:0] output_5_bit
);

  Multiplexer #(.width(5)) multiplexer_1 (
    .in0(input_6_bit[4:0]), .in1({5{1'b1}}), .out(output_5_bit), .sel(input_6_bit[5]));  // open: en
endmodule

// BS-0->31
module BS_helper_0__31 (
  input  [5:0] input_6_bit,
  output [4:0] output_5_bit
);

  wire nor_1_out, or_1_out;

  nor nor_1 (nor_1_out, input_6_bit[4], input_6_bit[3], input_6_bit[2], input_6_bit[1], input_6_bit[0]);
  or or_1 (or_1_out, nor_1_out, input_6_bit[5]);
  Multiplexer #(.width(5)) multiplexer_1 (
    .in0(input_6_bit[4:0]), .in1({5{1'b1}}), .out(output_5_bit), .sel(or_1_out));  // open: en
endmodule

module STATE_helper (
  input  [1:0] input_state,
  input  i,
  input  j,
  output [1:0] output_state
);

  wire [1:1] and_2_out;

  assign output_state = input_state & {2{and_2_out[1]}};  // AND_Gate and_1, 2 bits wide
  and and_2 (and_2_out[1], i, j);

  // Notes on the sheet:
  //   i: pull=down
  //   j: pull=down
  //   if cursor there, out = input state. Otherwise out = 00
endmodule

module exampleSTD__not_used (
  input  [2:0] Old_state,
  input  [2:0] in_2,
  input  [2:0] in_3,
  input  pause,
  input  [1:0] state
);

  wire [3:0] undriven, undriven_2;
  wire [4:4] newState;

  DotMatrix #(.inputtype("row"), .matrixcols(3), .matrixrows(3)) dotmatrix_1 (
    .row0(Old_state), .row1(in_2), .row2(in_3));
  aliveSTD___not_used alivestd_not_used_1 (
    .neighbours({in_3, in_2, Old_state}), .alive(newState[4]), .pause(pause), .input_state(state));
  // Probe on undriven[2:0]
  // Probe on {undriven_2[0], 1'b0, undriven[3]}
  // Probe on undriven_2[3:1]
  // Probe on Old_state
  // Probe on {in_2[2], newState[4], in_2[0]}
  // Probe on in_3
  DotMatrix #(.inputtype("row"), .matrixcols(3), .matrixrows(3)) dotmatrix_2 (
    .row0(Old_state), .row1({in_2[2], newState[4], in_2[0]}), .row2(in_3));

  // Other names for the same wires on the sheet: neighbours[8:0] = {in_3, in_2, Old_state};
  //   newState (some bits) = {in_3, in_2[2], in_2[0], Old_state}

  // Notes on the sheet:
  //   old state
  //   STANDART RULES:
  //   (You can edit)
  //   Old state
  //   How to use?
  //   1) look at 3x3
  //   2) B3/S23
  //   New state
  //   New state
  //   How to watch?
  //   X is cell's neighbours
  //   0 is current cell
endmodule

module example__not_used (
  input  [4:0] Old_state,
  input  [4:0] minus_2_line,
  input  [4:0] in_3,
  input  [4:0] minus_1_line,
  input  [4:0] in_5,
  input  [4:0] cur_line,
  input  [4:0] in_7,
  input  [4:0] plus_1_line,
  input  [4:0] in_9,
  input  [4:0] plus_2_line,
  input  [5:0] B__S,
  input  [5:0] num_1,
  input  [5:0] num_1_2,
  input  [5:0] num_2,
  input  [5:0] num_2_2,
  input  [5:0] num_3,
  input  [5:0] num_3_2,
  input  [5:0] num_4,
  input  [5:0] num_4_2,
  input  [5:0] num_5,
  input  [5:0] num_5_2,
  input  [5:0] num_6,
  input  [5:0] num_6_2,
  input  pause,
  input  [1:0] state
);

  wire [11:0] undriven, undriven_2;
  wire [12:12] newState;
  wire [29:0] birth, save;

  DotMatrix #(.inputtype("row"), .matrixrows(5)) dotmatrix_1 (
    .row0(Old_state), .row1(in_3), .row2(in_5), .row3(in_7), .row4(in_9));
  alive alive_1 (
    .neighbours({in_9, in_7, in_5, in_3, Old_state}),
    .look_at({plus_2_line, plus_1_line, cur_line, minus_1_line, minus_2_line}), .B1___birth(birth),
    .S1___save(save), .alive(newState[12]), .pause(pause), .input_state(state));  // open: B2___birth, S2___save
  // Probe on Old_state
  // Probe on in_3
  // Probe on {in_5[4:3], newState[12], in_5[1:0]}
  // Probe on in_7
  // Probe on in_9
  DotMatrix #(.inputtype("row"), .matrixrows(5)) dotmatrix_2 (
    .row0(Old_state), .row1(in_3), .row2({in_5[4:3], newState[12], in_5[1:0]}), .row3(in_7), .row4(in_9));
  // Probe on undriven[4:0]
  // Probe on undriven[9:5]
  // Probe on {undriven_2[1:0], 1'b0, undriven[11:10]}
  // Probe on undriven_2[6:2]
  // Probe on undriven_2[11:7]
  // Probe on birth[4:0]
  BS_helper bs_helper_1 (.input_6_bit(num_1), .output_5_bit(birth[4:0]));
  BS_helper bs_helper_2 (.input_6_bit(num_2), .output_5_bit(birth[9:5]));
  // Probe on birth[9:5]
  // Probe on birth[14:10]
  BS_helper bs_helper_3 (.input_6_bit(num_3), .output_5_bit(birth[14:10]));
  BS_helper bs_helper_4 (.input_6_bit(num_4), .output_5_bit(birth[19:15]));
  // Probe on birth[19:15]
  // Probe on birth[24:20]
  BS_helper bs_helper_5 (.input_6_bit(num_5), .output_5_bit(birth[24:20]));
  // Probe on birth[29:25]
  BS_helper bs_helper_6 (.input_6_bit(num_6), .output_5_bit(birth[29:25]));
  BS_helper bs_helper_7 (.input_6_bit(num_1_2), .output_5_bit(save[4:0]));
  // Probe on save[4:0]
  // Probe on save[9:5]
  BS_helper bs_helper_8 (.input_6_bit(num_2_2), .output_5_bit(save[9:5]));
  BS_helper bs_helper_9 (.input_6_bit(num_3_2), .output_5_bit(save[14:10]));
  // Probe on save[14:10]
  BS_helper bs_helper_10 (.input_6_bit(num_4_2), .output_5_bit(save[19:15]));
  // Probe on save[19:15]
  BS_helper bs_helper_11 (.input_6_bit(num_5_2), .output_5_bit(save[24:20]));
  // Probe on save[24:20]
  BS_helper bs_helper_12 (.input_6_bit(num_6_2), .output_5_bit(save[29:25]));
  // Probe on save[29:25]

  // Other names for the same wires on the sheet: lookAt[24:0] = {plus_2_line, plus_1_line, cur_line, minus_1_line, minus_2_line};
  //   neighbours[24:0] = {in_9, in_7, in_5, in_3, Old_state};
  //   newState (some bits) = {in_9, in_7, in_5[4:3], in_5[1:0], in_3, Old_state}

  // Notes on the sheet:
  //   old state
  //   (You can edit)
  //   Old state
  //   How to use?
  //   0~ — old
  //   10 — set DEAD
  //   11 — set ALIVE
  //   New state
  //   New state
  //   How to watch?
  //   X is cell's neighbours
  //   0 is current cell
  //   EDIT RULES:
  //   Standard rules:
  //   1) look at 3x3
  //   2) B3/S23
  //   if the number is >25, the rule is inactive
  //   B – birth
  //   look at
  //   You can choose up to 6 numbers from 0 to 25
  //   S – save
  //   ↓ 0 – use number in rules, 1 — don't use
  //   ↑ ↑ ↑ ↑ ↑ binary number from 0 to 25
endmodule

module neighboursSTD__not_used (
  input  minus_01_01,
  input  minus_01_00,
  input  minus_01_01_2,
  input  plus_00_01,
  input  plus_00_00,
  input  plus_00_01_2,
  input  plus_01_01,
  input  plus_01_00,
  input  plus_01_01_2,
  output [8:0] neighbours
);


  assign neighbours = {plus_01_01_2, plus_01_00, plus_01_01, plus_00_01_2, plus_00_00, plus_00_01, minus_01_01_2, minus_01_00, minus_01_01};
endmodule

module neighbours (
  input  minus_02_02,
  input  minus_02_01,
  input  minus_02_00,
  input  minus_02_01_2,
  input  minus_02_02_2,
  input  minus_01_02,
  input  minus_01_01,
  input  minus_01_00,
  input  minus_01_01_2,
  input  minus_01_02_2,
  input  plus_00_02,
  input  plus_00_01,
  input  plus_00_00,
  input  plus_00_01_2,
  input  plus_00_02_2,
  input  plus_01_02,
  input  plus_01_01,
  input  plus_01_00,
  input  plus_01_01_2,
  input  plus_01_02_2,
  input  plus_02_02,
  input  plus_02_01,
  input  plus_02_00,
  input  plus_02_01_2,
  input  plus_02_02_2,
  output [24:0] neighbours
);


  assign neighbours = {plus_02_02_2, plus_02_01_2, plus_02_00, plus_02_01, plus_02_02, plus_01_02_2, plus_01_01_2, plus_01_00, plus_01_01, plus_01_02, plus_00_02_2, plus_00_01_2, plus_00_00, plus_00_01, plus_00_02, minus_01_02_2, minus_01_01_2, minus_01_00, minus_01_01, minus_01_02, minus_02_02_2, minus_02_01_2, minus_02_00, minus_02_01, minus_02_02};
endmodule

module lineSTD__not_used (
  input  [31:0] J,
  input  [31:0] minus_1_line,
  input  [31:0] _1_line,
  input  I,
  input  Torus,
  input  [1:0] input_state,
  input  clock,
  input  pause,
  output [31:0] _0_line__out__1,
  output [31:0] display,
  output [31:0] _0_line__out__1_2
);

  wire minus_01_01_t, minus_01_32, plus_00_00new, plus_00_01_t, plus_00_01new, plus_00_02new, plus_00_03new,
       plus_00_04new, plus_00_05new, plus_00_06new, plus_00_07new, plus_00_08new, plus_00_09new,
       plus_00_10new, plus_00_11new, plus_00_12new, plus_00_13new, plus_00_14new, plus_00_15new,
       plus_00_16new, plus_00_17new, plus_00_18new, plus_00_19new, plus_00_20new, plus_00_21new,
       plus_00_22new, plus_00_23new, plus_00_24new, plus_00_25new, plus_00_26new, plus_00_27new,
       plus_00_28new, plus_00_29new, plus_00_30new, plus_00_31new, plus_00_32, plus_01_01_t, plus_01_32;
  wire [1:0] state_helper_1_output_state, state_helper_2_output_state, state_helper_3_output_state,
       state_helper_4_output_state, state_helper_5_output_state, state_helper_6_output_state,
       state_helper_7_output_state, state_helper_8_output_state, state_helper_9_output_state,
       state_helper_10_output_state, state_helper_11_output_state, state_helper_12_output_state,
       state_helper_13_output_state, state_helper_14_output_state, state_helper_15_output_state,
       state_helper_16_output_state, state_helper_17_output_state, state_helper_18_output_state,
       state_helper_19_output_state, state_helper_20_output_state, state_helper_21_output_state,
       state_helper_22_output_state, state_helper_23_output_state, state_helper_24_output_state,
       state_helper_25_output_state, state_helper_26_output_state, state_helper_27_output_state,
       state_helper_28_output_state, state_helper_29_output_state, state_helper_30_output_state,
       state_helper_31_output_state, state_helper_32_output_state;
  wire [8:0] neighboursstd_not_used_1_neighbours, neighboursstd_not_used_2_neighbours,
       neighboursstd_not_used_3_neighbours, neighboursstd_not_used_4_neighbours,
       neighboursstd_not_used_5_neighbours, neighboursstd_not_used_6_neighbours,
       neighboursstd_not_used_7_neighbours, neighboursstd_not_used_8_neighbours,
       neighboursstd_not_used_9_neighbours, neighboursstd_not_used_10_neighbours,
       neighboursstd_not_used_11_neighbours, neighboursstd_not_used_12_neighbours,
       neighboursstd_not_used_13_neighbours, neighboursstd_not_used_14_neighbours,
       neighboursstd_not_used_15_neighbours, neighboursstd_not_used_16_neighbours,
       neighboursstd_not_used_17_neighbours, neighboursstd_not_used_18_neighbours,
       neighboursstd_not_used_19_neighbours, neighboursstd_not_used_20_neighbours,
       neighboursstd_not_used_21_neighbours, neighboursstd_not_used_22_neighbours,
       neighboursstd_not_used_23_neighbours, neighboursstd_not_used_24_neighbours,
       neighboursstd_not_used_25_neighbours, neighboursstd_not_used_26_neighbours,
       neighboursstd_not_used_27_neighbours, neighboursstd_not_used_28_neighbours,
       neighboursstd_not_used_29_neighbours, neighboursstd_not_used_30_neighbours,
       neighboursstd_not_used_31_neighbours, neighboursstd_not_used_32_neighbours;

  neighboursSTD__not_used neighboursstd_not_used_1 (
    .minus_01_01(minus_01_01_t), .minus_01_00(minus_1_line[0]), .minus_01_01_2(minus_1_line[1]),
    .plus_00_01(plus_00_01_t), .plus_00_00(_0_line__out__1[31]), .plus_00_01_2(_0_line__out__1[30]),
    .plus_01_01(plus_01_01_t), .plus_01_00(_1_line[0]), .plus_01_01_2(_1_line[1]),
    .neighbours(neighboursstd_not_used_1_neighbours));
  aliveSTD___not_used alivestd_not_used_1 (
    .neighbours(neighboursstd_not_used_1_neighbours), .alive(plus_00_00new), .pause(pause),
    .input_state(state_helper_1_output_state));
  STATE_helper state_helper_1 (.input_state(input_state), .output_state(state_helper_1_output_state), .i(I), .j(J[0]));
  and and_1 (minus_01_32, minus_1_line[0], Torus);
  and and_2 (minus_01_01_t, minus_1_line[31], Torus);
  neighboursSTD__not_used neighboursstd_not_used_2 (
    .minus_01_01(minus_1_line[0]), .minus_01_00(minus_1_line[1]), .minus_01_01_2(minus_1_line[2]),
    .plus_00_01(_0_line__out__1[31]), .plus_00_00(_0_line__out__1[30]), .plus_00_01_2(_0_line__out__1[29]),
    .plus_01_01(_1_line[0]), .plus_01_00(_1_line[1]), .plus_01_01_2(_1_line[2]),
    .neighbours(neighboursstd_not_used_2_neighbours));
  Register #(.width(32), .trigger("falling")) register_1 (
    .D({plus_00_31new, plus_00_30new, plus_00_29new, plus_00_28new, plus_00_27new, plus_00_26new, plus_00_25new, plus_00_24new, plus_00_23new, plus_00_22new, plus_00_21new, plus_00_20new, plus_00_19new, plus_00_18new, plus_00_17new, plus_00_16new, plus_00_15new, plus_00_14new, plus_00_13new, plus_00_12new, plus_00_11new, plus_00_10new, plus_00_09new, plus_00_08new, plus_00_07new, plus_00_06new, plus_00_05new, plus_00_04new, plus_00_03new, plus_00_02new, plus_00_01new, plus_00_00new}),
    .Q({_0_line__out__1[0], _0_line__out__1[1], _0_line__out__1[2], _0_line__out__1[3], _0_line__out__1[4], _0_line__out__1[5], _0_line__out__1[6], _0_line__out__1[7], _0_line__out__1[8], _0_line__out__1[9], _0_line__out__1[10], _0_line__out__1[11], _0_line__out__1[12], _0_line__out__1[13], _0_line__out__1[14], _0_line__out__1[15], _0_line__out__1[16], _0_line__out__1[17], _0_line__out__1[18], _0_line__out__1[19], _0_line__out__1[20], _0_line__out__1[21], _0_line__out__1[22], _0_line__out__1[23], _0_line__out__1[24], _0_line__out__1[25], _0_line__out__1[26], _0_line__out__1[27], _0_line__out__1[28], _0_line__out__1[29], _0_line__out__1[30], _0_line__out__1[31]}),
    .clk(clock));  // open: en, clr
  aliveSTD___not_used alivestd_not_used_2 (
    .neighbours(neighboursstd_not_used_2_neighbours), .alive(plus_00_01new), .pause(pause),
    .input_state(state_helper_2_output_state));
  STATE_helper state_helper_2 (.input_state(input_state), .output_state(state_helper_2_output_state), .i(I), .j(J[1]));
  and and_3 (plus_01_32, _1_line[0], Torus);
  and and_4 (plus_01_01_t, _1_line[31], Torus);
  and and_5 (plus_00_32, _0_line__out__1[31], Torus);
  and and_6 (plus_00_01_t, _0_line__out__1[0], Torus);
  neighboursSTD__not_used neighboursstd_not_used_3 (
    .minus_01_01(minus_1_line[1]), .minus_01_00(minus_1_line[2]), .minus_01_01_2(minus_1_line[3]),
    .plus_00_01(_0_line__out__1[30]), .plus_00_00(_0_line__out__1[29]), .plus_00_01_2(_0_line__out__1[28]),
    .plus_01_01(_1_line[1]), .plus_01_00(_1_line[2]), .plus_01_01_2(_1_line[3]),
    .neighbours(neighboursstd_not_used_3_neighbours));
  aliveSTD___not_used alivestd_not_used_3 (
    .neighbours(neighboursstd_not_used_3_neighbours), .alive(plus_00_02new), .pause(pause),
    .input_state(state_helper_3_output_state));
  STATE_helper state_helper_3 (.input_state(input_state), .output_state(state_helper_3_output_state), .i(I), .j(J[2]));
  neighboursSTD__not_used neighboursstd_not_used_4 (
    .minus_01_01(minus_1_line[2]), .minus_01_00(minus_1_line[3]), .minus_01_01_2(minus_1_line[4]),
    .plus_00_01(_0_line__out__1[29]), .plus_00_00(_0_line__out__1[28]), .plus_00_01_2(_0_line__out__1[27]),
    .plus_01_01(_1_line[2]), .plus_01_00(_1_line[3]), .plus_01_01_2(_1_line[4]),
    .neighbours(neighboursstd_not_used_4_neighbours));
  aliveSTD___not_used alivestd_not_used_4 (
    .neighbours(neighboursstd_not_used_4_neighbours), .alive(plus_00_03new), .pause(pause),
    .input_state(state_helper_4_output_state));
  STATE_helper state_helper_4 (.input_state(input_state), .output_state(state_helper_4_output_state), .i(I), .j(J[3]));
  neighboursSTD__not_used neighboursstd_not_used_5 (
    .minus_01_01(minus_1_line[3]), .minus_01_00(minus_1_line[4]), .minus_01_01_2(minus_1_line[5]),
    .plus_00_01(_0_line__out__1[28]), .plus_00_00(_0_line__out__1[27]), .plus_00_01_2(_0_line__out__1[26]),
    .plus_01_01(_1_line[3]), .plus_01_00(_1_line[4]), .plus_01_01_2(_1_line[5]),
    .neighbours(neighboursstd_not_used_5_neighbours));
  aliveSTD___not_used alivestd_not_used_5 (
    .neighbours(neighboursstd_not_used_5_neighbours), .alive(plus_00_04new), .pause(pause),
    .input_state(state_helper_5_output_state));
  STATE_helper state_helper_5 (.input_state(input_state), .output_state(state_helper_5_output_state), .i(I), .j(J[4]));
  neighboursSTD__not_used neighboursstd_not_used_6 (
    .minus_01_01(minus_1_line[4]), .minus_01_00(minus_1_line[5]), .minus_01_01_2(minus_1_line[6]),
    .plus_00_01(_0_line__out__1[27]), .plus_00_00(_0_line__out__1[26]), .plus_00_01_2(_0_line__out__1[25]),
    .plus_01_01(_1_line[4]), .plus_01_00(_1_line[5]), .plus_01_01_2(_1_line[6]),
    .neighbours(neighboursstd_not_used_6_neighbours));
  aliveSTD___not_used alivestd_not_used_6 (
    .neighbours(neighboursstd_not_used_6_neighbours), .alive(plus_00_05new), .pause(pause),
    .input_state(state_helper_6_output_state));
  STATE_helper state_helper_6 (.input_state(input_state), .output_state(state_helper_6_output_state), .i(I), .j(J[5]));
  neighboursSTD__not_used neighboursstd_not_used_7 (
    .minus_01_01(minus_1_line[5]), .minus_01_00(minus_1_line[6]), .minus_01_01_2(minus_1_line[7]),
    .plus_00_01(_0_line__out__1[26]), .plus_00_00(_0_line__out__1[25]), .plus_00_01_2(_0_line__out__1[24]),
    .plus_01_01(_1_line[5]), .plus_01_00(_1_line[6]), .plus_01_01_2(_1_line[7]),
    .neighbours(neighboursstd_not_used_7_neighbours));
  aliveSTD___not_used alivestd_not_used_7 (
    .neighbours(neighboursstd_not_used_7_neighbours), .alive(plus_00_06new), .pause(pause),
    .input_state(state_helper_7_output_state));
  STATE_helper state_helper_7 (.input_state(input_state), .output_state(state_helper_7_output_state), .i(I), .j(J[6]));
  neighboursSTD__not_used neighboursstd_not_used_8 (
    .minus_01_01(minus_1_line[6]), .minus_01_00(minus_1_line[7]), .minus_01_01_2(minus_1_line[8]),
    .plus_00_01(_0_line__out__1[25]), .plus_00_00(_0_line__out__1[24]), .plus_00_01_2(_0_line__out__1[23]),
    .plus_01_01(_1_line[6]), .plus_01_00(_1_line[7]), .plus_01_01_2(_1_line[8]),
    .neighbours(neighboursstd_not_used_8_neighbours));
  aliveSTD___not_used alivestd_not_used_8 (
    .neighbours(neighboursstd_not_used_8_neighbours), .alive(plus_00_07new), .pause(pause),
    .input_state(state_helper_8_output_state));
  STATE_helper state_helper_8 (.input_state(input_state), .output_state(state_helper_8_output_state), .i(I), .j(J[7]));
  neighboursSTD__not_used neighboursstd_not_used_9 (
    .minus_01_01(minus_1_line[7]), .minus_01_00(minus_1_line[8]), .minus_01_01_2(minus_1_line[9]),
    .plus_00_01(_0_line__out__1[24]), .plus_00_00(_0_line__out__1[23]), .plus_00_01_2(_0_line__out__1[22]),
    .plus_01_01(_1_line[7]), .plus_01_00(_1_line[8]), .plus_01_01_2(_1_line[9]),
    .neighbours(neighboursstd_not_used_9_neighbours));
  aliveSTD___not_used alivestd_not_used_9 (
    .neighbours(neighboursstd_not_used_9_neighbours), .alive(plus_00_08new), .pause(pause),
    .input_state(state_helper_9_output_state));
  STATE_helper state_helper_9 (.input_state(input_state), .output_state(state_helper_9_output_state), .i(I), .j(J[8]));
  neighboursSTD__not_used neighboursstd_not_used_10 (
    .minus_01_01(minus_1_line[8]), .minus_01_00(minus_1_line[9]), .minus_01_01_2(minus_1_line[10]),
    .plus_00_01(_0_line__out__1[23]), .plus_00_00(_0_line__out__1[22]), .plus_00_01_2(_0_line__out__1[21]),
    .plus_01_01(_1_line[8]), .plus_01_00(_1_line[9]), .plus_01_01_2(_1_line[10]),
    .neighbours(neighboursstd_not_used_10_neighbours));
  aliveSTD___not_used alivestd_not_used_10 (
    .neighbours(neighboursstd_not_used_10_neighbours), .alive(plus_00_09new), .pause(pause),
    .input_state(state_helper_10_output_state));
  STATE_helper state_helper_10 (
    .input_state(input_state), .output_state(state_helper_10_output_state), .i(I), .j(J[9]));
  neighboursSTD__not_used neighboursstd_not_used_11 (
    .minus_01_01(minus_1_line[9]), .minus_01_00(minus_1_line[10]), .minus_01_01_2(minus_1_line[11]),
    .plus_00_01(_0_line__out__1[22]), .plus_00_00(_0_line__out__1[21]), .plus_00_01_2(_0_line__out__1[20]),
    .plus_01_01(_1_line[9]), .plus_01_00(_1_line[10]), .plus_01_01_2(_1_line[11]),
    .neighbours(neighboursstd_not_used_11_neighbours));
  aliveSTD___not_used alivestd_not_used_11 (
    .neighbours(neighboursstd_not_used_11_neighbours), .alive(plus_00_10new), .pause(pause),
    .input_state(state_helper_11_output_state));
  STATE_helper state_helper_11 (
    .input_state(input_state), .output_state(state_helper_11_output_state), .i(I), .j(J[10]));
  neighboursSTD__not_used neighboursstd_not_used_12 (
    .minus_01_01(minus_1_line[10]), .minus_01_00(minus_1_line[11]), .minus_01_01_2(minus_1_line[12]),
    .plus_00_01(_0_line__out__1[21]), .plus_00_00(_0_line__out__1[20]), .plus_00_01_2(_0_line__out__1[19]),
    .plus_01_01(_1_line[10]), .plus_01_00(_1_line[11]), .plus_01_01_2(_1_line[12]),
    .neighbours(neighboursstd_not_used_12_neighbours));
  aliveSTD___not_used alivestd_not_used_12 (
    .neighbours(neighboursstd_not_used_12_neighbours), .alive(plus_00_11new), .pause(pause),
    .input_state(state_helper_12_output_state));
  STATE_helper state_helper_12 (
    .input_state(input_state), .output_state(state_helper_12_output_state), .i(I), .j(J[11]));
  neighboursSTD__not_used neighboursstd_not_used_13 (
    .minus_01_01(minus_1_line[11]), .minus_01_00(minus_1_line[12]), .minus_01_01_2(minus_1_line[13]),
    .plus_00_01(_0_line__out__1[20]), .plus_00_00(_0_line__out__1[19]), .plus_00_01_2(_0_line__out__1[18]),
    .plus_01_01(_1_line[11]), .plus_01_00(_1_line[12]), .plus_01_01_2(_1_line[13]),
    .neighbours(neighboursstd_not_used_13_neighbours));
  aliveSTD___not_used alivestd_not_used_13 (
    .neighbours(neighboursstd_not_used_13_neighbours), .alive(plus_00_12new), .pause(pause),
    .input_state(state_helper_13_output_state));
  STATE_helper state_helper_13 (
    .input_state(input_state), .output_state(state_helper_13_output_state), .i(I), .j(J[12]));
  neighboursSTD__not_used neighboursstd_not_used_14 (
    .minus_01_01(minus_1_line[12]), .minus_01_00(minus_1_line[13]), .minus_01_01_2(minus_1_line[14]),
    .plus_00_01(_0_line__out__1[19]), .plus_00_00(_0_line__out__1[18]), .plus_00_01_2(_0_line__out__1[17]),
    .plus_01_01(_1_line[12]), .plus_01_00(_1_line[13]), .plus_01_01_2(_1_line[14]),
    .neighbours(neighboursstd_not_used_14_neighbours));
  aliveSTD___not_used alivestd_not_used_14 (
    .neighbours(neighboursstd_not_used_14_neighbours), .alive(plus_00_13new), .pause(pause),
    .input_state(state_helper_14_output_state));
  STATE_helper state_helper_14 (
    .input_state(input_state), .output_state(state_helper_14_output_state), .i(I), .j(J[13]));
  neighboursSTD__not_used neighboursstd_not_used_15 (
    .minus_01_01(minus_1_line[13]), .minus_01_00(minus_1_line[14]), .minus_01_01_2(minus_1_line[15]),
    .plus_00_01(_0_line__out__1[18]), .plus_00_00(_0_line__out__1[17]), .plus_00_01_2(_0_line__out__1[16]),
    .plus_01_01(_1_line[13]), .plus_01_00(_1_line[14]), .plus_01_01_2(_1_line[15]),
    .neighbours(neighboursstd_not_used_15_neighbours));
  aliveSTD___not_used alivestd_not_used_15 (
    .neighbours(neighboursstd_not_used_15_neighbours), .alive(plus_00_14new), .pause(pause),
    .input_state(state_helper_15_output_state));
  STATE_helper state_helper_15 (
    .input_state(input_state), .output_state(state_helper_15_output_state), .i(I), .j(J[14]));
  neighboursSTD__not_used neighboursstd_not_used_16 (
    .minus_01_01(minus_1_line[14]), .minus_01_00(minus_1_line[15]), .minus_01_01_2(minus_1_line[16]),
    .plus_00_01(_0_line__out__1[17]), .plus_00_00(_0_line__out__1[16]), .plus_00_01_2(_0_line__out__1[15]),
    .plus_01_01(_1_line[14]), .plus_01_00(_1_line[15]), .plus_01_01_2(_1_line[16]),
    .neighbours(neighboursstd_not_used_16_neighbours));
  aliveSTD___not_used alivestd_not_used_16 (
    .neighbours(neighboursstd_not_used_16_neighbours), .alive(plus_00_15new), .pause(pause),
    .input_state(state_helper_16_output_state));
  STATE_helper state_helper_16 (
    .input_state(input_state), .output_state(state_helper_16_output_state), .i(I), .j(J[15]));
  neighboursSTD__not_used neighboursstd_not_used_17 (
    .minus_01_01(minus_1_line[15]), .minus_01_00(minus_1_line[16]), .minus_01_01_2(minus_1_line[17]),
    .plus_00_01(_0_line__out__1[16]), .plus_00_00(_0_line__out__1[15]), .plus_00_01_2(_0_line__out__1[14]),
    .plus_01_01(_1_line[15]), .plus_01_00(_1_line[16]), .plus_01_01_2(_1_line[17]),
    .neighbours(neighboursstd_not_used_17_neighbours));
  aliveSTD___not_used alivestd_not_used_17 (
    .neighbours(neighboursstd_not_used_17_neighbours), .alive(plus_00_16new), .pause(pause),
    .input_state(state_helper_17_output_state));
  STATE_helper state_helper_17 (
    .input_state(input_state), .output_state(state_helper_17_output_state), .i(I), .j(J[16]));
  neighboursSTD__not_used neighboursstd_not_used_18 (
    .minus_01_01(minus_1_line[16]), .minus_01_00(minus_1_line[17]), .minus_01_01_2(minus_1_line[18]),
    .plus_00_01(_0_line__out__1[15]), .plus_00_00(_0_line__out__1[14]), .plus_00_01_2(_0_line__out__1[13]),
    .plus_01_01(_1_line[16]), .plus_01_00(_1_line[17]), .plus_01_01_2(_1_line[18]),
    .neighbours(neighboursstd_not_used_18_neighbours));
  aliveSTD___not_used alivestd_not_used_18 (
    .neighbours(neighboursstd_not_used_18_neighbours), .alive(plus_00_17new), .pause(pause),
    .input_state(state_helper_18_output_state));
  STATE_helper state_helper_18 (
    .input_state(input_state), .output_state(state_helper_18_output_state), .i(I), .j(J[17]));
  neighboursSTD__not_used neighboursstd_not_used_19 (
    .minus_01_01(minus_1_line[17]), .minus_01_00(minus_1_line[18]), .minus_01_01_2(minus_1_line[19]),
    .plus_00_01(_0_line__out__1[14]), .plus_00_00(_0_line__out__1[13]), .plus_00_01_2(_0_line__out__1[12]),
    .plus_01_01(_1_line[17]), .plus_01_00(_1_line[18]), .plus_01_01_2(_1_line[19]),
    .neighbours(neighboursstd_not_used_19_neighbours));
  aliveSTD___not_used alivestd_not_used_19 (
    .neighbours(neighboursstd_not_used_19_neighbours), .alive(plus_00_18new), .pause(pause),
    .input_state(state_helper_19_output_state));
  STATE_helper state_helper_19 (
    .input_state(input_state), .output_state(state_helper_19_output_state), .i(I), .j(J[18]));
  neighboursSTD__not_used neighboursstd_not_used_20 (
    .minus_01_01(minus_1_line[18]), .minus_01_00(minus_1_line[19]), .minus_01_01_2(minus_1_line[20]),
    .plus_00_01(_0_line__out__1[13]), .plus_00_00(_0_line__out__1[12]), .plus_00_01_2(_0_line__out__1[11]),
    .plus_01_01(_1_line[18]), .plus_01_00(_1_line[19]), .plus_01_01_2(_1_line[20]),
    .neighbours(neighboursstd_not_used_20_neighbours));
  aliveSTD___not_used alivestd_not_used_20 (
    .neighbours(neighboursstd_not_used_20_neighbours), .alive(plus_00_19new), .pause(pause),
    .input_state(state_helper_20_output_state));
  STATE_helper state_helper_20 (
    .input_state(input_state), .output_state(state_helper_20_output_state), .i(I), .j(J[19]));
  neighboursSTD__not_used neighboursstd_not_used_21 (
    .minus_01_01(minus_1_line[19]), .minus_01_00(minus_1_line[20]), .minus_01_01_2(minus_1_line[21]),
    .plus_00_01(_0_line__out__1[12]), .plus_00_00(_0_line__out__1[11]), .plus_00_01_2(_0_line__out__1[10]),
    .plus_01_01(_1_line[19]), .plus_01_00(_1_line[20]), .plus_01_01_2(_1_line[21]),
    .neighbours(neighboursstd_not_used_21_neighbours));
  aliveSTD___not_used alivestd_not_used_21 (
    .neighbours(neighboursstd_not_used_21_neighbours), .alive(plus_00_20new), .pause(pause),
    .input_state(state_helper_21_output_state));
  STATE_helper state_helper_21 (
    .input_state(input_state), .output_state(state_helper_21_output_state), .i(I), .j(J[20]));
  neighboursSTD__not_used neighboursstd_not_used_22 (
    .minus_01_01(minus_1_line[20]), .minus_01_00(minus_1_line[21]), .minus_01_01_2(minus_1_line[22]),
    .plus_00_01(_0_line__out__1[11]), .plus_00_00(_0_line__out__1[10]), .plus_00_01_2(_0_line__out__1[9]),
    .plus_01_01(_1_line[20]), .plus_01_00(_1_line[21]), .plus_01_01_2(_1_line[22]),
    .neighbours(neighboursstd_not_used_22_neighbours));
  aliveSTD___not_used alivestd_not_used_22 (
    .neighbours(neighboursstd_not_used_22_neighbours), .alive(plus_00_21new), .pause(pause),
    .input_state(state_helper_22_output_state));
  STATE_helper state_helper_22 (
    .input_state(input_state), .output_state(state_helper_22_output_state), .i(I), .j(J[21]));
  neighboursSTD__not_used neighboursstd_not_used_23 (
    .minus_01_01(minus_1_line[21]), .minus_01_00(minus_1_line[22]), .minus_01_01_2(minus_1_line[23]),
    .plus_00_01(_0_line__out__1[10]), .plus_00_00(_0_line__out__1[9]), .plus_00_01_2(_0_line__out__1[8]),
    .plus_01_01(_1_line[21]), .plus_01_00(_1_line[22]), .plus_01_01_2(_1_line[23]),
    .neighbours(neighboursstd_not_used_23_neighbours));
  aliveSTD___not_used alivestd_not_used_23 (
    .neighbours(neighboursstd_not_used_23_neighbours), .alive(plus_00_22new), .pause(pause),
    .input_state(state_helper_23_output_state));
  STATE_helper state_helper_23 (
    .input_state(input_state), .output_state(state_helper_23_output_state), .i(I), .j(J[22]));
  neighboursSTD__not_used neighboursstd_not_used_24 (
    .minus_01_01(minus_1_line[22]), .minus_01_00(minus_1_line[23]), .minus_01_01_2(minus_1_line[24]),
    .plus_00_01(_0_line__out__1[9]), .plus_00_00(_0_line__out__1[8]), .plus_00_01_2(_0_line__out__1[7]),
    .plus_01_01(_1_line[22]), .plus_01_00(_1_line[23]), .plus_01_01_2(_1_line[24]),
    .neighbours(neighboursstd_not_used_24_neighbours));
  aliveSTD___not_used alivestd_not_used_24 (
    .neighbours(neighboursstd_not_used_24_neighbours), .alive(plus_00_23new), .pause(pause),
    .input_state(state_helper_24_output_state));
  STATE_helper state_helper_24 (
    .input_state(input_state), .output_state(state_helper_24_output_state), .i(I), .j(J[23]));
  neighboursSTD__not_used neighboursstd_not_used_25 (
    .minus_01_01(minus_1_line[23]), .minus_01_00(minus_1_line[24]), .minus_01_01_2(minus_1_line[25]),
    .plus_00_01(_0_line__out__1[8]), .plus_00_00(_0_line__out__1[7]), .plus_00_01_2(_0_line__out__1[6]),
    .plus_01_01(_1_line[23]), .plus_01_00(_1_line[24]), .plus_01_01_2(_1_line[25]),
    .neighbours(neighboursstd_not_used_25_neighbours));
  aliveSTD___not_used alivestd_not_used_25 (
    .neighbours(neighboursstd_not_used_25_neighbours), .alive(plus_00_24new), .pause(pause),
    .input_state(state_helper_25_output_state));
  STATE_helper state_helper_25 (
    .input_state(input_state), .output_state(state_helper_25_output_state), .i(I), .j(J[24]));
  neighboursSTD__not_used neighboursstd_not_used_26 (
    .minus_01_01(minus_1_line[24]), .minus_01_00(minus_1_line[25]), .minus_01_01_2(minus_1_line[26]),
    .plus_00_01(_0_line__out__1[7]), .plus_00_00(_0_line__out__1[6]), .plus_00_01_2(_0_line__out__1[5]),
    .plus_01_01(_1_line[24]), .plus_01_00(_1_line[25]), .plus_01_01_2(_1_line[26]),
    .neighbours(neighboursstd_not_used_26_neighbours));
  aliveSTD___not_used alivestd_not_used_26 (
    .neighbours(neighboursstd_not_used_26_neighbours), .alive(plus_00_25new), .pause(pause),
    .input_state(state_helper_26_output_state));
  STATE_helper state_helper_26 (
    .input_state(input_state), .output_state(state_helper_26_output_state), .i(I), .j(J[25]));
  neighboursSTD__not_used neighboursstd_not_used_27 (
    .minus_01_01(minus_1_line[25]), .minus_01_00(minus_1_line[26]), .minus_01_01_2(minus_1_line[27]),
    .plus_00_01(_0_line__out__1[6]), .plus_00_00(_0_line__out__1[5]), .plus_00_01_2(_0_line__out__1[4]),
    .plus_01_01(_1_line[25]), .plus_01_00(_1_line[26]), .plus_01_01_2(_1_line[27]),
    .neighbours(neighboursstd_not_used_27_neighbours));
  aliveSTD___not_used alivestd_not_used_27 (
    .neighbours(neighboursstd_not_used_27_neighbours), .alive(plus_00_26new), .pause(pause),
    .input_state(state_helper_27_output_state));
  STATE_helper state_helper_27 (
    .input_state(input_state), .output_state(state_helper_27_output_state), .i(I), .j(J[26]));
  neighboursSTD__not_used neighboursstd_not_used_28 (
    .minus_01_01(minus_1_line[26]), .minus_01_00(minus_1_line[27]), .minus_01_01_2(minus_1_line[28]),
    .plus_00_01(_0_line__out__1[5]), .plus_00_00(_0_line__out__1[4]), .plus_00_01_2(_0_line__out__1[3]),
    .plus_01_01(_1_line[26]), .plus_01_00(_1_line[27]), .plus_01_01_2(_1_line[28]),
    .neighbours(neighboursstd_not_used_28_neighbours));
  aliveSTD___not_used alivestd_not_used_28 (
    .neighbours(neighboursstd_not_used_28_neighbours), .alive(plus_00_27new), .pause(pause),
    .input_state(state_helper_28_output_state));
  STATE_helper state_helper_28 (
    .input_state(input_state), .output_state(state_helper_28_output_state), .i(I), .j(J[27]));
  neighboursSTD__not_used neighboursstd_not_used_29 (
    .minus_01_01(minus_1_line[27]), .minus_01_00(minus_1_line[28]), .minus_01_01_2(minus_1_line[29]),
    .plus_00_01(_0_line__out__1[4]), .plus_00_00(_0_line__out__1[3]), .plus_00_01_2(_0_line__out__1[2]),
    .plus_01_01(_1_line[27]), .plus_01_00(_1_line[28]), .plus_01_01_2(_1_line[29]),
    .neighbours(neighboursstd_not_used_29_neighbours));
  aliveSTD___not_used alivestd_not_used_29 (
    .neighbours(neighboursstd_not_used_29_neighbours), .alive(plus_00_28new), .pause(pause),
    .input_state(state_helper_29_output_state));
  STATE_helper state_helper_29 (
    .input_state(input_state), .output_state(state_helper_29_output_state), .i(I), .j(J[28]));
  neighboursSTD__not_used neighboursstd_not_used_30 (
    .minus_01_01(minus_1_line[28]), .minus_01_00(minus_1_line[29]), .minus_01_01_2(minus_1_line[30]),
    .plus_00_01(_0_line__out__1[3]), .plus_00_00(_0_line__out__1[2]), .plus_00_01_2(_0_line__out__1[1]),
    .plus_01_01(_1_line[28]), .plus_01_00(_1_line[29]), .plus_01_01_2(_1_line[30]),
    .neighbours(neighboursstd_not_used_30_neighbours));
  aliveSTD___not_used alivestd_not_used_30 (
    .neighbours(neighboursstd_not_used_30_neighbours), .alive(plus_00_29new), .pause(pause),
    .input_state(state_helper_30_output_state));
  STATE_helper state_helper_30 (
    .input_state(input_state), .output_state(state_helper_30_output_state), .i(I), .j(J[29]));
  neighboursSTD__not_used neighboursstd_not_used_31 (
    .minus_01_01(minus_1_line[29]), .minus_01_00(minus_1_line[30]), .minus_01_01_2(minus_1_line[31]),
    .plus_00_01(_0_line__out__1[2]), .plus_00_00(_0_line__out__1[1]), .plus_00_01_2(_0_line__out__1[0]),
    .plus_01_01(_1_line[29]), .plus_01_00(_1_line[30]), .plus_01_01_2(_1_line[31]),
    .neighbours(neighboursstd_not_used_31_neighbours));
  aliveSTD___not_used alivestd_not_used_31 (
    .neighbours(neighboursstd_not_used_31_neighbours), .alive(plus_00_30new), .pause(pause),
    .input_state(state_helper_31_output_state));
  STATE_helper state_helper_31 (
    .input_state(input_state), .output_state(state_helper_31_output_state), .i(I), .j(J[30]));
  neighboursSTD__not_used neighboursstd_not_used_32 (
    .minus_01_01(minus_1_line[30]), .minus_01_00(minus_1_line[31]), .minus_01_01_2(minus_01_32),
    .plus_00_01(_0_line__out__1[1]), .plus_00_00(_0_line__out__1[0]), .plus_00_01_2(plus_00_32),
    .plus_01_01(_1_line[30]), .plus_01_00(_1_line[31]), .plus_01_01_2(plus_01_32),
    .neighbours(neighboursstd_not_used_32_neighbours));
  aliveSTD___not_used alivestd_not_used_32 (
    .neighbours(neighboursstd_not_used_32_neighbours), .alive(plus_00_31new), .pause(pause),
    .input_state(state_helper_32_output_state));
  STATE_helper state_helper_32 (
    .input_state(input_state), .output_state(state_helper_32_output_state), .i(I), .j(J[31]));

  assign _0_line__out__1_2 = _0_line__out__1;
  assign display = _0_line__out__1;

  // Other names for the same wires on the sheet: plus_00_31 = _0_line__out__1[0]; plus_00_30 = _0_line__out__1[1];
  //   plus_00_29 = _0_line__out__1[2]; plus_00_28 = _0_line__out__1[3]; plus_00_27 = _0_line__out__1[4];
  //   plus_00_26 = _0_line__out__1[5]; plus_00_25 = _0_line__out__1[6]; plus_00_24 = _0_line__out__1[7];
  //   plus_00_23 = _0_line__out__1[8]; plus_00_22 = _0_line__out__1[9]; plus_00_21 = _0_line__out__1[10];
  //   plus_00_20 = _0_line__out__1[11]; plus_00_19 = _0_line__out__1[12]; plus_00_18 = _0_line__out__1[13];
  //   plus_00_17 = _0_line__out__1[14]; plus_00_16 = _0_line__out__1[15]; plus_00_15 = _0_line__out__1[16];
  //   plus_00_14 = _0_line__out__1[17]; plus_00_13 = _0_line__out__1[18]; plus_00_12 = _0_line__out__1[19];
  //   plus_00_11 = _0_line__out__1[20]; plus_00_10 = _0_line__out__1[21]; plus_00_09 = _0_line__out__1[22];
  //   plus_00_08 = _0_line__out__1[23]; plus_00_07 = _0_line__out__1[24]; plus_00_06 = _0_line__out__1[25];
  //   plus_00_05 = _0_line__out__1[26]; plus_00_04 = _0_line__out__1[27]; plus_00_03 = _0_line__out__1[28];
  //   plus_00_02 = _0_line__out__1[29]; plus_00_01 = _0_line__out__1[30]; plus_00_00 = _0_line__out__1[31];
  //   plus_01_00 = _1_line[0]; plus_01_01 = _1_line[1]; plus_01_02 = _1_line[2]; plus_01_03 = _1_line[3];
  //   plus_01_04 = _1_line[4]; plus_01_05 = _1_line[5]; plus_01_06 = _1_line[6]; plus_01_07 = _1_line[7];
  //   plus_01_08 = _1_line[8]; plus_01_09 = _1_line[9]; plus_01_10 = _1_line[10]; plus_01_11 = _1_line[11];
  //   plus_01_12 = _1_line[12]; plus_01_13 = _1_line[13]; plus_01_14 = _1_line[14]; plus_01_15 = _1_line[15];
  //   plus_01_16 = _1_line[16]; plus_01_17 = _1_line[17]; plus_01_18 = _1_line[18]; plus_01_19 = _1_line[19];
  //   plus_01_20 = _1_line[20]; plus_01_21 = _1_line[21]; plus_01_22 = _1_line[22]; plus_01_23 = _1_line[23];
  //   plus_01_24 = _1_line[24]; plus_01_25 = _1_line[25]; plus_01_26 = _1_line[26]; plus_01_27 = _1_line[27];
  //   plus_01_28 = _1_line[28]; plus_01_29 = _1_line[29]; plus_01_30 = _1_line[30]; plus_01_31 = _1_line[31];
  //   minus_01_00 = minus_1_line[0]; minus_01_01 = minus_1_line[1]; minus_01_02 = minus_1_line[2];
  //   minus_01_03 = minus_1_line[3]; minus_01_04 = minus_1_line[4]; minus_01_05 = minus_1_line[5];
  //   minus_01_06 = minus_1_line[6]; minus_01_07 = minus_1_line[7]; minus_01_08 = minus_1_line[8];
  //   minus_01_09 = minus_1_line[9]; minus_01_10 = minus_1_line[10]; minus_01_11 = minus_1_line[11];
  //   minus_01_12 = minus_1_line[12]; minus_01_13 = minus_1_line[13]; minus_01_14 = minus_1_line[14];
  //   minus_01_15 = minus_1_line[15]; minus_01_16 = minus_1_line[16]; minus_01_17 = minus_1_line[17];
  //   minus_01_18 = minus_1_line[18]; minus_01_19 = minus_1_line[19]; minus_01_20 = minus_1_line[20];
  //   minus_01_21 = minus_1_line[21]; minus_01_22 = minus_1_line[22]; minus_01_23 = minus_1_line[23];
  //   minus_01_24 = minus_1_line[24]; minus_01_25 = minus_1_line[25]; minus_01_26 = minus_1_line[26];
  //   minus_01_27 = minus_1_line[27]; minus_01_28 = minus_1_line[28]; minus_01_29 = minus_1_line[29];
  //   minus_01_30 = minus_1_line[30]; minus_01_31 = minus_1_line[31]; state[1:0] = input_state

  // Notes on the sheet:
  //   clock: pull=down
  //   pause: pull=down
endmodule

module lineSTD_old__not_used (
  input  [31:0] J,
  input  [31:0] minus_1_line,
  input  [31:0] _1_line,
  input  I,
  input  Torus,
  input  [1:0] input_state,
  input  clock,
  input  pause,
  output [31:0] _0_line__out__1,
  output [31:0] display,
  output [31:0] _0_line__out__1_2
);

  wire minus_01_01_t, minus_01_32, plus_00_01_t, plus_00_32, plus_01_01_t, plus_01_32;
  wire [1:0] alivestd_old_not_used_1_p5, alivestd_old_not_used_2_p8, alivestd_old_not_used_3_p8,
       alivestd_old_not_used_4_p8, alivestd_old_not_used_5_p8, alivestd_old_not_used_6_p8,
       alivestd_old_not_used_7_p8, alivestd_old_not_used_8_p8, alivestd_old_not_used_9_p8,
       alivestd_old_not_used_10_p8, alivestd_old_not_used_11_p8, alivestd_old_not_used_12_p8,
       alivestd_old_not_used_13_p8, alivestd_old_not_used_14_p8, alivestd_old_not_used_15_p8,
       alivestd_old_not_used_16_p8, alivestd_old_not_used_17_p8, alivestd_old_not_used_18_p8,
       alivestd_old_not_used_19_p8, alivestd_old_not_used_20_p8, alivestd_old_not_used_21_p8,
       alivestd_old_not_used_22_p8, alivestd_old_not_used_23_p8, alivestd_old_not_used_24_p8,
       alivestd_old_not_used_25_p8, alivestd_old_not_used_26_p8, alivestd_old_not_used_27_p8,
       alivestd_old_not_used_28_p8, alivestd_old_not_used_29_p8, alivestd_old_not_used_30_p8,
       alivestd_old_not_used_31_p8, alivestd_old_not_used_32_p8;
  wire [8:0] lookAt, neighboursstd_not_used_1_neighbours, neighboursstd_not_used_2_neighbours,
       neighboursstd_not_used_3_neighbours, neighboursstd_not_used_4_neighbours,
       neighboursstd_not_used_5_neighbours, neighboursstd_not_used_6_neighbours,
       neighboursstd_not_used_7_neighbours, neighboursstd_not_used_8_neighbours,
       neighboursstd_not_used_9_neighbours, neighboursstd_not_used_10_neighbours,
       neighboursstd_not_used_11_neighbours, neighboursstd_not_used_12_neighbours,
       neighboursstd_not_used_13_neighbours, neighboursstd_not_used_14_neighbours,
       neighboursstd_not_used_15_neighbours, neighboursstd_not_used_16_neighbours,
       neighboursstd_not_used_17_neighbours, neighboursstd_not_used_18_neighbours,
       neighboursstd_not_used_19_neighbours, neighboursstd_not_used_20_neighbours,
       neighboursstd_not_used_21_neighbours, neighboursstd_not_used_22_neighbours,
       neighboursstd_not_used_23_neighbours, neighboursstd_not_used_24_neighbours,
       neighboursstd_not_used_25_neighbours, neighboursstd_not_used_26_neighbours,
       neighboursstd_not_used_27_neighbours, neighboursstd_not_used_28_neighbours,
       neighboursstd_not_used_29_neighbours, neighboursstd_not_used_30_neighbours,
       neighboursstd_not_used_31_neighbours, neighboursstd_not_used_32_neighbours;
  wire [29:0] birth, save;

  neighboursSTD__not_used neighboursstd_not_used_1 (
    .minus_01_01(minus_01_01_t), .minus_01_00(minus_1_line[0]), .minus_01_01_2(minus_1_line[1]),
    .plus_00_01(plus_00_01_t), .plus_00_00(_0_line__out__1[31]), .plus_00_01_2(_0_line__out__1[30]),
    .plus_01_01(plus_01_01_t), .plus_01_00(_1_line[0]), .plus_01_01_2(_1_line[1]),
    .neighbours(neighboursstd_not_used_1_neighbours));
  // aliveSTD__old__not_used alivestd_old_not_used_1: pin names not known; wires that end beside it: neighboursstd_not_used_1_neighbours, clock, _0_line__out__1[31], pause, alivestd_old_not_used_1_p5
  STATE_helper state_helper_1 (.input_state(input_state), .output_state(alivestd_old_not_used_1_p5), .i(I), .j(J[0]));
  and and_1 (minus_01_32, minus_1_line[0], Torus);
  and and_2 (minus_01_01_t, minus_1_line[31], Torus);
  neighboursSTD__not_used neighboursstd_not_used_2 (
    .minus_01_01(minus_1_line[0]), .minus_01_00(minus_1_line[1]), .minus_01_01_2(minus_1_line[2]),
    .plus_00_01(_0_line__out__1[31]), .plus_00_00(_0_line__out__1[30]), .plus_00_01_2(_0_line__out__1[29]),
    .plus_01_01(_1_line[0]), .plus_01_00(_1_line[1]), .plus_01_01_2(_1_line[2]),
    .neighbours(neighboursstd_not_used_2_neighbours));
  // aliveSTD__old__not_used alivestd_old_not_used_2: pin names not known; wires that end beside it: neighboursstd_not_used_2_neighbours, lookAt, birth, save, clock, _0_line__out__1[30], pause, alivestd_old_not_used_2_p8
  STATE_helper state_helper_2 (.input_state(input_state), .output_state(alivestd_old_not_used_2_p8), .i(I), .j(J[1]));
  and and_3 (plus_01_32, _1_line[0], Torus);
  and and_4 (plus_01_01_t, _1_line[31], Torus);
  and and_5 (plus_00_32, _0_line__out__1[31], Torus);
  and and_6 (plus_00_01_t, _0_line__out__1[0], Torus);
  neighboursSTD__not_used neighboursstd_not_used_3 (
    .minus_01_01(minus_1_line[1]), .minus_01_00(minus_1_line[2]), .minus_01_01_2(minus_1_line[3]),
    .plus_00_01(_0_line__out__1[30]), .plus_00_00(_0_line__out__1[29]), .plus_00_01_2(_0_line__out__1[28]),
    .plus_01_01(_1_line[1]), .plus_01_00(_1_line[2]), .plus_01_01_2(_1_line[3]),
    .neighbours(neighboursstd_not_used_3_neighbours));
  // aliveSTD__old__not_used alivestd_old_not_used_3: pin names not known; wires that end beside it: neighboursstd_not_used_3_neighbours, lookAt, birth, save, clock, _0_line__out__1[29], pause, alivestd_old_not_used_3_p8
  STATE_helper state_helper_3 (.input_state(input_state), .output_state(alivestd_old_not_used_3_p8), .i(I), .j(J[2]));
  neighboursSTD__not_used neighboursstd_not_used_4 (
    .minus_01_01(minus_1_line[2]), .minus_01_00(minus_1_line[3]), .minus_01_01_2(minus_1_line[4]),
    .plus_00_01(_0_line__out__1[29]), .plus_00_00(_0_line__out__1[28]), .plus_00_01_2(_0_line__out__1[27]),
    .plus_01_01(_1_line[2]), .plus_01_00(_1_line[3]), .plus_01_01_2(_1_line[4]),
    .neighbours(neighboursstd_not_used_4_neighbours));
  // aliveSTD__old__not_used alivestd_old_not_used_4: pin names not known; wires that end beside it: neighboursstd_not_used_4_neighbours, lookAt, birth, save, clock, _0_line__out__1[28], pause, alivestd_old_not_used_4_p8
  STATE_helper state_helper_4 (.input_state(input_state), .output_state(alivestd_old_not_used_4_p8), .i(I), .j(J[3]));
  Pull_Resistor pull_resistor_1 (.node(_0_line__out__1[31]));
  Pull_Resistor pull_resistor_2 ();  // open: node
  Pull_Resistor pull_resistor_3 (.node(_0_line__out__1[29]));
  Pull_Resistor pull_resistor_4 ();  // open: node
  Pull_Resistor pull_resistor_5 (.node(_0_line__out__1[27]));
  Pull_Resistor pull_resistor_6 ();  // open: node
  Pull_Resistor pull_resistor_7 (.node(_0_line__out__1[25]));
  Pull_Resistor pull_resistor_8 ();  // open: node
  Pull_Resistor pull_resistor_9 (.node(_0_line__out__1[23]));
  Pull_Resistor pull_resistor_10 ();  // open: node
  Pull_Resistor pull_resistor_11 (.node(_0_line__out__1[21]));
  Pull_Resistor pull_resistor_12 ();  // open: node
  Pull_Resistor pull_resistor_13 (.node(_0_line__out__1[19]));
  Pull_Resistor pull_resistor_14 ();  // open: node
  Pull_Resistor pull_resistor_15 (.node(_0_line__out__1[17]));
  Pull_Resistor pull_resistor_16 ();  // open: node
  Pull_Resistor pull_resistor_17 (.node(_0_line__out__1[15]));
  Pull_Resistor pull_resistor_18 ();  // open: node
  Pull_Resistor pull_resistor_19 (.node(_0_line__out__1[13]));
  Pull_Resistor pull_resistor_20 ();  // open: node
  Pull_Resistor pull_resistor_21 (.node(_0_line__out__1[11]));
  Pull_Resistor pull_resistor_22 ();  // open: node
  Pull_Resistor pull_resistor_23 (.node(_0_line__out__1[9]));
  Pull_Resistor pull_resistor_24 ();  // open: node
  Pull_Resistor pull_resistor_25 (.node(_0_line__out__1[7]));
  Pull_Resistor pull_resistor_26 ();  // open: node
  Pull_Resistor pull_resistor_27 (.node(_0_line__out__1[5]));
  Pull_Resistor pull_resistor_28 ();  // open: node
  Pull_Resistor pull_resistor_29 (.node(_0_line__out__1[3]));
  Pull_Resistor pull_resistor_30 ();  // open: node
  Pull_Resistor pull_resistor_31 (.node(_0_line__out__1[1]));
  Pull_Resistor pull_resistor_32 ();  // open: node
  neighboursSTD__not_used neighboursstd_not_used_5 (
    .minus_01_01(minus_1_line[3]), .minus_01_00(minus_1_line[4]), .minus_01_01_2(minus_1_line[5]),
    .plus_00_01(_0_line__out__1[28]), .plus_00_00(_0_line__out__1[27]), .plus_00_01_2(_0_line__out__1[26]),
    .plus_01_01(_1_line[3]), .plus_01_00(_1_line[4]), .plus_01_01_2(_1_line[5]),
    .neighbours(neighboursstd_not_used_5_neighbours));
  // aliveSTD__old__not_used alivestd_old_not_used_5: pin names not known; wires that end beside it: neighboursstd_not_used_5_neighbours, lookAt, birth, save, clock, _0_line__out__1[27], pause, alivestd_old_not_used_5_p8
  STATE_helper state_helper_5 (.input_state(input_state), .output_state(alivestd_old_not_used_5_p8), .i(I), .j(J[4]));
  neighboursSTD__not_used neighboursstd_not_used_6 (
    .minus_01_01(minus_1_line[4]), .minus_01_00(minus_1_line[5]), .minus_01_01_2(minus_1_line[6]),
    .plus_00_01(_0_line__out__1[27]), .plus_00_00(_0_line__out__1[26]), .plus_00_01_2(_0_line__out__1[25]),
    .plus_01_01(_1_line[4]), .plus_01_00(_1_line[5]), .plus_01_01_2(_1_line[6]),
    .neighbours(neighboursstd_not_used_6_neighbours));
  // aliveSTD__old__not_used alivestd_old_not_used_6: pin names not known; wires that end beside it: neighboursstd_not_used_6_neighbours, lookAt, birth, save, clock, _0_line__out__1[26], pause, alivestd_old_not_used_6_p8
  STATE_helper state_helper_6 (.input_state(input_state), .output_state(alivestd_old_not_used_6_p8), .i(I), .j(J[5]));
  neighboursSTD__not_used neighboursstd_not_used_7 (
    .minus_01_01(minus_1_line[5]), .minus_01_00(minus_1_line[6]), .minus_01_01_2(minus_1_line[7]),
    .plus_00_01(_0_line__out__1[26]), .plus_00_00(_0_line__out__1[25]), .plus_00_01_2(_0_line__out__1[24]),
    .plus_01_01(_1_line[5]), .plus_01_00(_1_line[6]), .plus_01_01_2(_1_line[7]),
    .neighbours(neighboursstd_not_used_7_neighbours));
  // aliveSTD__old__not_used alivestd_old_not_used_7: pin names not known; wires that end beside it: neighboursstd_not_used_7_neighbours, lookAt, birth, save, clock, _0_line__out__1[25], pause, alivestd_old_not_used_7_p8
  STATE_helper state_helper_7 (.input_state(input_state), .output_state(alivestd_old_not_used_7_p8), .i(I), .j(J[6]));
  neighboursSTD__not_used neighboursstd_not_used_8 (
    .minus_01_01(minus_1_line[6]), .minus_01_00(minus_1_line[7]), .minus_01_01_2(minus_1_line[8]),
    .plus_00_01(_0_line__out__1[25]), .plus_00_00(_0_line__out__1[24]), .plus_00_01_2(_0_line__out__1[23]),
    .plus_01_01(_1_line[6]), .plus_01_00(_1_line[7]), .plus_01_01_2(_1_line[8]),
    .neighbours(neighboursstd_not_used_8_neighbours));
  // aliveSTD__old__not_used alivestd_old_not_used_8: pin names not known; wires that end beside it: neighboursstd_not_used_8_neighbours, lookAt, birth, save, clock, _0_line__out__1[24], pause, alivestd_old_not_used_8_p8
  STATE_helper state_helper_8 (.input_state(input_state), .output_state(alivestd_old_not_used_8_p8), .i(I), .j(J[7]));
  neighboursSTD__not_used neighboursstd_not_used_9 (
    .minus_01_01(minus_1_line[7]), .minus_01_00(minus_1_line[8]), .minus_01_01_2(minus_1_line[9]),
    .plus_00_01(_0_line__out__1[24]), .plus_00_00(_0_line__out__1[23]), .plus_00_01_2(_0_line__out__1[22]),
    .plus_01_01(_1_line[7]), .plus_01_00(_1_line[8]), .plus_01_01_2(_1_line[9]),
    .neighbours(neighboursstd_not_used_9_neighbours));
  // aliveSTD__old__not_used alivestd_old_not_used_9: pin names not known; wires that end beside it: neighboursstd_not_used_9_neighbours, lookAt, birth, save, clock, _0_line__out__1[23], pause, alivestd_old_not_used_9_p8
  STATE_helper state_helper_9 (.input_state(input_state), .output_state(alivestd_old_not_used_9_p8), .i(I), .j(J[8]));
  neighboursSTD__not_used neighboursstd_not_used_10 (
    .minus_01_01(minus_1_line[8]), .minus_01_00(minus_1_line[9]), .minus_01_01_2(minus_1_line[10]),
    .plus_00_01(_0_line__out__1[23]), .plus_00_00(_0_line__out__1[22]), .plus_00_01_2(_0_line__out__1[21]),
    .plus_01_01(_1_line[8]), .plus_01_00(_1_line[9]), .plus_01_01_2(_1_line[10]),
    .neighbours(neighboursstd_not_used_10_neighbours));
  // aliveSTD__old__not_used alivestd_old_not_used_10: pin names not known; wires that end beside it: neighboursstd_not_used_10_neighbours, lookAt, birth, save, clock, _0_line__out__1[22], pause, alivestd_old_not_used_10_p8
  STATE_helper state_helper_10 (.input_state(input_state), .output_state(alivestd_old_not_used_10_p8), .i(I), .j(J[9]));
  neighboursSTD__not_used neighboursstd_not_used_11 (
    .minus_01_01(minus_1_line[9]), .minus_01_00(minus_1_line[10]), .minus_01_01_2(minus_1_line[11]),
    .plus_00_01(_0_line__out__1[22]), .plus_00_00(_0_line__out__1[21]), .plus_00_01_2(_0_line__out__1[20]),
    .plus_01_01(_1_line[9]), .plus_01_00(_1_line[10]), .plus_01_01_2(_1_line[11]),
    .neighbours(neighboursstd_not_used_11_neighbours));
  // aliveSTD__old__not_used alivestd_old_not_used_11: pin names not known; wires that end beside it: neighboursstd_not_used_11_neighbours, lookAt, birth, save, clock, _0_line__out__1[21], pause, alivestd_old_not_used_11_p8
  STATE_helper state_helper_11 (
    .input_state(input_state), .output_state(alivestd_old_not_used_11_p8), .i(I), .j(J[10]));
  neighboursSTD__not_used neighboursstd_not_used_12 (
    .minus_01_01(minus_1_line[10]), .minus_01_00(minus_1_line[11]), .minus_01_01_2(minus_1_line[12]),
    .plus_00_01(_0_line__out__1[21]), .plus_00_00(_0_line__out__1[20]), .plus_00_01_2(_0_line__out__1[19]),
    .plus_01_01(_1_line[10]), .plus_01_00(_1_line[11]), .plus_01_01_2(_1_line[12]),
    .neighbours(neighboursstd_not_used_12_neighbours));
  // aliveSTD__old__not_used alivestd_old_not_used_12: pin names not known; wires that end beside it: neighboursstd_not_used_12_neighbours, lookAt, birth, save, clock, _0_line__out__1[20], pause, alivestd_old_not_used_12_p8
  STATE_helper state_helper_12 (
    .input_state(input_state), .output_state(alivestd_old_not_used_12_p8), .i(I), .j(J[11]));
  neighboursSTD__not_used neighboursstd_not_used_13 (
    .minus_01_01(minus_1_line[11]), .minus_01_00(minus_1_line[12]), .minus_01_01_2(minus_1_line[13]),
    .plus_00_01(_0_line__out__1[20]), .plus_00_00(_0_line__out__1[19]), .plus_00_01_2(_0_line__out__1[18]),
    .plus_01_01(_1_line[11]), .plus_01_00(_1_line[12]), .plus_01_01_2(_1_line[13]),
    .neighbours(neighboursstd_not_used_13_neighbours));
  // aliveSTD__old__not_used alivestd_old_not_used_13: pin names not known; wires that end beside it: neighboursstd_not_used_13_neighbours, lookAt, birth, save, clock, _0_line__out__1[19], pause, alivestd_old_not_used_13_p8
  STATE_helper state_helper_13 (
    .input_state(input_state), .output_state(alivestd_old_not_used_13_p8), .i(I), .j(J[12]));
  neighboursSTD__not_used neighboursstd_not_used_14 (
    .minus_01_01(minus_1_line[12]), .minus_01_00(minus_1_line[13]), .minus_01_01_2(minus_1_line[14]),
    .plus_00_01(_0_line__out__1[19]), .plus_00_00(_0_line__out__1[18]), .plus_00_01_2(_0_line__out__1[17]),
    .plus_01_01(_1_line[12]), .plus_01_00(_1_line[13]), .plus_01_01_2(_1_line[14]),
    .neighbours(neighboursstd_not_used_14_neighbours));
  // aliveSTD__old__not_used alivestd_old_not_used_14: pin names not known; wires that end beside it: neighboursstd_not_used_14_neighbours, lookAt, birth, save, clock, _0_line__out__1[18], pause, alivestd_old_not_used_14_p8
  STATE_helper state_helper_14 (
    .input_state(input_state), .output_state(alivestd_old_not_used_14_p8), .i(I), .j(J[13]));
  neighboursSTD__not_used neighboursstd_not_used_15 (
    .minus_01_01(minus_1_line[13]), .minus_01_00(minus_1_line[14]), .minus_01_01_2(minus_1_line[15]),
    .plus_00_01(_0_line__out__1[18]), .plus_00_00(_0_line__out__1[17]), .plus_00_01_2(_0_line__out__1[16]),
    .plus_01_01(_1_line[13]), .plus_01_00(_1_line[14]), .plus_01_01_2(_1_line[15]),
    .neighbours(neighboursstd_not_used_15_neighbours));
  // aliveSTD__old__not_used alivestd_old_not_used_15: pin names not known; wires that end beside it: neighboursstd_not_used_15_neighbours, lookAt, birth, save, clock, _0_line__out__1[17], pause, alivestd_old_not_used_15_p8
  STATE_helper state_helper_15 (
    .input_state(input_state), .output_state(alivestd_old_not_used_15_p8), .i(I), .j(J[14]));
  neighboursSTD__not_used neighboursstd_not_used_16 (
    .minus_01_01(minus_1_line[14]), .minus_01_00(minus_1_line[15]), .minus_01_01_2(minus_1_line[16]),
    .plus_00_01(_0_line__out__1[17]), .plus_00_00(_0_line__out__1[16]), .plus_00_01_2(_0_line__out__1[15]),
    .plus_01_01(_1_line[14]), .plus_01_00(_1_line[15]), .plus_01_01_2(_1_line[16]),
    .neighbours(neighboursstd_not_used_16_neighbours));
  // aliveSTD__old__not_used alivestd_old_not_used_16: pin names not known; wires that end beside it: neighboursstd_not_used_16_neighbours, lookAt, birth, save, clock, _0_line__out__1[16], pause, alivestd_old_not_used_16_p8
  STATE_helper state_helper_16 (
    .input_state(input_state), .output_state(alivestd_old_not_used_16_p8), .i(I), .j(J[15]));
  neighboursSTD__not_used neighboursstd_not_used_17 (
    .minus_01_01(minus_1_line[15]), .minus_01_00(minus_1_line[16]), .minus_01_01_2(minus_1_line[17]),
    .plus_00_01(_0_line__out__1[16]), .plus_00_00(_0_line__out__1[15]), .plus_00_01_2(_0_line__out__1[14]),
    .plus_01_01(_1_line[15]), .plus_01_00(_1_line[16]), .plus_01_01_2(_1_line[17]),
    .neighbours(neighboursstd_not_used_17_neighbours));
  // aliveSTD__old__not_used alivestd_old_not_used_17: pin names not known; wires that end beside it: neighboursstd_not_used_17_neighbours, lookAt, birth, save, clock, _0_line__out__1[15], pause, alivestd_old_not_used_17_p8
  STATE_helper state_helper_17 (
    .input_state(input_state), .output_state(alivestd_old_not_used_17_p8), .i(I), .j(J[16]));
  neighboursSTD__not_used neighboursstd_not_used_18 (
    .minus_01_01(minus_1_line[16]), .minus_01_00(minus_1_line[17]), .minus_01_01_2(minus_1_line[18]),
    .plus_00_01(_0_line__out__1[15]), .plus_00_00(_0_line__out__1[14]), .plus_00_01_2(_0_line__out__1[13]),
    .plus_01_01(_1_line[16]), .plus_01_00(_1_line[17]), .plus_01_01_2(_1_line[18]),
    .neighbours(neighboursstd_not_used_18_neighbours));
  // aliveSTD__old__not_used alivestd_old_not_used_18: pin names not known; wires that end beside it: neighboursstd_not_used_18_neighbours, lookAt, birth, save, clock, _0_line__out__1[14], pause, alivestd_old_not_used_18_p8
  STATE_helper state_helper_18 (
    .input_state(input_state), .output_state(alivestd_old_not_used_18_p8), .i(I), .j(J[17]));
  neighboursSTD__not_used neighboursstd_not_used_19 (
    .minus_01_01(minus_1_line[17]), .minus_01_00(minus_1_line[18]), .minus_01_01_2(minus_1_line[19]),
    .plus_00_01(_0_line__out__1[14]), .plus_00_00(_0_line__out__1[13]), .plus_00_01_2(_0_line__out__1[12]),
    .plus_01_01(_1_line[17]), .plus_01_00(_1_line[18]), .plus_01_01_2(_1_line[19]),
    .neighbours(neighboursstd_not_used_19_neighbours));
  // aliveSTD__old__not_used alivestd_old_not_used_19: pin names not known; wires that end beside it: neighboursstd_not_used_19_neighbours, lookAt, birth, save, clock, _0_line__out__1[13], pause, alivestd_old_not_used_19_p8
  STATE_helper state_helper_19 (
    .input_state(input_state), .output_state(alivestd_old_not_used_19_p8), .i(I), .j(J[18]));
  neighboursSTD__not_used neighboursstd_not_used_20 (
    .minus_01_01(minus_1_line[18]), .minus_01_00(minus_1_line[19]), .minus_01_01_2(minus_1_line[20]),
    .plus_00_01(_0_line__out__1[13]), .plus_00_00(_0_line__out__1[12]), .plus_00_01_2(_0_line__out__1[11]),
    .plus_01_01(_1_line[18]), .plus_01_00(_1_line[19]), .plus_01_01_2(_1_line[20]),
    .neighbours(neighboursstd_not_used_20_neighbours));
  // aliveSTD__old__not_used alivestd_old_not_used_20: pin names not known; wires that end beside it: neighboursstd_not_used_20_neighbours, lookAt, birth, save, clock, _0_line__out__1[12], pause, alivestd_old_not_used_20_p8
  STATE_helper state_helper_20 (
    .input_state(input_state), .output_state(alivestd_old_not_used_20_p8), .i(I), .j(J[19]));
  neighboursSTD__not_used neighboursstd_not_used_21 (
    .minus_01_01(minus_1_line[19]), .minus_01_00(minus_1_line[20]), .minus_01_01_2(minus_1_line[21]),
    .plus_00_01(_0_line__out__1[12]), .plus_00_00(_0_line__out__1[11]), .plus_00_01_2(_0_line__out__1[10]),
    .plus_01_01(_1_line[19]), .plus_01_00(_1_line[20]), .plus_01_01_2(_1_line[21]),
    .neighbours(neighboursstd_not_used_21_neighbours));
  // aliveSTD__old__not_used alivestd_old_not_used_21: pin names not known; wires that end beside it: neighboursstd_not_used_21_neighbours, lookAt, birth, save, clock, _0_line__out__1[11], pause, alivestd_old_not_used_21_p8
  STATE_helper state_helper_21 (
    .input_state(input_state), .output_state(alivestd_old_not_used_21_p8), .i(I), .j(J[20]));
  neighboursSTD__not_used neighboursstd_not_used_22 (
    .minus_01_01(minus_1_line[20]), .minus_01_00(minus_1_line[21]), .minus_01_01_2(minus_1_line[22]),
    .plus_00_01(_0_line__out__1[11]), .plus_00_00(_0_line__out__1[10]), .plus_00_01_2(_0_line__out__1[9]),
    .plus_01_01(_1_line[20]), .plus_01_00(_1_line[21]), .plus_01_01_2(_1_line[22]),
    .neighbours(neighboursstd_not_used_22_neighbours));
  // aliveSTD__old__not_used alivestd_old_not_used_22: pin names not known; wires that end beside it: neighboursstd_not_used_22_neighbours, lookAt, birth, save, clock, _0_line__out__1[10], pause, alivestd_old_not_used_22_p8
  STATE_helper state_helper_22 (
    .input_state(input_state), .output_state(alivestd_old_not_used_22_p8), .i(I), .j(J[21]));
  neighboursSTD__not_used neighboursstd_not_used_23 (
    .minus_01_01(minus_1_line[21]), .minus_01_00(minus_1_line[22]), .minus_01_01_2(minus_1_line[23]),
    .plus_00_01(_0_line__out__1[10]), .plus_00_00(_0_line__out__1[9]), .plus_00_01_2(_0_line__out__1[8]),
    .plus_01_01(_1_line[21]), .plus_01_00(_1_line[22]), .plus_01_01_2(_1_line[23]),
    .neighbours(neighboursstd_not_used_23_neighbours));
  // aliveSTD__old__not_used alivestd_old_not_used_23: pin names not known; wires that end beside it: neighboursstd_not_used_23_neighbours, lookAt, birth, save, clock, _0_line__out__1[9], pause, alivestd_old_not_used_23_p8
  STATE_helper state_helper_23 (
    .input_state(input_state), .output_state(alivestd_old_not_used_23_p8), .i(I), .j(J[22]));
  neighboursSTD__not_used neighboursstd_not_used_24 (
    .minus_01_01(minus_1_line[22]), .minus_01_00(minus_1_line[23]), .minus_01_01_2(minus_1_line[24]),
    .plus_00_01(_0_line__out__1[9]), .plus_00_00(_0_line__out__1[8]), .plus_00_01_2(_0_line__out__1[7]),
    .plus_01_01(_1_line[22]), .plus_01_00(_1_line[23]), .plus_01_01_2(_1_line[24]),
    .neighbours(neighboursstd_not_used_24_neighbours));
  // aliveSTD__old__not_used alivestd_old_not_used_24: pin names not known; wires that end beside it: neighboursstd_not_used_24_neighbours, lookAt, birth, save, clock, _0_line__out__1[8], pause, alivestd_old_not_used_24_p8
  STATE_helper state_helper_24 (
    .input_state(input_state), .output_state(alivestd_old_not_used_24_p8), .i(I), .j(J[23]));
  neighboursSTD__not_used neighboursstd_not_used_25 (
    .minus_01_01(minus_1_line[23]), .minus_01_00(minus_1_line[24]), .minus_01_01_2(minus_1_line[25]),
    .plus_00_01(_0_line__out__1[8]), .plus_00_00(_0_line__out__1[7]), .plus_00_01_2(_0_line__out__1[6]),
    .plus_01_01(_1_line[23]), .plus_01_00(_1_line[24]), .plus_01_01_2(_1_line[25]),
    .neighbours(neighboursstd_not_used_25_neighbours));
  // aliveSTD__old__not_used alivestd_old_not_used_25: pin names not known; wires that end beside it: neighboursstd_not_used_25_neighbours, lookAt, birth, save, clock, _0_line__out__1[7], pause, alivestd_old_not_used_25_p8
  STATE_helper state_helper_25 (
    .input_state(input_state), .output_state(alivestd_old_not_used_25_p8), .i(I), .j(J[24]));
  neighboursSTD__not_used neighboursstd_not_used_26 (
    .minus_01_01(minus_1_line[24]), .minus_01_00(minus_1_line[25]), .minus_01_01_2(minus_1_line[26]),
    .plus_00_01(_0_line__out__1[7]), .plus_00_00(_0_line__out__1[6]), .plus_00_01_2(_0_line__out__1[5]),
    .plus_01_01(_1_line[24]), .plus_01_00(_1_line[25]), .plus_01_01_2(_1_line[26]),
    .neighbours(neighboursstd_not_used_26_neighbours));
  // aliveSTD__old__not_used alivestd_old_not_used_26: pin names not known; wires that end beside it: neighboursstd_not_used_26_neighbours, lookAt, birth, save, clock, _0_line__out__1[6], pause, alivestd_old_not_used_26_p8
  STATE_helper state_helper_26 (
    .input_state(input_state), .output_state(alivestd_old_not_used_26_p8), .i(I), .j(J[25]));
  neighboursSTD__not_used neighboursstd_not_used_27 (
    .minus_01_01(minus_1_line[25]), .minus_01_00(minus_1_line[26]), .minus_01_01_2(minus_1_line[27]),
    .plus_00_01(_0_line__out__1[6]), .plus_00_00(_0_line__out__1[5]), .plus_00_01_2(_0_line__out__1[4]),
    .plus_01_01(_1_line[25]), .plus_01_00(_1_line[26]), .plus_01_01_2(_1_line[27]),
    .neighbours(neighboursstd_not_used_27_neighbours));
  // aliveSTD__old__not_used alivestd_old_not_used_27: pin names not known; wires that end beside it: neighboursstd_not_used_27_neighbours, lookAt, birth, save, clock, _0_line__out__1[5], pause, alivestd_old_not_used_27_p8
  STATE_helper state_helper_27 (
    .input_state(input_state), .output_state(alivestd_old_not_used_27_p8), .i(I), .j(J[26]));
  neighboursSTD__not_used neighboursstd_not_used_28 (
    .minus_01_01(minus_1_line[26]), .minus_01_00(minus_1_line[27]), .minus_01_01_2(minus_1_line[28]),
    .plus_00_01(_0_line__out__1[5]), .plus_00_00(_0_line__out__1[4]), .plus_00_01_2(_0_line__out__1[3]),
    .plus_01_01(_1_line[26]), .plus_01_00(_1_line[27]), .plus_01_01_2(_1_line[28]),
    .neighbours(neighboursstd_not_used_28_neighbours));
  // aliveSTD__old__not_used alivestd_old_not_used_28: pin names not known; wires that end beside it: neighboursstd_not_used_28_neighbours, lookAt, birth, save, clock, _0_line__out__1[4], pause, alivestd_old_not_used_28_p8
  STATE_helper state_helper_28 (
    .input_state(input_state), .output_state(alivestd_old_not_used_28_p8), .i(I), .j(J[27]));
  neighboursSTD__not_used neighboursstd_not_used_29 (
    .minus_01_01(minus_1_line[27]), .minus_01_00(minus_1_line[28]), .minus_01_01_2(minus_1_line[29]),
    .plus_00_01(_0_line__out__1[4]), .plus_00_00(_0_line__out__1[3]), .plus_00_01_2(_0_line__out__1[2]),
    .plus_01_01(_1_line[27]), .plus_01_00(_1_line[28]), .plus_01_01_2(_1_line[29]),
    .neighbours(neighboursstd_not_used_29_neighbours));
  // aliveSTD__old__not_used alivestd_old_not_used_29: pin names not known; wires that end beside it: neighboursstd_not_used_29_neighbours, lookAt, birth, save, clock, _0_line__out__1[3], pause, alivestd_old_not_used_29_p8
  STATE_helper state_helper_29 (
    .input_state(input_state), .output_state(alivestd_old_not_used_29_p8), .i(I), .j(J[28]));
  neighboursSTD__not_used neighboursstd_not_used_30 (
    .minus_01_01(minus_1_line[28]), .minus_01_00(minus_1_line[29]), .minus_01_01_2(minus_1_line[30]),
    .plus_00_01(_0_line__out__1[3]), .plus_00_00(_0_line__out__1[2]), .plus_00_01_2(_0_line__out__1[1]),
    .plus_01_01(_1_line[28]), .plus_01_00(_1_line[29]), .plus_01_01_2(_1_line[30]),
    .neighbours(neighboursstd_not_used_30_neighbours));
  // aliveSTD__old__not_used alivestd_old_not_used_30: pin names not known; wires that end beside it: neighboursstd_not_used_30_neighbours, lookAt, birth, save, clock, _0_line__out__1[2], pause, alivestd_old_not_used_30_p8
  STATE_helper state_helper_30 (
    .input_state(input_state), .output_state(alivestd_old_not_used_30_p8), .i(I), .j(J[29]));
  neighboursSTD__not_used neighboursstd_not_used_31 (
    .minus_01_01(minus_1_line[29]), .minus_01_00(minus_1_line[30]), .minus_01_01_2(minus_1_line[31]),
    .plus_00_01(_0_line__out__1[2]), .plus_00_00(_0_line__out__1[1]), .plus_00_01_2(_0_line__out__1[0]),
    .plus_01_01(_1_line[29]), .plus_01_00(_1_line[30]), .plus_01_01_2(_1_line[31]),
    .neighbours(neighboursstd_not_used_31_neighbours));
  // aliveSTD__old__not_used alivestd_old_not_used_31: pin names not known; wires that end beside it: neighboursstd_not_used_31_neighbours, lookAt, birth, save, clock, _0_line__out__1[1], pause, alivestd_old_not_used_31_p8
  STATE_helper state_helper_31 (
    .input_state(input_state), .output_state(alivestd_old_not_used_31_p8), .i(I), .j(J[30]));
  neighboursSTD__not_used neighboursstd_not_used_32 (
    .minus_01_01(minus_1_line[30]), .minus_01_00(minus_1_line[31]), .minus_01_01_2(minus_01_32),
    .plus_00_01(_0_line__out__1[1]), .plus_00_00(_0_line__out__1[0]), .plus_00_01_2(plus_00_32),
    .plus_01_01(_1_line[30]), .plus_01_00(_1_line[31]), .plus_01_01_2(plus_01_32),
    .neighbours(neighboursstd_not_used_32_neighbours));
  // aliveSTD__old__not_used alivestd_old_not_used_32: pin names not known; wires that end beside it: neighboursstd_not_used_32_neighbours, lookAt, birth, save, clock, _0_line__out__1[0], pause, alivestd_old_not_used_32_p8
  STATE_helper state_helper_32 (
    .input_state(input_state), .output_state(alivestd_old_not_used_32_p8), .i(I), .j(J[31]));

  assign _0_line__out__1_2 = _0_line__out__1;
  assign display = _0_line__out__1;

  // Other names for the same wires on the sheet: plus_00_31 = _0_line__out__1[0]; plus_00_30 = _0_line__out__1[1];
  //   plus_00_29 = _0_line__out__1[2]; plus_00_28 = _0_line__out__1[3]; plus_00_27 = _0_line__out__1[4];
  //   plus_00_26 = _0_line__out__1[5]; plus_00_25 = _0_line__out__1[6]; plus_00_24 = _0_line__out__1[7];
  //   plus_00_23 = _0_line__out__1[8]; plus_00_22 = _0_line__out__1[9]; plus_00_21 = _0_line__out__1[10];
  //   plus_00_20 = _0_line__out__1[11]; plus_00_19 = _0_line__out__1[12]; plus_00_18 = _0_line__out__1[13];
  //   plus_00_17 = _0_line__out__1[14]; plus_00_16 = _0_line__out__1[15]; plus_00_15 = _0_line__out__1[16];
  //   plus_00_14 = _0_line__out__1[17]; plus_00_13 = _0_line__out__1[18]; plus_00_12 = _0_line__out__1[19];
  //   plus_00_11 = _0_line__out__1[20]; plus_00_10 = _0_line__out__1[21]; plus_00_09 = _0_line__out__1[22];
  //   plus_00_08 = _0_line__out__1[23]; plus_00_07 = _0_line__out__1[24]; plus_00_06 = _0_line__out__1[25];
  //   plus_00_05 = _0_line__out__1[26]; plus_00_04 = _0_line__out__1[27]; plus_00_03 = _0_line__out__1[28];
  //   plus_00_02 = _0_line__out__1[29]; plus_00_01 = _0_line__out__1[30]; plus_00_00 = _0_line__out__1[31];
  //   plus_01_00 = _1_line[0]; plus_01_01 = _1_line[1]; plus_01_02 = _1_line[2]; plus_01_03 = _1_line[3];
  //   plus_01_04 = _1_line[4]; plus_01_05 = _1_line[5]; plus_01_06 = _1_line[6]; plus_01_07 = _1_line[7];
  //   plus_01_08 = _1_line[8]; plus_01_09 = _1_line[9]; plus_01_10 = _1_line[10]; plus_01_11 = _1_line[11];
  //   plus_01_12 = _1_line[12]; plus_01_13 = _1_line[13]; plus_01_14 = _1_line[14]; plus_01_15 = _1_line[15];
  //   plus_01_16 = _1_line[16]; plus_01_17 = _1_line[17]; plus_01_18 = _1_line[18]; plus_01_19 = _1_line[19];
  //   plus_01_20 = _1_line[20]; plus_01_21 = _1_line[21]; plus_01_22 = _1_line[22]; plus_01_23 = _1_line[23];
  //   plus_01_24 = _1_line[24]; plus_01_25 = _1_line[25]; plus_01_26 = _1_line[26]; plus_01_27 = _1_line[27];
  //   plus_01_28 = _1_line[28]; plus_01_29 = _1_line[29]; plus_01_30 = _1_line[30]; plus_01_31 = _1_line[31];
  //   minus_01_00 = minus_1_line[0]; minus_01_01 = minus_1_line[1]; minus_01_02 = minus_1_line[2];
  //   minus_01_03 = minus_1_line[3]; minus_01_04 = minus_1_line[4]; minus_01_05 = minus_1_line[5];
  //   minus_01_06 = minus_1_line[6]; minus_01_07 = minus_1_line[7]; minus_01_08 = minus_1_line[8];
  //   minus_01_09 = minus_1_line[9]; minus_01_10 = minus_1_line[10]; minus_01_11 = minus_1_line[11];
  //   minus_01_12 = minus_1_line[12]; minus_01_13 = minus_1_line[13]; minus_01_14 = minus_1_line[14];
  //   minus_01_15 = minus_1_line[15]; minus_01_16 = minus_1_line[16]; minus_01_17 = minus_1_line[17];
  //   minus_01_18 = minus_1_line[18]; minus_01_19 = minus_1_line[19]; minus_01_20 = minus_1_line[20];
  //   minus_01_21 = minus_1_line[21]; minus_01_22 = minus_1_line[22]; minus_01_23 = minus_1_line[23];
  //   minus_01_24 = minus_1_line[24]; minus_01_25 = minus_1_line[25]; minus_01_26 = minus_1_line[26];
  //   minus_01_27 = minus_1_line[27]; minus_01_28 = minus_1_line[28]; minus_01_29 = minus_1_line[29];
  //   minus_01_30 = minus_1_line[30]; minus_01_31 = minus_1_line[31]; state[1:0] = input_state

  // Notes on the sheet:
  //   clock: pull=down
  //   pause: pull=down
endmodule
module line (
  input  [15:0] J,
  input  [15:0] minus_2_line,
  input  [15:0] minus_1_line,
  input  [15:0] _1_line,
  input  [15:0] _2_line,
  input  I,
  input  Torus,
  input  [1:0] input_state,
  input  clock,
  input  pause,
  input  clear,
  input  enable,
  input  random,
  input  [24:0] lookAt,
  input  [29:0] birth1,
  input  [29:0] save1,
  input  [29:0] birth2,
  input  [29:0] save2,
  input  [15:0] preset,
  input  loadPreset,
  output [15:0] _0_line__out__2,
  output [15:0] _0_line__out__1,
  output [15:0] display,
  output [15:0] _0_line__out__1_2,
  output [15:0] _0_line__out__2_2
);

  wire minus_01_01_t, minus_01_02_t, minus_01_16, minus_01_17, minus_02_01_t, minus_02_02_t, minus_02_16,
       minus_02_17, or_1_out, plus_00_00new, plus_00_01_t, plus_00_01new, plus_00_02_t, plus_00_02new,
       plus_00_03new, plus_00_04new, plus_00_05new, plus_00_06new, plus_00_07new, plus_00_08new,
       plus_00_09new, plus_00_10new, plus_00_11new, plus_00_12new, plus_00_13new, plus_00_14new,
       plus_00_15new, plus_00_16, plus_00_17, plus_01_01_t, plus_01_02_t, plus_01_16, plus_01_17,
       plus_02_01_t, plus_02_02_t, plus_02_16, plus_02_17;
  wire [1:0] state_helper_1_output_state, state_helper_2_output_state, state_helper_3_output_state,
       state_helper_4_output_state, state_helper_5_output_state, state_helper_6_output_state,
       state_helper_7_output_state, state_helper_8_output_state, state_helper_9_output_state,
       state_helper_10_output_state, state_helper_11_output_state, state_helper_12_output_state,
       state_helper_13_output_state, state_helper_14_output_state, state_helper_15_output_state,
       state_helper_16_output_state;
  wire [15:0] multiplexer_1_out, multiplexer_2_out, random_1_out;
  wire [24:0] neighbours_1_neighbours, neighbours_2_neighbours, neighbours_3_neighbours,
       neighbours_4_neighbours, neighbours_5_neighbours, neighbours_6_neighbours, neighbours_7_neighbours,
       neighbours_8_neighbours, neighbours_9_neighbours, neighbours_10_neighbours, neighbours_11_neighbours,
       neighbours_12_neighbours, neighbours_13_neighbours, neighbours_14_neighbours,
       neighbours_15_neighbours, neighbours_16_neighbours;

  Pull_Resistor pull_resistor_1 (.node(preset[11]));
  Pull_Resistor pull_resistor_2 (.node(preset[12]));
  Pull_Resistor pull_resistor_3 (.node(preset[13]));
  Pull_Resistor pull_resistor_4 (.node(preset[15]));
  Pull_Resistor pull_resistor_5 (.node(preset[14]));
  Pull_Resistor pull_resistor_6 (.node(preset[10]));
  Pull_Resistor pull_resistor_7 (.node(preset[7]));
  Pull_Resistor pull_resistor_8 (.node(preset[6]));
  Pull_Resistor pull_resistor_9 (.node(preset[8]));
  Pull_Resistor pull_resistor_10 (.node(preset[3]));
  Pull_Resistor pull_resistor_11 (.node(preset[9]));
  Pull_Resistor pull_resistor_12 (.node(preset[2]));
  Pull_Resistor pull_resistor_13 (.node(preset[4]));
  Pull_Resistor pull_resistor_14 (.node(preset[5]));
  Pull_Resistor pull_resistor_15 (.node(preset[1]));
  Pull_Resistor pull_resistor_16 (.node(preset[0]));
  neighbours neighbours_1 (
    .minus_02_02(minus_02_02_t), .minus_02_01(minus_02_01_t), .minus_02_00(minus_2_line[0]),
    .minus_02_01_2(minus_2_line[1]), .minus_02_02_2(minus_2_line[2]), .minus_01_02(minus_01_02_t),
    .minus_01_01(minus_01_01_t), .minus_01_00(minus_1_line[0]), .minus_01_01_2(minus_1_line[1]),
    .minus_01_02_2(minus_1_line[2]), .plus_00_02(plus_00_02_t), .plus_00_01(plus_00_01_t),
    .plus_00_00(_0_line__out__1[0]), .neighbours(neighbours_1_neighbours), .plus_00_01_2(_0_line__out__1[1]),
    .plus_00_02_2(_0_line__out__1[2]), .plus_01_02(plus_01_02_t), .plus_01_01(plus_01_01_t),
    .plus_01_00(_1_line[0]), .plus_01_01_2(_1_line[1]), .plus_01_02_2(_1_line[2]), .plus_02_02(plus_02_02_t),
    .plus_02_01(plus_02_01_t), .plus_02_00(_2_line[0]), .plus_02_01_2(_2_line[1]), .plus_02_02_2(_2_line[2]));
  Random #(.width(16)) random_1 (.clk(clock), .next(random), .out(random_1_out));  // open: clr
  and and_1 (minus_02_16, minus_2_line[0], Torus);
  and and_2 (minus_02_17, minus_2_line[1], Torus);
  and and_3 (minus_02_01_t, minus_2_line[15], Torus);
  and and_4 (minus_02_02_t, minus_2_line[14], Torus);
  alive alive_1 (
    .neighbours(neighbours_1_neighbours), .look_at(lookAt), .B1___birth(birth1), .S1___save(save1),
    .alive(plus_00_00new), .pause(pause), .input_state(state_helper_1_output_state));  // open: B2___birth, S2___save
  STATE_helper state_helper_1 (.input_state(input_state), .output_state(state_helper_1_output_state), .i(I), .j(J[0]));
  Multiplexer #(.width(16), .enable("false")) multiplexer_1 (
    .in0({plus_00_15new, plus_00_14new, plus_00_13new, plus_00_12new, plus_00_11new, plus_00_10new, plus_00_09new, plus_00_08new, plus_00_07new, plus_00_06new, plus_00_05new, plus_00_04new, plus_00_03new, plus_00_02new, plus_00_01new, plus_00_00new}),
    .in1(random_1_out), .out(multiplexer_1_out), .sel(random));
  Multiplexer #(.width(16), .enable("false")) multiplexer_2 (
    .in0(multiplexer_1_out), .in1(preset), .out(multiplexer_2_out), .sel(loadPreset));
  or or_1 (or_1_out, pause, enable);
  and and_5 (minus_01_16, minus_1_line[0], Torus);
  and and_6 (minus_01_17, minus_1_line[1], Torus);
  and and_7 (minus_01_01_t, minus_1_line[15], Torus);
  and and_8 (minus_01_02_t, minus_1_line[14], Torus);
  neighbours neighbours_2 (
    .minus_02_02(minus_02_01_t), .minus_02_01(minus_2_line[0]), .minus_02_00(minus_2_line[1]),
    .minus_02_01_2(minus_2_line[2]), .minus_02_02_2(minus_2_line[3]), .minus_01_02(minus_01_01_t),
    .minus_01_01(minus_1_line[0]), .minus_01_00(minus_1_line[1]), .minus_01_01_2(minus_1_line[2]),
    .minus_01_02_2(minus_1_line[3]), .plus_00_02(plus_00_01_t), .plus_00_01(_0_line__out__1[0]),
    .plus_00_00(_0_line__out__1[1]), .neighbours(neighbours_2_neighbours), .plus_00_01_2(_0_line__out__1[2]),
    .plus_00_02_2(_0_line__out__1[3]), .plus_01_02(plus_01_01_t), .plus_01_01(_1_line[0]),
    .plus_01_00(_1_line[1]), .plus_01_01_2(_1_line[2]), .plus_01_02_2(_1_line[3]), .plus_02_02(plus_02_01_t),
    .plus_02_01(_2_line[0]), .plus_02_00(_2_line[1]), .plus_02_01_2(_2_line[2]), .plus_02_02_2(_2_line[3]));
  Register #(.width(16), .trigger("falling")) register_1 (
    .D(multiplexer_2_out), .en(or_1_out), .Q(_0_line__out__1), .clk(clock), .clr(clear));
  alive alive_2 (
    .neighbours(neighbours_2_neighbours), .look_at(lookAt), .B1___birth(birth1), .S1___save(save1),
    .alive(plus_00_01new), .pause(pause), .input_state(state_helper_2_output_state));  // open: B2___birth, S2___save
  STATE_helper state_helper_2 (.input_state(input_state), .output_state(state_helper_2_output_state), .i(I), .j(J[1]));
  and and_9 (plus_01_16, _1_line[0], Torus);
  and and_10 (plus_01_17, _1_line[1], Torus);
  and and_11 (plus_01_01_t, _1_line[15], Torus);
  and and_12 (plus_01_02_t, _1_line[14], Torus);
  and and_13 (plus_02_16, _2_line[0], Torus);
  and and_14 (plus_02_17, _2_line[1], Torus);
  and and_15 (plus_02_01_t, _2_line[15], Torus);
  and and_16 (plus_02_02_t, _2_line[14], Torus);
  neighbours neighbours_3 (
    .minus_02_02(minus_2_line[0]), .minus_02_01(minus_2_line[1]), .minus_02_00(minus_2_line[2]),
    .minus_02_01_2(minus_2_line[3]), .minus_02_02_2(minus_2_line[4]), .minus_01_02(minus_1_line[0]),
    .minus_01_01(minus_1_line[1]), .minus_01_00(minus_1_line[2]), .minus_01_01_2(minus_1_line[3]),
    .minus_01_02_2(minus_1_line[4]), .plus_00_02(_0_line__out__1[0]), .plus_00_01(_0_line__out__1[1]),
    .plus_00_00(_0_line__out__1[2]), .neighbours(neighbours_3_neighbours), .plus_00_01_2(_0_line__out__1[3]),
    .plus_00_02_2(_0_line__out__1[4]), .plus_01_02(_1_line[0]), .plus_01_01(_1_line[1]),
    .plus_01_00(_1_line[2]), .plus_01_01_2(_1_line[3]), .plus_01_02_2(_1_line[4]), .plus_02_02(_2_line[0]),
    .plus_02_01(_2_line[1]), .plus_02_00(_2_line[2]), .plus_02_01_2(_2_line[3]), .plus_02_02_2(_2_line[4]));
  alive alive_3 (
    .neighbours(neighbours_3_neighbours), .look_at(lookAt), .B1___birth(birth1), .S1___save(save1),
    .alive(plus_00_02new), .pause(pause), .input_state(state_helper_3_output_state));  // open: B2___birth, S2___save
  STATE_helper state_helper_3 (.input_state(input_state), .output_state(state_helper_3_output_state), .i(I), .j(J[2]));
  and and_17 (plus_00_16, _0_line__out__1[0], Torus);
  and and_18 (plus_00_17, _0_line__out__1[1], Torus);
  and and_19 (plus_00_01_t, _0_line__out__1[15], Torus);
  and and_20 (plus_00_02_t, _0_line__out__1[14], Torus);
  neighbours neighbours_4 (
    .minus_02_02(minus_2_line[1]), .minus_02_01(minus_2_line[2]), .minus_02_00(minus_2_line[3]),
    .minus_02_01_2(minus_2_line[4]), .minus_02_02_2(minus_2_line[5]), .minus_01_02(minus_1_line[1]),
    .minus_01_01(minus_1_line[2]), .minus_01_00(minus_1_line[3]), .minus_01_01_2(minus_1_line[4]),
    .minus_01_02_2(minus_1_line[5]), .plus_00_02(_0_line__out__1[1]), .plus_00_01(_0_line__out__1[2]),
    .plus_00_00(_0_line__out__1[3]), .neighbours(neighbours_4_neighbours), .plus_00_01_2(_0_line__out__1[4]),
    .plus_00_02_2(_0_line__out__1[5]), .plus_01_02(_1_line[1]), .plus_01_01(_1_line[2]),
    .plus_01_00(_1_line[3]), .plus_01_01_2(_1_line[4]), .plus_01_02_2(_1_line[5]), .plus_02_02(_2_line[1]),
    .plus_02_01(_2_line[2]), .plus_02_00(_2_line[3]), .plus_02_01_2(_2_line[4]), .plus_02_02_2(_2_line[5]));
  alive alive_4 (
    .neighbours(neighbours_4_neighbours), .look_at(lookAt), .B1___birth(birth1), .S1___save(save1),
    .alive(plus_00_03new), .pause(pause), .input_state(state_helper_4_output_state));  // open: B2___birth, S2___save
  STATE_helper state_helper_4 (.input_state(input_state), .output_state(state_helper_4_output_state), .i(I), .j(J[3]));
  neighbours neighbours_5 (
    .minus_02_02(minus_2_line[2]), .minus_02_01(minus_2_line[3]), .minus_02_00(minus_2_line[4]),
    .minus_02_01_2(minus_2_line[5]), .minus_02_02_2(minus_2_line[6]), .minus_01_02(minus_1_line[2]),
    .minus_01_01(minus_1_line[3]), .minus_01_00(minus_1_line[4]), .minus_01_01_2(minus_1_line[5]),
    .minus_01_02_2(minus_1_line[6]), .plus_00_02(_0_line__out__1[2]), .plus_00_01(_0_line__out__1[3]),
    .plus_00_00(_0_line__out__1[4]), .neighbours(neighbours_5_neighbours), .plus_00_01_2(_0_line__out__1[5]),
    .plus_00_02_2(_0_line__out__1[6]), .plus_01_02(_1_line[2]), .plus_01_01(_1_line[3]),
    .plus_01_00(_1_line[4]), .plus_01_01_2(_1_line[5]), .plus_01_02_2(_1_line[6]), .plus_02_02(_2_line[2]),
    .plus_02_01(_2_line[3]), .plus_02_00(_2_line[4]), .plus_02_01_2(_2_line[5]), .plus_02_02_2(_2_line[6]));
  alive alive_5 (
    .neighbours(neighbours_5_neighbours), .look_at(lookAt), .B1___birth(birth1), .S1___save(save1),
    .alive(plus_00_04new), .pause(pause), .input_state(state_helper_5_output_state));  // open: B2___birth, S2___save
  STATE_helper state_helper_5 (.input_state(input_state), .output_state(state_helper_5_output_state), .i(I), .j(J[4]));
  neighbours neighbours_6 (
    .minus_02_02(minus_2_line[3]), .minus_02_01(minus_2_line[4]), .minus_02_00(minus_2_line[5]),
    .minus_02_01_2(minus_2_line[6]), .minus_02_02_2(minus_2_line[7]), .minus_01_02(minus_1_line[3]),
    .minus_01_01(minus_1_line[4]), .minus_01_00(minus_1_line[5]), .minus_01_01_2(minus_1_line[6]),
    .minus_01_02_2(minus_1_line[7]), .plus_00_02(_0_line__out__1[3]), .plus_00_01(_0_line__out__1[4]),
    .plus_00_00(_0_line__out__1[5]), .neighbours(neighbours_6_neighbours), .plus_00_01_2(_0_line__out__1[6]),
    .plus_00_02_2(_0_line__out__1[7]), .plus_01_02(_1_line[3]), .plus_01_01(_1_line[4]),
    .plus_01_00(_1_line[5]), .plus_01_01_2(_1_line[6]), .plus_01_02_2(_1_line[7]), .plus_02_02(_2_line[3]),
    .plus_02_01(_2_line[4]), .plus_02_00(_2_line[5]), .plus_02_01_2(_2_line[6]), .plus_02_02_2(_2_line[7]));
  alive alive_6 (
    .neighbours(neighbours_6_neighbours), .look_at(lookAt), .B1___birth(birth1), .S1___save(save1),
    .alive(plus_00_05new), .pause(pause), .input_state(state_helper_6_output_state));  // open: B2___birth, S2___save
  STATE_helper state_helper_6 (.input_state(input_state), .output_state(state_helper_6_output_state), .i(I), .j(J[5]));
  neighbours neighbours_7 (
    .minus_02_02(minus_2_line[4]), .minus_02_01(minus_2_line[5]), .minus_02_00(minus_2_line[6]),
    .minus_02_01_2(minus_2_line[7]), .minus_02_02_2(minus_2_line[8]), .minus_01_02(minus_1_line[4]),
    .minus_01_01(minus_1_line[5]), .minus_01_00(minus_1_line[6]), .minus_01_01_2(minus_1_line[7]),
    .minus_01_02_2(minus_1_line[8]), .plus_00_02(_0_line__out__1[4]), .plus_00_01(_0_line__out__1[5]),
    .plus_00_00(_0_line__out__1[6]), .neighbours(neighbours_7_neighbours), .plus_00_01_2(_0_line__out__1[7]),
    .plus_00_02_2(_0_line__out__1[8]), .plus_01_02(_1_line[4]), .plus_01_01(_1_line[5]),
    .plus_01_00(_1_line[6]), .plus_01_01_2(_1_line[7]), .plus_01_02_2(_1_line[8]), .plus_02_02(_2_line[4]),
    .plus_02_01(_2_line[5]), .plus_02_00(_2_line[6]), .plus_02_01_2(_2_line[7]), .plus_02_02_2(_2_line[8]));
  alive alive_7 (
    .neighbours(neighbours_7_neighbours), .look_at(lookAt), .B1___birth(birth1), .S1___save(save1),
    .alive(plus_00_06new), .pause(pause), .input_state(state_helper_7_output_state));  // open: B2___birth, S2___save
  STATE_helper state_helper_7 (.input_state(input_state), .output_state(state_helper_7_output_state), .i(I), .j(J[6]));
  neighbours neighbours_8 (
    .minus_02_02(minus_2_line[5]), .minus_02_01(minus_2_line[6]), .minus_02_00(minus_2_line[7]),
    .minus_02_01_2(minus_2_line[8]), .minus_02_02_2(minus_2_line[9]), .minus_01_02(minus_1_line[5]),
    .minus_01_01(minus_1_line[6]), .minus_01_00(minus_1_line[7]), .minus_01_01_2(minus_1_line[8]),
    .minus_01_02_2(minus_1_line[9]), .plus_00_02(_0_line__out__1[5]), .plus_00_01(_0_line__out__1[6]),
    .plus_00_00(_0_line__out__1[7]), .neighbours(neighbours_8_neighbours), .plus_00_01_2(_0_line__out__1[8]),
    .plus_00_02_2(_0_line__out__1[9]), .plus_01_02(_1_line[5]), .plus_01_01(_1_line[6]),
    .plus_01_00(_1_line[7]), .plus_01_01_2(_1_line[8]), .plus_01_02_2(_1_line[9]), .plus_02_02(_2_line[5]),
    .plus_02_01(_2_line[6]), .plus_02_00(_2_line[7]), .plus_02_01_2(_2_line[8]), .plus_02_02_2(_2_line[9]));
  alive alive_8 (
    .neighbours(neighbours_8_neighbours), .look_at(lookAt), .B1___birth(birth1), .S1___save(save1),
    .alive(plus_00_07new), .pause(pause), .input_state(state_helper_8_output_state));  // open: B2___birth, S2___save
  STATE_helper state_helper_8 (.input_state(input_state), .output_state(state_helper_8_output_state), .i(I), .j(J[7]));
  neighbours neighbours_9 (
    .minus_02_02(minus_2_line[6]), .minus_02_01(minus_2_line[7]), .minus_02_00(minus_2_line[8]),
    .minus_02_01_2(minus_2_line[9]), .minus_02_02_2(minus_2_line[10]), .minus_01_02(minus_1_line[6]),
    .minus_01_01(minus_1_line[7]), .minus_01_00(minus_1_line[8]), .minus_01_01_2(minus_1_line[9]),
    .minus_01_02_2(minus_1_line[10]), .plus_00_02(_0_line__out__1[6]), .plus_00_01(_0_line__out__1[7]),
    .plus_00_00(_0_line__out__1[8]), .neighbours(neighbours_9_neighbours), .plus_00_01_2(_0_line__out__1[9]),
    .plus_00_02_2(_0_line__out__1[10]), .plus_01_02(_1_line[6]), .plus_01_01(_1_line[7]),
    .plus_01_00(_1_line[8]), .plus_01_01_2(_1_line[9]), .plus_01_02_2(_1_line[10]), .plus_02_02(_2_line[6]),
    .plus_02_01(_2_line[7]), .plus_02_00(_2_line[8]), .plus_02_01_2(_2_line[9]), .plus_02_02_2(_2_line[10]));
  alive alive_9 (
    .neighbours(neighbours_9_neighbours), .look_at(lookAt), .B1___birth(birth1), .S1___save(save1),
    .alive(plus_00_08new), .pause(pause), .input_state(state_helper_9_output_state));  // open: B2___birth, S2___save
  STATE_helper state_helper_9 (.input_state(input_state), .output_state(state_helper_9_output_state), .i(I), .j(J[8]));
  neighbours neighbours_10 (
    .minus_02_02(minus_2_line[7]), .minus_02_01(minus_2_line[8]), .minus_02_00(minus_2_line[9]),
    .minus_02_01_2(minus_2_line[10]), .minus_02_02_2(minus_2_line[11]), .minus_01_02(minus_1_line[7]),
    .minus_01_01(minus_1_line[8]), .minus_01_00(minus_1_line[9]), .minus_01_01_2(minus_1_line[10]),
    .minus_01_02_2(minus_1_line[11]), .plus_00_02(_0_line__out__1[7]), .plus_00_01(_0_line__out__1[8]),
    .plus_00_00(_0_line__out__1[9]), .neighbours(neighbours_10_neighbours),
    .plus_00_01_2(_0_line__out__1[10]), .plus_00_02_2(_0_line__out__1[11]), .plus_01_02(_1_line[7]),
    .plus_01_01(_1_line[8]), .plus_01_00(_1_line[9]), .plus_01_01_2(_1_line[10]), .plus_01_02_2(_1_line[11]),
    .plus_02_02(_2_line[7]), .plus_02_01(_2_line[8]), .plus_02_00(_2_line[9]), .plus_02_01_2(_2_line[10]),
    .plus_02_02_2(_2_line[11]));
  alive alive_10 (
    .neighbours(neighbours_10_neighbours), .look_at(lookAt), .B1___birth(birth1), .S1___save(save1),
    .alive(plus_00_09new), .pause(pause), .input_state(state_helper_10_output_state));  // open: B2___birth, S2___save
  STATE_helper state_helper_10 (
    .input_state(input_state), .output_state(state_helper_10_output_state), .i(I), .j(J[9]));
  neighbours neighbours_11 (
    .minus_02_02(minus_2_line[8]), .minus_02_01(minus_2_line[9]), .minus_02_00(minus_2_line[10]),
    .minus_02_01_2(minus_2_line[11]), .minus_02_02_2(minus_2_line[12]), .minus_01_02(minus_1_line[8]),
    .minus_01_01(minus_1_line[9]), .minus_01_00(minus_1_line[10]), .minus_01_01_2(minus_1_line[11]),
    .minus_01_02_2(minus_1_line[12]), .plus_00_02(_0_line__out__1[8]), .plus_00_01(_0_line__out__1[9]),
    .plus_00_00(_0_line__out__1[10]), .neighbours(neighbours_11_neighbours),
    .plus_00_01_2(_0_line__out__1[11]), .plus_00_02_2(_0_line__out__1[12]), .plus_01_02(_1_line[8]),
    .plus_01_01(_1_line[9]), .plus_01_00(_1_line[10]), .plus_01_01_2(_1_line[11]),
    .plus_01_02_2(_1_line[12]), .plus_02_02(_2_line[8]), .plus_02_01(_2_line[9]), .plus_02_00(_2_line[10]),
    .plus_02_01_2(_2_line[11]), .plus_02_02_2(_2_line[12]));
  alive alive_11 (
    .neighbours(neighbours_11_neighbours), .look_at(lookAt), .B1___birth(birth1), .S1___save(save1),
    .alive(plus_00_10new), .pause(pause), .input_state(state_helper_11_output_state));  // open: B2___birth, S2___save
  STATE_helper state_helper_11 (
    .input_state(input_state), .output_state(state_helper_11_output_state), .i(I), .j(J[10]));
  neighbours neighbours_12 (
    .minus_02_02(minus_2_line[9]), .minus_02_01(minus_2_line[10]), .minus_02_00(minus_2_line[11]),
    .minus_02_01_2(minus_2_line[12]), .minus_02_02_2(minus_2_line[13]), .minus_01_02(minus_1_line[9]),
    .minus_01_01(minus_1_line[10]), .minus_01_00(minus_1_line[11]), .minus_01_01_2(minus_1_line[12]),
    .minus_01_02_2(minus_1_line[13]), .plus_00_02(_0_line__out__1[9]), .plus_00_01(_0_line__out__1[10]),
    .plus_00_00(_0_line__out__1[11]), .neighbours(neighbours_12_neighbours),
    .plus_00_01_2(_0_line__out__1[12]), .plus_00_02_2(_0_line__out__1[13]), .plus_01_02(_1_line[9]),
    .plus_01_01(_1_line[10]), .plus_01_00(_1_line[11]), .plus_01_01_2(_1_line[12]),
    .plus_01_02_2(_1_line[13]), .plus_02_02(_2_line[9]), .plus_02_01(_2_line[10]), .plus_02_00(_2_line[11]),
    .plus_02_01_2(_2_line[12]), .plus_02_02_2(_2_line[13]));
  alive alive_12 (
    .neighbours(neighbours_12_neighbours), .look_at(lookAt), .B1___birth(birth1), .S1___save(save1),
    .alive(plus_00_11new), .pause(pause), .input_state(state_helper_12_output_state));  // open: B2___birth, S2___save
  STATE_helper state_helper_12 (
    .input_state(input_state), .output_state(state_helper_12_output_state), .i(I), .j(J[11]));
  neighbours neighbours_13 (
    .minus_02_02(minus_2_line[10]), .minus_02_01(minus_2_line[11]), .minus_02_00(minus_2_line[12]),
    .minus_02_01_2(minus_2_line[13]), .minus_02_02_2(minus_2_line[14]), .minus_01_02(minus_1_line[10]),
    .minus_01_01(minus_1_line[11]), .minus_01_00(minus_1_line[12]), .minus_01_01_2(minus_1_line[13]),
    .minus_01_02_2(minus_1_line[14]), .plus_00_02(_0_line__out__1[10]), .plus_00_01(_0_line__out__1[11]),
    .plus_00_00(_0_line__out__1[12]), .neighbours(neighbours_13_neighbours),
    .plus_00_01_2(_0_line__out__1[13]), .plus_00_02_2(_0_line__out__1[14]), .plus_01_02(_1_line[10]),
    .plus_01_01(_1_line[11]), .plus_01_00(_1_line[12]), .plus_01_01_2(_1_line[13]),
    .plus_01_02_2(_1_line[14]), .plus_02_02(_2_line[10]), .plus_02_01(_2_line[11]), .plus_02_00(_2_line[12]),
    .plus_02_01_2(_2_line[13]), .plus_02_02_2(_2_line[14]));
  alive alive_13 (
    .neighbours(neighbours_13_neighbours), .look_at(lookAt), .B1___birth(birth1), .S1___save(save1),
    .alive(plus_00_12new), .pause(pause), .input_state(state_helper_13_output_state));  // open: B2___birth, S2___save
  STATE_helper state_helper_13 (
    .input_state(input_state), .output_state(state_helper_13_output_state), .i(I), .j(J[12]));
  neighbours neighbours_14 (
    .minus_02_02(minus_2_line[11]), .minus_02_01(minus_2_line[12]), .minus_02_00(minus_2_line[13]),
    .minus_02_01_2(minus_2_line[14]), .minus_02_02_2(minus_2_line[15]), .minus_01_02(minus_1_line[11]),
    .minus_01_01(minus_1_line[12]), .minus_01_00(minus_1_line[13]), .minus_01_01_2(minus_1_line[14]),
    .minus_01_02_2(minus_1_line[15]), .plus_00_02(_0_line__out__1[11]), .plus_00_01(_0_line__out__1[12]),
    .plus_00_00(_0_line__out__1[13]), .neighbours(neighbours_14_neighbours),
    .plus_00_01_2(_0_line__out__1[14]), .plus_00_02_2(_0_line__out__1[15]), .plus_01_02(_1_line[11]),
    .plus_01_01(_1_line[12]), .plus_01_00(_1_line[13]), .plus_01_01_2(_1_line[14]),
    .plus_01_02_2(_1_line[15]), .plus_02_02(_2_line[11]), .plus_02_01(_2_line[12]), .plus_02_00(_2_line[13]),
    .plus_02_01_2(_2_line[14]), .plus_02_02_2(_2_line[15]));
  alive alive_14 (
    .neighbours(neighbours_14_neighbours), .look_at(lookAt), .B1___birth(birth1), .S1___save(save1),
    .alive(plus_00_13new), .pause(pause), .input_state(state_helper_14_output_state));  // open: B2___birth, S2___save
  STATE_helper state_helper_14 (
    .input_state(input_state), .output_state(state_helper_14_output_state), .i(I), .j(J[13]));
  neighbours neighbours_15 (
    .minus_02_02(minus_2_line[12]), .minus_02_01(minus_2_line[13]), .minus_02_00(minus_2_line[14]),
    .minus_02_01_2(minus_2_line[15]), .minus_02_02_2(minus_02_16), .minus_01_02(minus_1_line[12]),
    .minus_01_01(minus_1_line[13]), .minus_01_00(minus_1_line[14]), .minus_01_01_2(minus_1_line[15]),
    .minus_01_02_2(minus_01_16), .plus_00_02(_0_line__out__1[12]), .plus_00_01(_0_line__out__1[13]),
    .plus_00_00(_0_line__out__1[14]), .neighbours(neighbours_15_neighbours),
    .plus_00_01_2(_0_line__out__1[15]), .plus_00_02_2(plus_00_16), .plus_01_02(_1_line[12]),
    .plus_01_01(_1_line[13]), .plus_01_00(_1_line[14]), .plus_01_01_2(_1_line[15]),
    .plus_01_02_2(plus_01_16), .plus_02_02(_2_line[12]), .plus_02_01(_2_line[13]), .plus_02_00(_2_line[14]),
    .plus_02_01_2(_2_line[15]), .plus_02_02_2(plus_02_16));
  alive alive_15 (
    .neighbours(neighbours_15_neighbours), .look_at(lookAt), .B1___birth(birth1), .S1___save(save1),
    .alive(plus_00_14new), .pause(pause), .input_state(state_helper_15_output_state));  // open: B2___birth, S2___save
  STATE_helper state_helper_15 (
    .input_state(input_state), .output_state(state_helper_15_output_state), .i(I), .j(J[14]));
  neighbours neighbours_16 (
    .minus_02_02(minus_2_line[13]), .minus_02_01(minus_2_line[14]), .minus_02_00(minus_2_line[15]),
    .minus_02_01_2(minus_02_16), .minus_02_02_2(minus_02_17), .minus_01_02(minus_1_line[13]),
    .minus_01_01(minus_1_line[14]), .minus_01_00(minus_1_line[15]), .minus_01_01_2(minus_01_16),
    .minus_01_02_2(minus_01_17), .plus_00_02(_0_line__out__1[13]), .plus_00_01(_0_line__out__1[14]),
    .plus_00_00(_0_line__out__1[15]), .neighbours(neighbours_16_neighbours), .plus_00_01_2(plus_00_16),
    .plus_00_02_2(plus_00_17), .plus_01_02(_1_line[13]), .plus_01_01(_1_line[14]), .plus_01_00(_1_line[15]),
    .plus_01_01_2(plus_01_16), .plus_01_02_2(plus_01_17), .plus_02_02(_2_line[13]), .plus_02_01(_2_line[14]),
    .plus_02_00(_2_line[15]), .plus_02_01_2(plus_02_16), .plus_02_02_2(plus_02_17));
  alive alive_16 (
    .neighbours(neighbours_16_neighbours), .look_at(lookAt), .B1___birth(birth1), .S1___save(save1),
    .alive(plus_00_15new), .pause(pause), .input_state(state_helper_16_output_state));  // open: B2___birth, S2___save
  STATE_helper state_helper_16 (
    .input_state(input_state), .output_state(state_helper_16_output_state), .i(I), .j(J[15]));

  assign _0_line__out__1_2 = _0_line__out__1;
  assign _0_line__out__2 = _0_line__out__1;
  assign _0_line__out__2_2 = _0_line__out__1;
  assign display = _0_line__out__1;

  // Other names for the same wires on the sheet: plus_00_00 = _0_line__out__1[0]; plus_00_01 = _0_line__out__1[1];
  //   plus_00_02 = _0_line__out__1[2]; plus_00_03 = _0_line__out__1[3]; plus_00_04 = _0_line__out__1[4];
  //   plus_00_05 = _0_line__out__1[5]; plus_00_06 = _0_line__out__1[6]; plus_00_07 = _0_line__out__1[7];
  //   plus_00_08 = _0_line__out__1[8]; plus_00_09 = _0_line__out__1[9]; plus_00_10 = _0_line__out__1[10];
  //   plus_00_11 = _0_line__out__1[11]; plus_00_12 = _0_line__out__1[12]; plus_00_13 = _0_line__out__1[13];
  //   plus_00_14 = _0_line__out__1[14]; plus_00_15 = _0_line__out__1[15]; plus_01_00 = _1_line[0];
  //   plus_01_01 = _1_line[1]; plus_01_02 = _1_line[2]; plus_01_03 = _1_line[3]; plus_01_04 = _1_line[4];
  //   plus_01_05 = _1_line[5]; plus_01_06 = _1_line[6]; plus_01_07 = _1_line[7]; plus_01_08 = _1_line[8];
  //   plus_01_09 = _1_line[9]; plus_01_10 = _1_line[10]; plus_01_11 = _1_line[11]; plus_01_12 = _1_line[12];
  //   plus_01_13 = _1_line[13]; plus_01_14 = _1_line[14]; plus_01_15 = _1_line[15]; plus_02_00 = _2_line[0];
  //   plus_02_01 = _2_line[1]; plus_02_02 = _2_line[2]; plus_02_03 = _2_line[3]; plus_02_04 = _2_line[4];
  //   plus_02_05 = _2_line[5]; plus_02_06 = _2_line[6]; plus_02_07 = _2_line[7]; plus_02_08 = _2_line[8];
  //   plus_02_09 = _2_line[9]; plus_02_10 = _2_line[10]; plus_02_11 = _2_line[11]; plus_02_12 = _2_line[12];
  //   plus_02_13 = _2_line[13]; plus_02_14 = _2_line[14]; plus_02_15 = _2_line[15]; birth[29:0] = birth1;
  //   minus_01_00 = minus_1_line[0]; minus_01_01 = minus_1_line[1]; minus_01_02 = minus_1_line[2];
  //   minus_01_03 = minus_1_line[3]; minus_01_04 = minus_1_line[4]; minus_01_05 = minus_1_line[5];
  //   minus_01_06 = minus_1_line[6]; minus_01_07 = minus_1_line[7]; minus_01_08 = minus_1_line[8];
  //   minus_01_09 = minus_1_line[9]; minus_01_10 = minus_1_line[10]; minus_01_11 = minus_1_line[11];
  //   minus_01_12 = minus_1_line[12]; minus_01_13 = minus_1_line[13]; minus_01_14 = minus_1_line[14];
  //   minus_01_15 = minus_1_line[15]; minus_02_00 = minus_2_line[0]; minus_02_01 = minus_2_line[1];
  //   minus_02_02 = minus_2_line[2]; minus_02_03 = minus_2_line[3]; minus_02_04 = minus_2_line[4];
  //   minus_02_05 = minus_2_line[5]; minus_02_06 = minus_2_line[6]; minus_02_07 = minus_2_line[7];
  //   minus_02_08 = minus_2_line[8]; minus_02_09 = minus_2_line[9]; minus_02_10 = minus_2_line[10];
  //   minus_02_11 = minus_2_line[11]; minus_02_12 = minus_2_line[12]; minus_02_13 = minus_2_line[13];
  //   minus_02_14 = minus_2_line[14]; minus_02_15 = minus_2_line[15]; save[29:0] = save1; state[1:0] = input_state

  // Notes on the sheet:
  //   clear: pull=down
  //   birth2: pull=down
  //   save2: pull=down
  //   birth1: pull=down
  //   save1: pull=down
  //   clock: pull=down
  //   lookAt: pull=down
  //   enable: pull=down
  //   pause: pull=down
  //   if the game is paused, there will be no
  //   further iterations, but cursor can work
endmodule

module matrixSTD__not_used (
  input  [31:0] i,
  input  [31:0] J,
  input  Torus,
  input  [1:0] input_state,
  input  clock,
  input  pause,
  output [31:0] LINE_31,
  output [31:0] LINE_30,
  output [31:0] LINE_29,
  output [31:0] LINE_28,
  output [31:0] LINE_27,
  output [31:0] LINE_26,
  output [31:0] LINE_25,
  output [31:0] LINE_24,
  output [31:0] LINE_23,
  output [31:0] LINE_22,
  output [31:0] LINE_21,
  output [31:0] LINE_20,
  output [31:0] LINE_19,
  output [31:0] LINE_18,
  output [31:0] LINE_17,
  output [31:0] LINE_16,
  output [31:0] LINE_15,
  output [31:0] LINE_14,
  output [31:0] LINE_13,
  output [31:0] LINE_12,
  output [31:0] LINE_11,
  output [31:0] LINE_10,
  output [31:0] LINE_9,
  output [31:0] LINE_8,
  output [31:0] LINE_7,
  output [31:0] LINE_6,
  output [31:0] LINE_5,
  output [31:0] LINE_4,
  output [31:0] LINE_3,
  output [31:0] LINE_2,
  output [31:0] LINE_1,
  output [31:0] LINE_0
);

  wire [31:0] _0__0_line__out__1_2, _1__0_line__out__1, _1__0_line__out__1_2, _2__0_line__out__1,
       _2__0_line__out__1_2, _3__0_line__out__1, _3__0_line__out__1_2, _4__0_line__out__1,
       _4__0_line__out__1_2, _5__0_line__out__1, _5__0_line__out__1_2, _6__0_line__out__1,
       _6__0_line__out__1_2, _7__0_line__out__1, _7__0_line__out__1_2, _8__0_line__out__1,
       _8__0_line__out__1_2, _9__0_line__out__1, _9__0_line__out__1_2, _10__0_line__out__1,
       _10__0_line__out__1_2, _11__0_line__out__1, _11__0_line__out__1_2, _12__0_line__out__1,
       _12__0_line__out__1_2, _13__0_line__out__1, _13__0_line__out__1_2, _14__0_line__out__1,
       _14__0_line__out__1_2, _15__0_line__out__1, _15__0_line__out__1_2, _16__0_line__out__1,
       _16__0_line__out__1_2, _17__0_line__out__1, _17__0_line__out__1_2, _18__0_line__out__1,
       _18__0_line__out__1_2, _19__0_line__out__1, _19__0_line__out__1_2, _20__0_line__out__1,
       _20__0_line__out__1_2, _21__0_line__out__1, _21__0_line__out__1_2, _22__0_line__out__1,
       _22__0_line__out__1_2, _23__0_line__out__1, _23__0_line__out__1_2, _24__0_line__out__1,
       _24__0_line__out__1_2, _25__0_line__out__1, _25__0_line__out__1_2, _26__0_line__out__1,
       _26__0_line__out__1_2, _27__0_line__out__1, _27__0_line__out__1_2, _28__0_line__out__1,
       _28__0_line__out__1_2, _29__0_line__out__1, _29__0_line__out__1_2, _30__0_line__out__1,
       _30__0_line__out__1_2, _31__0_line__out__1, and_1_out, and_2_out, minus_01, plus_32;

  assign and_1_out = plus_32 & {32{Torus}};  // AND_Gate and_1, 32 bits wide
  lineSTD__not_used _0 (
    .J(J), .minus_1_line(and_1_out), ._1_line(_1__0_line__out__1), .I(i[31]), .Torus(Torus),
    .input_state(input_state), ._0_line__out__1(minus_01), .display(LINE_31),
    ._0_line__out__1_2(_0__0_line__out__1_2), .clock(clock), .pause(pause));
  lineSTD__not_used _1 (
    .J(J), .minus_1_line(_0__0_line__out__1_2), ._1_line(_2__0_line__out__1), .I(i[30]), .Torus(Torus),
    .input_state(input_state), ._0_line__out__1(_1__0_line__out__1), .display(LINE_30),
    ._0_line__out__1_2(_1__0_line__out__1_2), .clock(clock), .pause(pause));
  lineSTD__not_used _2 (
    .J(J), .minus_1_line(_1__0_line__out__1_2), ._1_line(_3__0_line__out__1), .I(i[29]), .Torus(Torus),
    .input_state(input_state), ._0_line__out__1(_2__0_line__out__1), .display(LINE_29),
    ._0_line__out__1_2(_2__0_line__out__1_2), .clock(clock), .pause(pause));
  lineSTD__not_used _3 (
    .J(J), .minus_1_line(_2__0_line__out__1_2), ._1_line(_4__0_line__out__1), .I(i[28]), .Torus(Torus),
    .input_state(input_state), ._0_line__out__1(_3__0_line__out__1), .display(LINE_28),
    ._0_line__out__1_2(_3__0_line__out__1_2), .clock(clock), .pause(pause));
  lineSTD__not_used _4 (
    .J(J), .minus_1_line(_3__0_line__out__1_2), ._1_line(_5__0_line__out__1), .I(i[27]), .Torus(Torus),
    .input_state(input_state), ._0_line__out__1(_4__0_line__out__1), .display(LINE_27),
    ._0_line__out__1_2(_4__0_line__out__1_2), .clock(clock), .pause(pause));
  lineSTD__not_used _5 (
    .J(J), .minus_1_line(_4__0_line__out__1_2), ._1_line(_6__0_line__out__1), .I(i[26]), .Torus(Torus),
    .input_state(input_state), ._0_line__out__1(_5__0_line__out__1), .display(LINE_26),
    ._0_line__out__1_2(_5__0_line__out__1_2), .clock(clock), .pause(pause));
  lineSTD__not_used _6 (
    .J(J), .minus_1_line(_5__0_line__out__1_2), ._1_line(_7__0_line__out__1), .I(i[25]), .Torus(Torus),
    .input_state(input_state), ._0_line__out__1(_6__0_line__out__1), .display(LINE_25),
    ._0_line__out__1_2(_6__0_line__out__1_2), .clock(clock), .pause(pause));
  lineSTD__not_used _7 (
    .J(J), .minus_1_line(_6__0_line__out__1_2), ._1_line(_8__0_line__out__1), .I(i[24]), .Torus(Torus),
    .input_state(input_state), ._0_line__out__1(_7__0_line__out__1), .display(LINE_24),
    ._0_line__out__1_2(_7__0_line__out__1_2), .clock(clock), .pause(pause));
  lineSTD__not_used _8 (
    .J(J), .minus_1_line(_7__0_line__out__1_2), ._1_line(_9__0_line__out__1), .I(i[23]), .Torus(Torus),
    .input_state(input_state), ._0_line__out__1(_8__0_line__out__1), .display(LINE_23),
    ._0_line__out__1_2(_8__0_line__out__1_2), .clock(clock), .pause(pause));
  lineSTD__not_used _9 (
    .J(J), .minus_1_line(_8__0_line__out__1_2), ._1_line(_10__0_line__out__1), .I(i[22]), .Torus(Torus),
    .input_state(input_state), ._0_line__out__1(_9__0_line__out__1), .display(LINE_22),
    ._0_line__out__1_2(_9__0_line__out__1_2), .clock(clock), .pause(pause));
  lineSTD__not_used _10 (
    .J(J), .minus_1_line(_9__0_line__out__1_2), ._1_line(_11__0_line__out__1), .I(i[21]), .Torus(Torus),
    .input_state(input_state), ._0_line__out__1(_10__0_line__out__1), .display(LINE_21),
    ._0_line__out__1_2(_10__0_line__out__1_2), .clock(clock), .pause(pause));
  lineSTD__not_used _11 (
    .J(J), .minus_1_line(_10__0_line__out__1_2), ._1_line(_12__0_line__out__1), .I(i[20]), .Torus(Torus),
    .input_state(input_state), ._0_line__out__1(_11__0_line__out__1), .display(LINE_20),
    ._0_line__out__1_2(_11__0_line__out__1_2), .clock(clock), .pause(pause));
  lineSTD__not_used _12 (
    .J(J), .minus_1_line(_11__0_line__out__1_2), ._1_line(_13__0_line__out__1), .I(i[19]), .Torus(Torus),
    .input_state(input_state), ._0_line__out__1(_12__0_line__out__1), .display(LINE_19),
    ._0_line__out__1_2(_12__0_line__out__1_2), .clock(clock), .pause(pause));
  lineSTD__not_used _13 (
    .J(J), .minus_1_line(_12__0_line__out__1_2), ._1_line(_14__0_line__out__1), .I(i[18]), .Torus(Torus),
    .input_state(input_state), ._0_line__out__1(_13__0_line__out__1), .display(LINE_18),
    ._0_line__out__1_2(_13__0_line__out__1_2), .clock(clock), .pause(pause));
  lineSTD__not_used _14 (
    .J(J), .minus_1_line(_13__0_line__out__1_2), ._1_line(_15__0_line__out__1), .I(i[17]), .Torus(Torus),
    .input_state(input_state), ._0_line__out__1(_14__0_line__out__1), .display(LINE_17),
    ._0_line__out__1_2(_14__0_line__out__1_2), .clock(clock), .pause(pause));
  lineSTD__not_used _15 (
    .J(J), .minus_1_line(_14__0_line__out__1_2), ._1_line(_16__0_line__out__1), .I(i[16]), .Torus(Torus),
    .input_state(input_state), ._0_line__out__1(_15__0_line__out__1), .display(LINE_16),
    ._0_line__out__1_2(_15__0_line__out__1_2), .clock(clock), .pause(pause));
  lineSTD__not_used _16 (
    .J(J), .minus_1_line(_15__0_line__out__1_2), ._1_line(_17__0_line__out__1), .I(i[15]), .Torus(Torus),
    .input_state(input_state), ._0_line__out__1(_16__0_line__out__1), .display(LINE_15),
    ._0_line__out__1_2(_16__0_line__out__1_2), .clock(clock), .pause(pause));
  lineSTD__not_used _17 (
    .J(J), .minus_1_line(_16__0_line__out__1_2), ._1_line(_18__0_line__out__1), .I(i[14]), .Torus(Torus),
    .input_state(input_state), ._0_line__out__1(_17__0_line__out__1), .display(LINE_14),
    ._0_line__out__1_2(_17__0_line__out__1_2), .clock(clock), .pause(pause));
  lineSTD__not_used _18 (
    .J(J), .minus_1_line(_17__0_line__out__1_2), ._1_line(_19__0_line__out__1), .I(i[13]), .Torus(Torus),
    .input_state(input_state), ._0_line__out__1(_18__0_line__out__1), .display(LINE_13),
    ._0_line__out__1_2(_18__0_line__out__1_2), .clock(clock), .pause(pause));
  lineSTD__not_used _19 (
    .J(J), .minus_1_line(_18__0_line__out__1_2), ._1_line(_20__0_line__out__1), .I(i[12]), .Torus(Torus),
    .input_state(input_state), ._0_line__out__1(_19__0_line__out__1), .display(LINE_12),
    ._0_line__out__1_2(_19__0_line__out__1_2), .clock(clock), .pause(pause));
  lineSTD__not_used _20 (
    .J(J), .minus_1_line(_19__0_line__out__1_2), ._1_line(_21__0_line__out__1), .I(i[11]), .Torus(Torus),
    .input_state(input_state), ._0_line__out__1(_20__0_line__out__1), .display(LINE_11),
    ._0_line__out__1_2(_20__0_line__out__1_2), .clock(clock), .pause(pause));
  lineSTD__not_used _21 (
    .J(J), .minus_1_line(_20__0_line__out__1_2), ._1_line(_22__0_line__out__1), .I(i[10]), .Torus(Torus),
    .input_state(input_state), ._0_line__out__1(_21__0_line__out__1), .display(LINE_10),
    ._0_line__out__1_2(_21__0_line__out__1_2), .clock(clock), .pause(pause));
  lineSTD__not_used _22 (
    .J(J), .minus_1_line(_21__0_line__out__1_2), ._1_line(_23__0_line__out__1), .I(i[9]), .Torus(Torus),
    .input_state(input_state), ._0_line__out__1(_22__0_line__out__1), .display(LINE_9),
    ._0_line__out__1_2(_22__0_line__out__1_2), .clock(clock), .pause(pause));
  lineSTD__not_used _23 (
    .J(J), .minus_1_line(_22__0_line__out__1_2), ._1_line(_24__0_line__out__1), .I(i[8]), .Torus(Torus),
    .input_state(input_state), ._0_line__out__1(_23__0_line__out__1), .display(LINE_8),
    ._0_line__out__1_2(_23__0_line__out__1_2), .clock(clock), .pause(pause));
  lineSTD__not_used _24 (
    .J(J), .minus_1_line(_23__0_line__out__1_2), ._1_line(_25__0_line__out__1), .I(i[7]), .Torus(Torus),
    .input_state(input_state), ._0_line__out__1(_24__0_line__out__1), .display(LINE_7),
    ._0_line__out__1_2(_24__0_line__out__1_2), .clock(clock), .pause(pause));
  lineSTD__not_used _25 (
    .J(J), .minus_1_line(_24__0_line__out__1_2), ._1_line(_26__0_line__out__1), .I(i[6]), .Torus(Torus),
    .input_state(input_state), ._0_line__out__1(_25__0_line__out__1), .display(LINE_6),
    ._0_line__out__1_2(_25__0_line__out__1_2), .clock(clock), .pause(pause));
  lineSTD__not_used _26 (
    .J(J), .minus_1_line(_25__0_line__out__1_2), ._1_line(_27__0_line__out__1), .I(i[5]), .Torus(Torus),
    .input_state(input_state), ._0_line__out__1(_26__0_line__out__1), .display(LINE_5),
    ._0_line__out__1_2(_26__0_line__out__1_2), .clock(clock), .pause(pause));
  lineSTD__not_used _27 (
    .J(J), .minus_1_line(_26__0_line__out__1_2), ._1_line(_28__0_line__out__1), .I(i[4]), .Torus(Torus),
    .input_state(input_state), ._0_line__out__1(_27__0_line__out__1), .display(LINE_4),
    ._0_line__out__1_2(_27__0_line__out__1_2), .clock(clock), .pause(pause));
  lineSTD__not_used _28 (
    .J(J), .minus_1_line(_27__0_line__out__1_2), ._1_line(_29__0_line__out__1), .I(i[3]), .Torus(Torus),
    .input_state(input_state), ._0_line__out__1(_28__0_line__out__1), .display(LINE_3),
    ._0_line__out__1_2(_28__0_line__out__1_2), .clock(clock), .pause(pause));
  lineSTD__not_used _29 (
    .J(J), .minus_1_line(_28__0_line__out__1_2), ._1_line(_30__0_line__out__1), .I(i[2]), .Torus(Torus),
    .input_state(input_state), ._0_line__out__1(_29__0_line__out__1), .display(LINE_2),
    ._0_line__out__1_2(_29__0_line__out__1_2), .clock(clock), .pause(pause));
  lineSTD__not_used _30 (
    .J(J), .minus_1_line(_29__0_line__out__1_2), ._1_line(_31__0_line__out__1), .I(i[1]), .Torus(Torus),
    .input_state(input_state), ._0_line__out__1(_30__0_line__out__1), .display(LINE_1),
    ._0_line__out__1_2(_30__0_line__out__1_2), .clock(clock), .pause(pause));
  lineSTD__not_used _31 (
    .J(J), .minus_1_line(_30__0_line__out__1_2), ._1_line(and_2_out), .I(i[0]), .Torus(Torus),
    .input_state(input_state), ._0_line__out__1(_31__0_line__out__1), .display(LINE_0),
    ._0_line__out__1_2(plus_32), .clock(clock), .pause(pause));
  assign and_2_out = {32{Torus}} & minus_01;  // AND_Gate and_2, 32 bits wide

  // Other names for the same wires on the sheet: state[1:0] = input_state

  // Notes on the sheet:
  //   LINE_14: pull=down
  //   LINE_0: pull=down
  //   LINE_17: pull=down
  //   LINE_4: pull=down
  //   LINE_23: pull=down
  //   LINE_3: pull=down
  //   LINE_18: pull=down
  //   LINE_2: pull=down
  //   LINE_29: pull=down
  //   LINE_27: pull=down
  //   LINE_19: pull=down
  //   LINE_31: pull=down
  //   LINE_6: pull=down
  //   LINE_10: pull=down
  //   LINE_11: pull=down
  //   LINE_25: pull=down
  //   LINE_12: pull=down
  //   LINE_28: pull=down
  //   LINE_22: pull=down
  //   LINE_7: pull=down
  //   LINE_9: pull=down
  //   LINE_20: pull=down
  //   LINE_30: pull=down
  //   LINE_1: pull=down
  //   LINE_15: pull=down
  //   LINE_16: pull=down
  //   LINE_8: pull=down
  //   LINE_26: pull=down
  //   LINE_24: pull=down
  //   LINE_5: pull=down
  //   LINE_21: pull=down
  //   LINE_13: pull=down
  //   0~ — old
  //   10 — set DEAD
  //   11 — set ALIVE
endmodule

module matrix (
  input  clock,
  input  [15:0] i,
  input  [15:0] J,
  input  Torus,
  input  [1:0] input_state,
  input  pause,
  input  clear,
  input  enable,
  input  random,
  input  [24:0] lookAt,
  input  [29:0] birth1,
  input  [29:0] save1,
  input  [29:0] birth2,
  input  [29:0] save2,
  input  [1:0] whatPreset,
  output [15:0] LINE_15,
  output [15:0] LINE_14,
  output [15:0] LINE_13,
  output [15:0] LINE_12,
  output [15:0] LINE_11,
  output [15:0] LINE_10,
  output [15:0] LINE_9,
  output [15:0] LINE_8,
  output [15:0] LINE_7,
  output [15:0] LINE_6,
  output [15:0] LINE_5,
  output [15:0] LINE_4,
  output [15:0] LINE_3,
  output [15:0] LINE_2,
  output [15:0] LINE_1,
  output [15:0] LINE_0
);

  wire loadPreset;
  wire [15:0] and_1_out, and_2_out, and_3_out, and_4_out, and_5_out, and_6_out, line_1__0_line__out__1_2,
       line_1__0_line__out__2_2, line_2__0_line__out__1, line_2__0_line__out__1_2, line_2__0_line__out__2_2,
       line_3__0_line__out__1, line_3__0_line__out__1_2, line_3__0_line__out__2, line_3__0_line__out__2_2,
       line_4__0_line__out__1, line_4__0_line__out__1_2, line_4__0_line__out__2, line_4__0_line__out__2_2,
       line_5__0_line__out__1, line_5__0_line__out__1_2, line_5__0_line__out__2, line_5__0_line__out__2_2,
       line_6__0_line__out__1, line_6__0_line__out__1_2, line_6__0_line__out__2, line_6__0_line__out__2_2,
       line_7__0_line__out__1, line_7__0_line__out__1_2, line_7__0_line__out__2, line_7__0_line__out__2_2,
       line_8__0_line__out__1, line_8__0_line__out__1_2, line_8__0_line__out__2, line_8__0_line__out__2_2,
       line_9__0_line__out__1, line_9__0_line__out__1_2, line_9__0_line__out__2, line_9__0_line__out__2_2,
       line_10__0_line__out__1, line_10__0_line__out__1_2, line_10__0_line__out__2,
       line_10__0_line__out__2_2, line_11__0_line__out__1, line_11__0_line__out__1_2,
       line_11__0_line__out__2, line_11__0_line__out__2_2, line_12__0_line__out__1,
       line_12__0_line__out__1_2, line_12__0_line__out__2, line_12__0_line__out__2_2,
       line_13__0_line__out__1, line_13__0_line__out__1_2, line_13__0_line__out__2,
       line_13__0_line__out__2_2, line_14__0_line__out__1, line_14__0_line__out__1_2,
       line_14__0_line__out__2, line_14__0_line__out__2_2, line_15__0_line__out__1,
       line_15__0_line__out__1_2, line_15__0_line__out__2, line_16__0_line__out__1, minus_01, minus_01_star,
       minus_02, plus_16, plus_16_star, plus_17, presetLine0, presetLine1, presetLine2, presetLine3,
       presetLine4, presetLine5, presetLine6, presetLine7, presetLine8, presetLine9, presetLineA,
       presetLineB, presetLineC, presetLineD, presetLineE, presetLineF;

  Pull_Resistor pull_resistor_1 (.node(input_state[1]));
  Pull_Resistor pull_resistor_2 (.node(Torus));
  Pull_Resistor pull_resistor_3 (.node(input_state[0]));
  Pull_Resistor #(.pull(1)) pull_resistor_4 (.node(pause));
  Pull_Resistor pull_resistor_5 (.node(clear));
  Pull_Resistor #(.pull(1)) pull_resistor_6 (.node(enable));
  Pull_Resistor pull_resistor_7 (.node(random));
  Multiplexer #(.select(2), .width(16), .enable("false")) multiplexer_1 (
    .in0({16{1'b0}}), .in1({16{1'b0}}), .in2(16'hc0), .in3(16'hfe7f), .out(presetLine0), .sel(whatPreset));
  Multiplexer #(.select(2), .width(16), .enable("false")) multiplexer_2 (
    .in0({16{1'b0}}), .in1(16'h6db6), .in2(16'h2c0), .in3(16'ha245), .out(presetLine1), .sel(whatPreset));
  Multiplexer #(.select(2), .width(16), .enable("false")) multiplexer_3 (
    .in0({16{1'b0}}), .in1(16'h7ffe), .in2(16'h7c0), .in3(16'he667), .out(presetLine2), .sel(whatPreset));
  Multiplexer #(.select(2), .width(16), .enable("false")) multiplexer_4 (
    .in0({16{1'b0}}), .in1(16'h2004), .in2(16'hdc0), .in3(16'h8c31), .out(presetLine3), .sel(whatPreset));
  Multiplexer #(.select(2), .width(16), .enable("false")) multiplexer_5 (
    .in0({16{1'b0}}), .in1(16'h2004), .in2(16'h18c0), .in3(16'h9819), .out(presetLine4), .sel(whatPreset));
  Multiplexer #(.select(2), .width(16), .enable("false")) multiplexer_6 (
    .in0({16{1'b0}}), .in1(16'h2664), .in2(16'h3060), .in3(16'hb00d), .out(presetLine5), .sel(whatPreset));
  Multiplexer #(.select(2), .width(16), .enable("false")) multiplexer_7 (
    .in0({16{1'b0}}), .in1(16'h2664), .in2(16'h3fe0), .in3(16'he007), .out(presetLine6), .sel(whatPreset));
  Multiplexer #(.select(2), .width(16), .enable("false")) multiplexer_8 (
    .in0({16{1'b0}}), .in1(16'h2004), .in2(16'h2020), .in3({16{1'b0}}), .out(presetLine7), .sel(whatPreset));
  Multiplexer #(.select(2), .width(16), .enable("false")) multiplexer_9 (
    .in0({16{1'b0}}), .in1(16'h2004), .in2(16'h2fa0), .in3({16{1'b0}}), .out(presetLine8), .sel(whatPreset));
  Multiplexer #(.select(2), .width(16), .enable("false")) multiplexer_10 (
    .in0({16{1'b0}}), .in1(16'h2604), .in2(16'h2aa0), .in3(16'he007), .out(presetLine9), .sel(whatPreset));
  Multiplexer #(.select(2), .width(16), .enable("false")) multiplexer_11 (
    .in0({16{1'b0}}), .in1(16'h27e4), .in2(16'h2fbc), .in3(16'hb00d), .out(presetLineA), .sel(whatPreset));
  Multiplexer #(.select(2), .width(16), .enable("false")) multiplexer_12 (
    .in0({16{1'b0}}), .in1(16'h23c4), .in2(16'h2aa4), .in3(16'h9819), .out(presetLineB), .sel(whatPreset));
  Multiplexer #(.select(2), .width(16), .enable("false")) multiplexer_13 (
    .in0({16{1'b0}}), .in1(16'h2004), .in2(16'h2fac), .in3(16'h8c31), .out(presetLineC), .sel(whatPreset));
  Multiplexer #(.select(2), .width(16), .enable("false")) multiplexer_14 (
    .in0({16{1'b0}}), .in1(16'h3ffc), .in2(16'h2024), .in3(16'he667), .out(presetLineD), .sel(whatPreset));
  Multiplexer #(.select(2), .width(16), .enable("false")) multiplexer_15 (
    .in0({16{1'b0}}), .in1({16{1'b0}}), .in2(16'h3ffc), .in3(16'ha245), .out(presetLineE), .sel(whatPreset));
  Multiplexer #(.select(2), .width(16), .enable("false")) multiplexer_16 (
    .in0({16{1'b0}}), .in1({16{1'b0}}), .in2({16{1'b0}}), .in3(16'hfe7f), .out(presetLineF), .sel(whatPreset));
  or or_1 (loadPreset, whatPreset[0], whatPreset[1]);
  assign and_1_out = plus_17 & {16{Torus}};  // AND_Gate and_1, 16 bits wide
  assign and_2_out = plus_16 & {16{Torus}};  // AND_Gate and_2, 16 bits wide
  assign and_3_out = minus_02 & {16{Torus}};  // AND_Gate and_3, 16 bits wide
  assign and_4_out = {16{Torus}} & minus_01;  // AND_Gate and_4, 16 bits wide
  assign and_5_out = plus_16_star & {16{Torus}};  // AND_Gate and_5, 16 bits wide
  assign and_6_out = {16{Torus}} & minus_01_star;  // AND_Gate and_6, 16 bits wide
  line u_line_1 (
    .J(J), .minus_2_line(and_1_out), .minus_1_line(and_5_out), ._1_line(line_2__0_line__out__1),
    ._2_line(line_3__0_line__out__2), .I(i[15]), .Torus(Torus), .input_state(input_state),
    ._0_line__out__2(minus_02), ._0_line__out__1(minus_01_star),
    ._0_line__out__1_2(line_1__0_line__out__1_2), ._0_line__out__2_2(line_1__0_line__out__2_2),
    .display(LINE_15), .clock(clock), .pause(pause), .lookAt(lookAt), .birth1(birth1), .save1(save1),
    .birth2(birth2), .save2(save2), .clear(clear), .enable(enable), .random(random), .preset(presetLine0),
    .loadPreset(loadPreset));
  line u_line_2 (
    .J(J), .minus_2_line(and_2_out), .minus_1_line(line_1__0_line__out__1_2),
    ._1_line(line_3__0_line__out__1), ._2_line(line_4__0_line__out__2), .I(i[14]), .Torus(Torus),
    .input_state(input_state), ._0_line__out__2(minus_01), ._0_line__out__1(line_2__0_line__out__1),
    ._0_line__out__1_2(line_2__0_line__out__1_2), ._0_line__out__2_2(line_2__0_line__out__2_2),
    .display(LINE_14), .clock(clock), .pause(pause), .lookAt(lookAt), .birth1(birth1), .save1(save1),
    .birth2(birth2), .save2(save2), .clear(clear), .enable(enable), .random(random), .preset(presetLine1),
    .loadPreset(loadPreset));
  line u_line_3 (
    .J(J), .minus_2_line(line_1__0_line__out__2_2), .minus_1_line(line_2__0_line__out__1_2),
    ._1_line(line_4__0_line__out__1), ._2_line(line_5__0_line__out__2), .I(i[13]), .Torus(Torus),
    .input_state(input_state), ._0_line__out__2(line_3__0_line__out__2),
    ._0_line__out__1(line_3__0_line__out__1), ._0_line__out__1_2(line_3__0_line__out__1_2),
    ._0_line__out__2_2(line_3__0_line__out__2_2), .display(LINE_13), .clock(clock), .pause(pause),
    .lookAt(lookAt), .birth1(birth1), .save1(save1), .birth2(birth2), .save2(save2), .clear(clear),
    .enable(enable), .random(random), .preset(presetLine2), .loadPreset(loadPreset));
  line u_line_4 (
    .J(J), .minus_2_line(line_2__0_line__out__2_2), .minus_1_line(line_3__0_line__out__1_2),
    ._1_line(line_5__0_line__out__1), ._2_line(line_6__0_line__out__2), .I(i[12]), .Torus(Torus),
    .input_state(input_state), ._0_line__out__2(line_4__0_line__out__2),
    ._0_line__out__1(line_4__0_line__out__1), ._0_line__out__1_2(line_4__0_line__out__1_2),
    ._0_line__out__2_2(line_4__0_line__out__2_2), .display(LINE_12), .clock(clock), .pause(pause),
    .lookAt(lookAt), .birth1(birth1), .save1(save1), .birth2(birth2), .save2(save2), .clear(clear),
    .enable(enable), .random(random), .preset(presetLine3), .loadPreset(loadPreset));
  line u_line_5 (
    .J(J), .minus_2_line(line_3__0_line__out__2_2), .minus_1_line(line_4__0_line__out__1_2),
    ._1_line(line_6__0_line__out__1), ._2_line(line_7__0_line__out__2), .I(i[11]), .Torus(Torus),
    .input_state(input_state), ._0_line__out__2(line_5__0_line__out__2),
    ._0_line__out__1(line_5__0_line__out__1), ._0_line__out__1_2(line_5__0_line__out__1_2),
    ._0_line__out__2_2(line_5__0_line__out__2_2), .display(LINE_11), .clock(clock), .pause(pause),
    .lookAt(lookAt), .birth1(birth1), .save1(save1), .birth2(birth2), .save2(save2), .clear(clear),
    .enable(enable), .random(random), .preset(presetLine4), .loadPreset(loadPreset));
  line u_line_6 (
    .J(J), .minus_2_line(line_4__0_line__out__2_2), .minus_1_line(line_5__0_line__out__1_2),
    ._1_line(line_7__0_line__out__1), ._2_line(line_8__0_line__out__2), .I(i[10]), .Torus(Torus),
    .input_state(input_state), ._0_line__out__2(line_6__0_line__out__2),
    ._0_line__out__1(line_6__0_line__out__1), ._0_line__out__1_2(line_6__0_line__out__1_2),
    ._0_line__out__2_2(line_6__0_line__out__2_2), .display(LINE_10), .clock(clock), .pause(pause),
    .lookAt(lookAt), .birth1(birth1), .save1(save1), .birth2(birth2), .save2(save2), .clear(clear),
    .enable(enable), .random(random), .preset(presetLine5), .loadPreset(loadPreset));
  line u_line_7 (
    .J(J), .minus_2_line(line_5__0_line__out__2_2), .minus_1_line(line_6__0_line__out__1_2),
    ._1_line(line_8__0_line__out__1), ._2_line(line_9__0_line__out__2), .I(i[9]), .Torus(Torus),
    .input_state(input_state), ._0_line__out__2(line_7__0_line__out__2),
    ._0_line__out__1(line_7__0_line__out__1), ._0_line__out__1_2(line_7__0_line__out__1_2),
    ._0_line__out__2_2(line_7__0_line__out__2_2), .display(LINE_9), .clock(clock), .pause(pause),
    .lookAt(lookAt), .birth1(birth1), .save1(save1), .birth2(birth2), .save2(save2), .clear(clear),
    .enable(enable), .random(random), .preset(presetLine6), .loadPreset(loadPreset));
  line u_line_8 (
    .J(J), .minus_2_line(line_6__0_line__out__2_2), .minus_1_line(line_7__0_line__out__1_2),
    ._1_line(line_9__0_line__out__1), ._2_line(line_10__0_line__out__2), .I(i[8]), .Torus(Torus),
    .input_state(input_state), ._0_line__out__2(line_8__0_line__out__2),
    ._0_line__out__1(line_8__0_line__out__1), ._0_line__out__1_2(line_8__0_line__out__1_2),
    ._0_line__out__2_2(line_8__0_line__out__2_2), .display(LINE_8), .clock(clock), .pause(pause),
    .lookAt(lookAt), .birth1(birth1), .save1(save1), .birth2(birth2), .save2(save2), .clear(clear),
    .enable(enable), .random(random), .preset(presetLine7), .loadPreset(loadPreset));
  line u_line_9 (
    .J(J), .minus_2_line(line_7__0_line__out__2_2), .minus_1_line(line_8__0_line__out__1_2),
    ._1_line(line_10__0_line__out__1), ._2_line(line_11__0_line__out__2), .I(i[7]), .Torus(Torus),
    .input_state(input_state), ._0_line__out__2(line_9__0_line__out__2),
    ._0_line__out__1(line_9__0_line__out__1), ._0_line__out__1_2(line_9__0_line__out__1_2),
    ._0_line__out__2_2(line_9__0_line__out__2_2), .display(LINE_7), .clock(clock), .pause(pause),
    .lookAt(lookAt), .birth1(birth1), .save1(save1), .birth2(birth2), .save2(save2), .clear(clear),
    .enable(enable), .random(random), .preset(presetLine8), .loadPreset(loadPreset));
  line u_line_10 (
    .J(J), .minus_2_line(line_8__0_line__out__2_2), .minus_1_line(line_9__0_line__out__1_2),
    ._1_line(line_11__0_line__out__1), ._2_line(line_12__0_line__out__2), .I(i[6]), .Torus(Torus),
    .input_state(input_state), ._0_line__out__2(line_10__0_line__out__2),
    ._0_line__out__1(line_10__0_line__out__1), ._0_line__out__1_2(line_10__0_line__out__1_2),
    ._0_line__out__2_2(line_10__0_line__out__2_2), .display(LINE_6), .clock(clock), .pause(pause),
    .lookAt(lookAt), .birth1(birth1), .save1(save1), .birth2(birth2), .save2(save2), .clear(clear),
    .enable(enable), .random(random), .preset(presetLine9), .loadPreset(loadPreset));
  line u_line_11 (
    .J(J), .minus_2_line(line_9__0_line__out__2_2), .minus_1_line(line_10__0_line__out__1_2),
    ._1_line(line_12__0_line__out__1), ._2_line(line_13__0_line__out__2), .I(i[5]), .Torus(Torus),
    .input_state(input_state), ._0_line__out__2(line_11__0_line__out__2),
    ._0_line__out__1(line_11__0_line__out__1), ._0_line__out__1_2(line_11__0_line__out__1_2),
    ._0_line__out__2_2(line_11__0_line__out__2_2), .display(LINE_5), .clock(clock), .pause(pause),
    .lookAt(lookAt), .birth1(birth1), .save1(save1), .birth2(birth2), .save2(save2), .clear(clear),
    .enable(enable), .random(random), .preset(presetLineA), .loadPreset(loadPreset));
  line u_line_12 (
    .J(J), .minus_2_line(line_10__0_line__out__2_2), .minus_1_line(line_11__0_line__out__1_2),
    ._1_line(line_13__0_line__out__1), ._2_line(line_14__0_line__out__2), .I(i[4]), .Torus(Torus),
    .input_state(input_state), ._0_line__out__2(line_12__0_line__out__2),
    ._0_line__out__1(line_12__0_line__out__1), ._0_line__out__1_2(line_12__0_line__out__1_2),
    ._0_line__out__2_2(line_12__0_line__out__2_2), .display(LINE_4), .clock(clock), .pause(pause),
    .lookAt(lookAt), .birth1(birth1), .save1(save1), .birth2(birth2), .save2(save2), .clear(clear),
    .enable(enable), .random(random), .preset(presetLineB), .loadPreset(loadPreset));
  line u_line_13 (
    .J(J), .minus_2_line(line_11__0_line__out__2_2), .minus_1_line(line_12__0_line__out__1_2),
    ._1_line(line_14__0_line__out__1), ._2_line(line_15__0_line__out__2), .I(i[3]), .Torus(Torus),
    .input_state(input_state), ._0_line__out__2(line_13__0_line__out__2),
    ._0_line__out__1(line_13__0_line__out__1), ._0_line__out__1_2(line_13__0_line__out__1_2),
    ._0_line__out__2_2(line_13__0_line__out__2_2), .display(LINE_3), .clock(clock), .pause(pause),
    .lookAt(lookAt), .birth1(birth1), .save1(save1), .birth2(birth2), .save2(save2), .clear(clear),
    .enable(enable), .random(random), .preset(presetLineC), .loadPreset(loadPreset));
  line u_line_14 (
    .J(J), .minus_2_line(line_12__0_line__out__2_2), .minus_1_line(line_13__0_line__out__1_2),
    ._1_line(line_15__0_line__out__1), .I(i[2]), .Torus(Torus), .input_state(input_state),
    ._0_line__out__2(line_14__0_line__out__2), ._0_line__out__1(line_14__0_line__out__1),
    ._0_line__out__1_2(line_14__0_line__out__1_2), ._0_line__out__2_2(line_14__0_line__out__2_2),
    .display(LINE_2), .clock(clock), .pause(pause), .lookAt(lookAt), .birth1(birth1), .save1(save1),
    .birth2(birth2), .save2(save2), .clear(clear), .enable(enable), .random(random), .preset(presetLineD),
    .loadPreset(loadPreset));  // open: _2_line
  line u_line_15 (
    .J(J), .minus_2_line(line_13__0_line__out__2_2), .minus_1_line(line_14__0_line__out__1_2),
    ._1_line(line_16__0_line__out__1), ._2_line(and_4_out), .I(i[1]), .Torus(Torus),
    .input_state(input_state), ._0_line__out__2(line_15__0_line__out__2),
    ._0_line__out__1(line_15__0_line__out__1), ._0_line__out__1_2(line_15__0_line__out__1_2),
    ._0_line__out__2_2(plus_16), .display(LINE_1), .clock(clock), .pause(pause), .lookAt(lookAt),
    .birth1(birth1), .save1(save1), .birth2(birth2), .save2(save2), .clear(clear), .enable(enable),
    .random(random), .preset(presetLineE), .loadPreset(loadPreset));
  line line_16 (
    .J(J), .minus_2_line(line_14__0_line__out__2_2), .minus_1_line(line_15__0_line__out__1_2),
    ._1_line(and_6_out), ._2_line(and_3_out), .I(i[0]), .Torus(Torus), .input_state(input_state),
    ._0_line__out__1(line_16__0_line__out__1), ._0_line__out__1_2(plus_16_star), ._0_line__out__2_2(plus_17),
    .display(LINE_0), .clock(clock), .pause(pause), .lookAt(lookAt), .birth1(birth1), .save1(save1),
    .birth2(birth2), .save2(save2), .clear(clear), .enable(enable), .random(random), .preset(presetLineF),
    .loadPreset(loadPreset));  // open: _0_line__out__2

  // Other names for the same wires on the sheet: B1[29:0] = birth1; B2[29:0] = birth2; S1[29:0] = save1;
  //   S2[29:0] = save2; state[1:0] = input_state; torus16[15:0] = {16{Torus}}

  // Notes on the sheet:
  //   birth2: pull=down
  //   save1: pull=down
  //   LINE_3: pull=down
  //   LINE_11: pull=down
  //   LINE_6: pull=down
  //   LINE_13: pull=down
  //   LINE_15: pull=down
  //   save2: pull=down
  //   LINE_8: pull=down
  //   LINE_14: pull=down
  //   LINE_9: pull=down
  //   LINE_5: pull=down
  //   LINE_10: pull=down
  //   LINE_7: pull=down
  //   LINE_12: pull=down
  //   birth1: pull=down
  //   LINE_2: pull=down
  //   LINE_1: pull=down
  //   lookAt: pull=down
  //   LINE_4: pull=down
  //   LINE_0: pull=down
  //   preset 1
  //   00 — old
  //   01 — invert
  //   10 — set DEAD
  //   11 — set ALIVE
endmodule

module gameSTD__not_used (
  input  in_1,
  input  [31:0] i,
  input  in_3,
  input  in_4,
  input  [31:0] j,
  input  torus,
  input  [1:0] state,
  input  pause
);

  wire clock_1_out;
  wire [31:0] matrixstd_not_used_1_line_0, matrixstd_not_used_1_line_1, matrixstd_not_used_1_line_2,
       matrixstd_not_used_1_line_3, matrixstd_not_used_1_line_4, matrixstd_not_used_1_line_5,
       matrixstd_not_used_1_line_6, matrixstd_not_used_1_line_7, matrixstd_not_used_1_line_8,
       matrixstd_not_used_1_line_9, matrixstd_not_used_1_line_10, matrixstd_not_used_1_line_11,
       matrixstd_not_used_1_line_12, matrixstd_not_used_1_line_13, matrixstd_not_used_1_line_14,
       matrixstd_not_used_1_line_15, matrixstd_not_used_1_line_16, matrixstd_not_used_1_line_17,
       matrixstd_not_used_1_line_18, matrixstd_not_used_1_line_19, matrixstd_not_used_1_line_20,
       matrixstd_not_used_1_line_21, matrixstd_not_used_1_line_22, matrixstd_not_used_1_line_23,
       matrixstd_not_used_1_line_24, matrixstd_not_used_1_line_25, matrixstd_not_used_1_line_26,
       matrixstd_not_used_1_line_27, matrixstd_not_used_1_line_28, matrixstd_not_used_1_line_29,
       matrixstd_not_used_1_line_30, matrixstd_not_used_1_line_31, multiplexer_1_out, multiplexer_2_out,
       multiplexer_3_out;

  Multiplexer #(.width(32)) multiplexer_1 (
    .in0({32{1'b0}}), .in1({32{1'b1}}), .out(multiplexer_1_out), .sel(in_1));  // open: en
  Multiplexer #(.width(32)) multiplexer_2 (
    .in0(i), .in1(multiplexer_1_out), .out(multiplexer_2_out), .sel(in_3));  // open: en
  Multiplexer #(.width(32)) multiplexer_3 (
    .in0(j), .in1(multiplexer_1_out), .out(multiplexer_3_out), .sel(in_4));  // open: en
  Clock clock_1 (.out(clock_1_out));
  matrixSTD__not_used matrixstd_not_used_1 (
    .i(multiplexer_2_out), .J(multiplexer_3_out), .Torus(torus), .input_state(state), .clock(clock_1_out),
    .pause(pause), .LINE_31(matrixstd_not_used_1_line_31), .LINE_30(matrixstd_not_used_1_line_30),
    .LINE_29(matrixstd_not_used_1_line_29), .LINE_28(matrixstd_not_used_1_line_28),
    .LINE_27(matrixstd_not_used_1_line_27), .LINE_26(matrixstd_not_used_1_line_26),
    .LINE_25(matrixstd_not_used_1_line_25), .LINE_24(matrixstd_not_used_1_line_24),
    .LINE_23(matrixstd_not_used_1_line_23), .LINE_22(matrixstd_not_used_1_line_22),
    .LINE_21(matrixstd_not_used_1_line_21), .LINE_20(matrixstd_not_used_1_line_20),
    .LINE_19(matrixstd_not_used_1_line_19), .LINE_18(matrixstd_not_used_1_line_18),
    .LINE_17(matrixstd_not_used_1_line_17), .LINE_16(matrixstd_not_used_1_line_16),
    .LINE_15(matrixstd_not_used_1_line_15), .LINE_14(matrixstd_not_used_1_line_14),
    .LINE_13(matrixstd_not_used_1_line_13), .LINE_12(matrixstd_not_used_1_line_12),
    .LINE_11(matrixstd_not_used_1_line_11), .LINE_10(matrixstd_not_used_1_line_10),
    .LINE_9(matrixstd_not_used_1_line_9), .LINE_8(matrixstd_not_used_1_line_8),
    .LINE_7(matrixstd_not_used_1_line_7), .LINE_6(matrixstd_not_used_1_line_6),
    .LINE_5(matrixstd_not_used_1_line_5), .LINE_4(matrixstd_not_used_1_line_4),
    .LINE_3(matrixstd_not_used_1_line_3), .LINE_2(matrixstd_not_used_1_line_2),
    .LINE_1(matrixstd_not_used_1_line_1), .LINE_0(matrixstd_not_used_1_line_0));
  DotMatrix #(.inputtype("row"), .matrixcols(32), .matrixrows(32)) dotmatrix_1 (
    .row0(matrixstd_not_used_1_line_31), .row1(matrixstd_not_used_1_line_30),
    .row2(matrixstd_not_used_1_line_29), .row3(matrixstd_not_used_1_line_28),
    .row4(matrixstd_not_used_1_line_27), .row5(matrixstd_not_used_1_line_26),
    .row6(matrixstd_not_used_1_line_25), .row7(matrixstd_not_used_1_line_24),
    .row8(matrixstd_not_used_1_line_23), .row9(matrixstd_not_used_1_line_22),
    .row10(matrixstd_not_used_1_line_21), .row11(matrixstd_not_used_1_line_20),
    .row12(matrixstd_not_used_1_line_19), .row13(matrixstd_not_used_1_line_18),
    .row14(matrixstd_not_used_1_line_17), .row15(matrixstd_not_used_1_line_16),
    .row16(matrixstd_not_used_1_line_15), .row17(matrixstd_not_used_1_line_14),
    .row18(matrixstd_not_used_1_line_13), .row19(matrixstd_not_used_1_line_12),
    .row20(matrixstd_not_used_1_line_11), .row21(matrixstd_not_used_1_line_10),
    .row22(matrixstd_not_used_1_line_9), .row23(matrixstd_not_used_1_line_8),
    .row24(matrixstd_not_used_1_line_7), .row25(matrixstd_not_used_1_line_6),
    .row26(matrixstd_not_used_1_line_5), .row27(matrixstd_not_used_1_line_4),
    .row28(matrixstd_not_used_1_line_3), .row29(matrixstd_not_used_1_line_2),
    .row30(matrixstd_not_used_1_line_1), .row31(matrixstd_not_used_1_line_0));

  // Notes on the sheet:
  //   00 — old
  //   01 — invert
  //   10 — set DEAD
  //   11 — set ALIVE
endmodule

module game (
  input  Rules_editor__below___0__or_Standard_rules__1,
  input  [4:0] minus_2_line,
  input  [5:0] num_1,
  input  [5:0] num_1_2,
  input  [4:0] minus_1_line,
  input  [5:0] num_2,
  input  [5:0] num_2_2,
  input  [4:0] cur_line,
  input  [5:0] num_3,
  input  [5:0] num_3_2,
  input  [4:0] plus_1_line,
  input  [5:0] num_4,
  input  [5:0] num_4_2,
  input  [4:0] plus_2_line,
  input  [5:0] num_5,
  input  [5:0] num_5_2,
  input  [5:0] num_6,
  input  [5:0] num_6_2,
  input  [5:0] num_7,
  input  [5:0] num_7_2,
  input  [5:0] num_8,
  input  [5:0] num_8_2,
  input  [5:0] num_9,
  input  [5:0] num_9_2,
  input  [5:0] num_10,
  input  [5:0] num_10_2,
  input  [5:0] num_11,
  input  [5:0] num_11_2,
  input  [5:0] num_12,
  input  [5:0] num_12_2
);

  wire _0, _1, clear, clock, D, inv, L, main_1_clear, main_1_enable, main_1_pause, main_1_torus, pause, R,
       tor, tunnel, U;
  wire [1:0] main_1_state;
  wire [7:0] KB_out;
  wire [15:0] i, j, matrix_1_line_0, matrix_1_line_1, matrix_1_line_2, matrix_1_line_3, matrix_1_line_4,
       matrix_1_line_5, matrix_1_line_6, matrix_1_line_7, matrix_1_line_8, matrix_1_line_9, matrix_1_line_10,
       matrix_1_line_11, matrix_1_line_12, matrix_1_line_13, matrix_1_line_14, matrix_1_line_15;
  wire [24:0] lookAt;
  wire [29:0] birth1, birth2, RE_birth1, RE_birth2, RE_save1, RE_save2, save1, save2;

  Multiplexer #(.width(25), .enable("false")) multiplexer_1 (
    .in0({plus_2_line, plus_1_line, cur_line, minus_1_line, minus_2_line}), .in1(25'h729c0), .out(lookAt),
    .sel(Rules_editor__below___0__or_Standard_rules__1));
  Multiplexer #(.width(30), .enable("false")) multiplexer_2 (
    .in0(RE_birth1), .in1(30'h3fffffe3), .out(birth1), .sel(Rules_editor__below___0__or_Standard_rules__1));
  Multiplexer #(.width(30), .enable("false")) multiplexer_3 (
    .in0(RE_save1), .in1(30'h3ffffc62), .out(save1), .sel(Rules_editor__below___0__or_Standard_rules__1));
  Multiplexer #(.width(30), .enable("false")) multiplexer_4 (
    .in0(RE_birth2), .in1({30{1'b1}}), .out(birth2), .sel(Rules_editor__below___0__or_Standard_rules__1));
  Multiplexer #(.width(30), .enable("false")) multiplexer_5 (
    .in0(RE_save2), .in1({30{1'b1}}), .out(save2), .sel(Rules_editor__below___0__or_Standard_rules__1));
  BS_helper bs_helper_1 (.input_6_bit(num_1), .output_5_bit(RE_birth1[4:0]));
  BS_helper_0__31 bs_helper_0_31_1 (.input_6_bit(num_2), .output_5_bit(RE_birth1[9:5]));
  BS_helper_0__31 bs_helper_0_31_2 (.input_6_bit(num_3), .output_5_bit(RE_birth1[14:10]));
  BS_helper_0__31 bs_helper_0_31_3 (.input_6_bit(num_4), .output_5_bit(RE_birth1[19:15]));
  BS_helper_0__31 bs_helper_0_31_4 (.input_6_bit(num_5), .output_5_bit(RE_birth1[24:20]));
  BS_helper_0__31 bs_helper_0_31_5 (.input_6_bit(num_6), .output_5_bit(RE_birth1[29:25]));
  BS_helper_0__31 bs_helper_0_31_6 (.input_6_bit(num_7), .output_5_bit(RE_birth2[4:0]));
  BS_helper_0__31 bs_helper_0_31_7 (.input_6_bit(num_8), .output_5_bit(RE_birth2[9:5]));
  BS_helper_0__31 bs_helper_0_31_8 (.input_6_bit(num_9), .output_5_bit(RE_birth2[14:10]));
  BS_helper_0__31 bs_helper_0_31_9 (.input_6_bit(num_10), .output_5_bit(RE_birth2[19:15]));
  BS_helper_0__31 bs_helper_0_31_10 (.input_6_bit(num_11), .output_5_bit(RE_birth2[24:20]));
  BS_helper_0__31 bs_helper_0_31_11 (.input_6_bit(num_12), .output_5_bit(RE_birth2[29:25]));
  main main_1 (
    .clock(clock), .KeyBoard(KB_out), .i__row(i), .j__column(j), .torus(main_1_torus), .state(main_1_state),
    .pause(main_1_pause), .clear(main_1_clear), .enable(main_1_enable), .KB_lamp(tunnel));
  Clock clock_1 (.out(clock));
  // Probe on RE_birth1[4:0]
  // Probe on RE_birth1[9:5]
  // Probe on RE_birth1[14:10]
  // Probe on RE_birth1[19:15]
  // Probe on RE_birth1[24:20]
  // Probe on RE_birth1[29:25]
  // Probe on RE_birth2[4:0]
  // Probe on RE_birth2[9:5]
  // Probe on RE_birth2[14:10]
  // Probe on RE_birth2[19:15]
  // Probe on RE_birth2[24:20]
  // Probe on RE_birth2[29:25]
  // Probe on 5'b00011
  // Probe on {5{1'b1}}
  // Probe on {5{1'b1}}
  // Probe on {5{1'b1}}
  // Probe on {5{1'b1}}
  // Probe on {5{1'b1}}
  // Probe on {5{1'b1}}
  // Probe on {5{1'b1}}
  // Probe on {5{1'b1}}
  // Probe on {5{1'b1}}
  // Probe on {5{1'b1}}
  // Probe on {5{1'b1}}
  DotMatrix #(.inputtype("row"), .matrixcols(16), .matrixrows(1)) dotmatrix_1 (.row0(j));
  DotMatrix #(.inputtype("row"), .matrixcols(16), .matrixrows(16)) dotmatrix_2 (
    .row0(matrix_1_line_15), .row1(matrix_1_line_14), .row2(matrix_1_line_13), .row3(matrix_1_line_12),
    .row4(matrix_1_line_11), .row5(matrix_1_line_10), .row6(matrix_1_line_9), .row7(matrix_1_line_8),
    .row8(matrix_1_line_7), .row9(matrix_1_line_6), .row10(matrix_1_line_5), .row11(matrix_1_line_4),
    .row12(matrix_1_line_3), .row13(matrix_1_line_2), .row14(matrix_1_line_1), .row15(matrix_1_line_0));
  matrix matrix_1 (
    .i(i), .J(j), .Torus(main_1_torus), .input_state(main_1_state), .LINE_0(matrix_1_line_0),
    .LINE_1(matrix_1_line_1), .LINE_2(matrix_1_line_2), .LINE_3(matrix_1_line_3), .LINE_4(matrix_1_line_4),
    .LINE_5(matrix_1_line_5), .LINE_6(matrix_1_line_6), .LINE_7(matrix_1_line_7), .LINE_8(matrix_1_line_8),
    .LINE_9(matrix_1_line_9), .LINE_10(matrix_1_line_10), .LINE_11(matrix_1_line_11),
    .LINE_12(matrix_1_line_12), .LINE_13(matrix_1_line_13), .LINE_14(matrix_1_line_14),
    .LINE_15(matrix_1_line_15), .clock(clock), .pause(main_1_pause), .lookAt(lookAt), .birth1(birth1),
    .save1(save1), .birth2(birth2), .save2(save2), .clear(main_1_clear), .enable(main_1_enable));  // open: random, whatPreset
  Button u_tor (.out(tor));
  DotMatrix #(.inputtype("row"), .matrixcols(1), .matrixrows(16)) dotmatrix_3 (
    .row0(i[15]), .row1(i[14]), .row2(i[13]), .row3(i[12]), .row4(i[11]), .row5(i[10]), .row6(i[9]),
    .row7(i[8]), .row8(i[7]), .row9(i[6]), .row10(i[5]), .row11(i[4]), .row12(i[3]), .row13(i[2]),
    .row14(i[1]), .row15(i[0]));
  Button u__1 (.out(_1));
  Button u_inv (.out(inv));
  Button u__0 (.out(_0));
  Button u_clear (.out(clear));
  BS_helper bs_helper_2 (.input_6_bit(num_1_2), .output_5_bit(RE_save1[4:0]));
  // Probe on RE_save1[4:0]
  // Probe on RE_save1[9:5]
  BS_helper_0__31 bs_helper_0_31_12 (.input_6_bit(num_2_2), .output_5_bit(RE_save1[9:5]));
  // Probe on RE_save1[14:10]
  BS_helper_0__31 bs_helper_0_31_13 (.input_6_bit(num_3_2), .output_5_bit(RE_save1[14:10]));
  BS_helper_0__31 bs_helper_0_31_14 (.input_6_bit(num_4_2), .output_5_bit(RE_save1[19:15]));
  // Probe on RE_save1[19:15]
  BS_helper_0__31 bs_helper_0_31_15 (.input_6_bit(num_5_2), .output_5_bit(RE_save1[24:20]));
  // Probe on RE_save1[24:20]
  // Probe on RE_save1[29:25]
  BS_helper_0__31 bs_helper_0_31_16 (.input_6_bit(num_6_2), .output_5_bit(RE_save1[29:25]));
  BS_helper_0__31 bs_helper_0_31_17 (.input_6_bit(num_7_2), .output_5_bit(RE_save2[4:0]));
  // Probe on RE_save2[4:0]
  // Probe on RE_save2[9:5]
  BS_helper_0__31 bs_helper_0_31_18 (.input_6_bit(num_8_2), .output_5_bit(RE_save2[9:5]));
  // Probe on RE_save2[14:10]
  BS_helper_0__31 bs_helper_0_31_19 (.input_6_bit(num_9_2), .output_5_bit(RE_save2[14:10]));
  BS_helper_0__31 bs_helper_0_31_20 (.input_6_bit(num_10_2), .output_5_bit(RE_save2[19:15]));
  // Probe on RE_save2[19:15]
  // Probe on RE_save2[24:20]
  BS_helper_0__31 bs_helper_0_31_21 (.input_6_bit(num_11_2), .output_5_bit(RE_save2[24:20]));
  // Probe on RE_save2[29:25]
  BS_helper_0__31 bs_helper_0_31_22 (.input_6_bit(num_12_2), .output_5_bit(RE_save2[29:25]));
  // Probe on 5'b00010
  // Probe on 5'b00011
  // Probe on {5{1'b1}}
  // Probe on {5{1'b1}}
  // Probe on {5{1'b1}}
  // Probe on {5{1'b1}}
  // Probe on {5{1'b1}}
  // Probe on {5{1'b1}}
  // Probe on {5{1'b1}}
  // Probe on {5{1'b1}}
  // Probe on {5{1'b1}}
  // Probe on {5{1'b1}}
  Button button (.out(L));
  Button space (.out(pause));
  // Probe on KB_out
  LED led_1 (.in(tunnel));
  Button button_2 (.out(U));
  Button button_3 (.out(R));
  Button button_4 (.out(D));
  // Probe on KB_out
  KeyBoard keyboard_1 (
    .LEFT(L), .DOWN(D), .RIGHT(R), .UP(U), ._1(_1), ._0(_0), .SPACE(pause), .out(KB_out), .CLEAR(clear),
    .INVERT(inv), .torus(tor));
  LED led_2 (.in(U));
  LED led_3 (.in(R));
  LED led_4 (.in(L));
  LED led_5 (.in(D));

  // Other names for the same wires on the sheet: RE_lookAt[24:0] = {plus_2_line, plus_1_line, cur_line, minus_1_line, minus_2_line}

  // Notes on the sheet:
  //   Standard rules:
  //   0. Neighbors are nearby cells (like a king in chess)
  //   I. 3 neighbours — cell can be born
  //   II. 2 or 3 neighbours — cell continues to live
  //   III. Otherwise, the cell dies
  //   look at
  //   look at
  //   birth
  //   birth
  //   Set up rules
  //   Standard rules
  //   KeyBoard
  //   save
  //   save
endmodule

module reverse16Bits (
  input  [15:0] in,
  output [15:0] out
);


  assign out = {in[0], in[1], in[2], in[3], in[4], in[5], in[6], in[7], in[8], in[9], in[10], in[11], in[12], in[13], in[14], in[15]};

  // Notes on the sheet:
  //   in: pull=down
  //   out: pull=down
endmodule

// NO_CDM
module insteadOfCDM8 (
  input  clock,
  input  [7:0] KeyBoard,
  output KB_lamp,
  output [15:0] i__row,
  output [15:0] j__column,
  output torus,
  output [1:0] state,
  output pause,
  output clear,
  output enable
);

  wire and_1_out, and_2_out, comparator_1_eq, comparator_2_eq, not_1_out, not_2_out, or_1_out, or_2_out,
       or_3_out, or_4_out, torus_t;
  wire [15:0] bit_extender_1_out, j, up_right_down_left_1_out_i_j, up_right_down_left_2_out_i_j;

  reverse16Bits reverse16bits_1 (.in(j), .out(j__column));
  not not_1 (not_1_out, torus);
  and u_torus (torus_t, KeyBoard[0], KeyBoard[1], KeyBoard[2], KeyBoard[3]);
  not not_2 (not_2_out, pause);
  Register #(.width(1)) torus_2 (.D(not_1_out), .en(torus_t), .Q(torus), .clk(clock));  // open: clr
  Register #(.width(2)) u_state (.D(KeyBoard[5:4]), .Q(state), .clk(clock));  // open: en, clr
  Register #(.width(1)) u_pause (.D(not_2_out), .en(KeyBoard[7]), .Q(pause), .clk(clock));  // open: clr
  assign bit_extender_1_out = {{15{1'b0}}, 1'b0};  // Bit_Extender bit_extender_1
  up_right_down_left up_right_down_left_1 (
    .i_j(i__row), .down_left(KeyBoard[1]), .out_i_j(up_right_down_left_1_out_i_j));
  Comparator #(.width(16)) comparator_1 (.a(i__row), .b(bit_extender_1_out), .eq(comparator_1_eq));  // open: gt, lt
  or or_1 (or_1_out, comparator_1_eq, and_1_out);
  or or_2 (or_2_out, KeyBoard[1], KeyBoard[3]);
  and and_1 (and_1_out, or_2_out, ~torus_t);  // AND_Gate
  up_right_down_left up_right_down_left_2 (.i_j(j), .down_left(KeyBoard[0]), .out_i_j(up_right_down_left_2_out_i_j));
  Comparator #(.width(16)) comparator_2 (.a(bit_extender_1_out), .b(j), .eq(comparator_2_eq));  // open: gt, lt
  or or_3 (or_3_out, comparator_2_eq, and_2_out);
  or or_4 (or_4_out, KeyBoard[0], KeyBoard[2]);
  and and_2 (and_2_out, or_4_out, ~torus_t);  // AND_Gate
  Register #(.width(16)) i (.D(up_right_down_left_1_out_i_j), .en(or_1_out), .Q(i__row), .clk(clock));  // open: clr
  Register #(.width(16)) u_j (.D(up_right_down_left_2_out_i_j), .en(or_3_out), .Q(j), .clk(clock));  // open: clr

  assign clear = KeyBoard[6];
  assign enable = 1'b1;
  assign KB_lamp = 1'b1;

  // Other names for the same wires on the sheet: KB_out[7:0] = KeyBoard; i[15:0] = i__row; left = KeyBoard[0];
  //   down = KeyBoard[1]; right = KeyBoard[2]; up = KeyBoard[3]; state_t[4:0] = {KeyBoard[6], pause, state, torus}

  // Notes on the sheet:
  //   enable
  //   clear
endmodule

module up_right_down_left (
  input  [15:0] i_j,
  input  down_left,
  output [15:0] out_i_j
);

  wire or_1_out;
  wire [15:0] multiplexer_1_out, multiplexer_2_out, multiplexer_3_out;

  Multiplexer #(.width(16)) multiplexer_1 (
    .in0({1'b0, i_j[15:1]}), .in1(i_j), .out(multiplexer_1_out), .sel(i_j[0]));  // open: en
  Multiplexer #(.width(16)) multiplexer_2 (
    .in0({i_j[14:0], 1'b0}), .in1(i_j), .out(multiplexer_2_out), .sel(i_j[15]));  // open: en
  Multiplexer #(.width(16)) multiplexer_3 (
    .in0(multiplexer_2_out), .in1(multiplexer_1_out), .out(multiplexer_3_out), .sel(down_left));  // open: en
  Multiplexer #(.width(16)) multiplexer_4 (
    .in0(16'h1), .in1(multiplexer_3_out), .out(out_i_j), .sel(or_1_out));  // open: en
  or or_1 (or_1_out, i_j[15], i_j[14], i_j[13], i_j[12], i_j[11], i_j[10], i_j[9], i_j[8], i_j[7], i_j[6], i_j[5], i_j[4], i_j[3], i_j[2], i_j[1], i_j[0]);

  // Notes on the sheet:
  //   up/right
  //   if cursor is max, I can't move it
  //   down/left
  //   if cursor is min, I can't move it
  //   if i/j == 0 set 1
endmodule

module gameWithOutCDM8 (
  input  Rules_editor__below___0__or_Standard_rules__1,
  input  [4:0] minus_2_line,
  input  [5:0] num_1,
  input  [5:0] num_1_2,
  input  [4:0] minus_1_line,
  input  [5:0] num_2,
  input  [5:0] num_2_2,
  input  [4:0] cur_line,
  input  [5:0] num_3,
  input  [5:0] num_3_2,
  input  [4:0] plus_1_line,
  input  [5:0] num_4,
  input  [5:0] num_4_2,
  input  [4:0] plus_2_line,
  input  [5:0] num_5,
  input  [5:0] num_5_2,
  input  [5:0] num_6,
  input  [5:0] num_6_2,
  input  [5:0] num_7,
  input  [5:0] num_7_2,
  input  [5:0] num_8,
  input  [5:0] num_8_2,
  input  [5:0] num_9,
  input  [5:0] num_9_2,
  input  [5:0] num_10,
  input  [5:0] num_10_2,
  input  [5:0] num_11,
  input  [5:0] num_11_2,
  input  [5:0] num_12,
  input  [5:0] num_12_2
);

  wire _0, _1, clear, clock, D, insteadofcdm8_1_clear, insteadofcdm8_1_enable, inv, L, pause, pre1, pre2,
       pre3, R, random, sP, sT, tor, tunnel, U;
  wire [1:0] insteadofcdm8_1_state, multiplexer_1_out, multiplexer_2_out, preset;
  wire [7:0] KB_out;
  wire [15:0] i, j, matrix_1_line_0, matrix_1_line_1, matrix_1_line_2, matrix_1_line_3, matrix_1_line_4,
       matrix_1_line_5, matrix_1_line_6, matrix_1_line_7, matrix_1_line_8, matrix_1_line_9, matrix_1_line_10,
       matrix_1_line_11, matrix_1_line_12, matrix_1_line_13, matrix_1_line_14, matrix_1_line_15;
  wire [24:0] lookAt;
  wire [29:0] birth1, birth2, RE_birth1, RE_birth2, RE_save1, RE_save2, save1, save2;

  Multiplexer #(.width(2), .disabled(0), .enable("false")) multiplexer_1 (
    .in0(2'b00), .in1(2'b11), .out(multiplexer_1_out), .sel(pre3));
  Multiplexer #(.width(2), .disabled(0), .enable("false")) multiplexer_2 (
    .in0(multiplexer_1_out), .in1(2'b10), .out(multiplexer_2_out), .sel(pre2));
  Multiplexer #(.width(25), .enable("false")) multiplexer_3 (
    .in0({plus_2_line, plus_1_line, cur_line, minus_1_line, minus_2_line}), .in1(25'h729c0), .out(lookAt),
    .sel(Rules_editor__below___0__or_Standard_rules__1));
  Multiplexer #(.width(30), .enable("false")) multiplexer_4 (
    .in0(RE_birth1), .in1(30'h3fffffe3), .out(birth1), .sel(Rules_editor__below___0__or_Standard_rules__1));
  Multiplexer #(.width(30), .enable("false")) multiplexer_5 (
    .in0(RE_save1), .in1(30'h3ffffc62), .out(save1), .sel(Rules_editor__below___0__or_Standard_rules__1));
  Multiplexer #(.width(30), .enable("false")) multiplexer_6 (
    .in0(RE_birth2), .in1({30{1'b1}}), .out(birth2), .sel(Rules_editor__below___0__or_Standard_rules__1));
  Multiplexer #(.width(30), .enable("false")) multiplexer_7 (
    .in0(RE_save2), .in1({30{1'b1}}), .out(save2), .sel(Rules_editor__below___0__or_Standard_rules__1));
  Multiplexer #(.width(2), .disabled(0), .enable("false")) multiplexer_8 (
    .in0(multiplexer_2_out), .in1(2'b01), .out(preset), .sel(pre1));
  // Probe on {5{1'b0}}
  // Probe on 5'b01110
  // Probe on 5'b01010
  // Probe on 5'b01110
  // Probe on {5{1'b0}}
  BS_helper bs_helper_1 (.input_6_bit(num_1), .output_5_bit(RE_birth1[4:0]));
  BS_helper_0__31 bs_helper_0_31_1 (.input_6_bit(num_2), .output_5_bit(RE_birth1[9:5]));
  BS_helper_0__31 bs_helper_0_31_2 (.input_6_bit(num_3), .output_5_bit(RE_birth1[14:10]));
  BS_helper_0__31 bs_helper_0_31_3 (.input_6_bit(num_4), .output_5_bit(RE_birth1[19:15]));
  BS_helper_0__31 bs_helper_0_31_4 (.input_6_bit(num_5), .output_5_bit(RE_birth1[24:20]));
  BS_helper_0__31 bs_helper_0_31_5 (.input_6_bit(num_6), .output_5_bit(RE_birth1[29:25]));
  BS_helper_0__31 bs_helper_0_31_6 (.input_6_bit(num_7), .output_5_bit(RE_birth2[4:0]));
  BS_helper_0__31 bs_helper_0_31_7 (.input_6_bit(num_8), .output_5_bit(RE_birth2[9:5]));
  BS_helper_0__31 bs_helper_0_31_8 (.input_6_bit(num_9), .output_5_bit(RE_birth2[14:10]));
  BS_helper_0__31 bs_helper_0_31_9 (.input_6_bit(num_10), .output_5_bit(RE_birth2[19:15]));
  BS_helper_0__31 bs_helper_0_31_10 (.input_6_bit(num_11), .output_5_bit(RE_birth2[24:20]));
  BS_helper_0__31 bs_helper_0_31_11 (.input_6_bit(num_12), .output_5_bit(RE_birth2[29:25]));
  insteadOfCDM8 insteadofcdm8_1 (
    .clock(clock), .KeyBoard(KB_out), .i__row(i), .j__column(j), .torus(sT), .state(insteadofcdm8_1_state),
    .pause(sP), .clear(insteadofcdm8_1_clear), .enable(insteadofcdm8_1_enable), .KB_lamp(tunnel));
  Clock clock_1 (.out(clock));
  // Probe on RE_birth1[4:0]
  // Probe on RE_birth1[9:5]
  // Probe on RE_birth1[14:10]
  // Probe on RE_birth1[19:15]
  // Probe on RE_birth1[24:20]
  // Probe on RE_birth1[29:25]
  // Probe on RE_birth2[4:0]
  // Probe on RE_birth2[9:5]
  // Probe on RE_birth2[14:10]
  // Probe on RE_birth2[19:15]
  // Probe on RE_birth2[24:20]
  // Probe on RE_birth2[29:25]
  // Probe on 5'b00011
  // Probe on {5{1'b1}}
  // Probe on {5{1'b1}}
  // Probe on {5{1'b1}}
  // Probe on {5{1'b1}}
  // Probe on {5{1'b1}}
  // Probe on {5{1'b1}}
  // Probe on {5{1'b1}}
  // Probe on {5{1'b1}}
  // Probe on {5{1'b1}}
  // Probe on {5{1'b1}}
  // Probe on {5{1'b1}}
  DotMatrix #(.inputtype("row"), .matrixcols(16), .matrixrows(1)) dotmatrix_1 (.row0(j));
  DotMatrix #(.inputtype("row"), .matrixcols(16), .matrixrows(16)) dotmatrix_2 (
    .row0(matrix_1_line_15), .row1(matrix_1_line_14), .row2(matrix_1_line_13), .row3(matrix_1_line_12),
    .row4(matrix_1_line_11), .row5(matrix_1_line_10), .row6(matrix_1_line_9), .row7(matrix_1_line_8),
    .row8(matrix_1_line_7), .row9(matrix_1_line_6), .row10(matrix_1_line_5), .row11(matrix_1_line_4),
    .row12(matrix_1_line_3), .row13(matrix_1_line_2), .row14(matrix_1_line_1), .row15(matrix_1_line_0));
  matrix matrix_1 (
    .i(i), .J(j), .Torus(sT), .input_state(insteadofcdm8_1_state), .LINE_0(matrix_1_line_0),
    .LINE_1(matrix_1_line_1), .LINE_2(matrix_1_line_2), .LINE_3(matrix_1_line_3), .LINE_4(matrix_1_line_4),
    .LINE_5(matrix_1_line_5), .LINE_6(matrix_1_line_6), .LINE_7(matrix_1_line_7), .LINE_8(matrix_1_line_8),
    .LINE_9(matrix_1_line_9), .LINE_10(matrix_1_line_10), .LINE_11(matrix_1_line_11),
    .LINE_12(matrix_1_line_12), .LINE_13(matrix_1_line_13), .LINE_14(matrix_1_line_14),
    .LINE_15(matrix_1_line_15), .clock(clock), .pause(sP), .lookAt(lookAt), .birth1(birth1), .save1(save1),
    .birth2(birth2), .save2(save2), .clear(insteadofcdm8_1_clear), .enable(insteadofcdm8_1_enable),
    .random(random), .whatPreset(preset));
  Button u_tor (.out(tor));
  LED led_1 (.in(sT));
  Button u_pre2 (.out(pre2));
  Button u_pre1 (.out(pre1));
  DotMatrix #(.inputtype("row"), .matrixcols(1), .matrixrows(16)) dotmatrix_3 (
    .row0(i[15]), .row1(i[14]), .row2(i[13]), .row3(i[12]), .row4(i[11]), .row5(i[10]), .row6(i[9]),
    .row7(i[8]), .row8(i[7]), .row9(i[6]), .row10(i[5]), .row11(i[4]), .row12(i[3]), .row13(i[2]),
    .row14(i[1]), .row15(i[0]));
  Button u_inv (.out(inv));
  Button u__1 (.out(_1));
  Button u__0 (.out(_0));
  Button u_clear (.out(clear));
  Button u_pre3 (.out(pre3));
  // Probe on RE_save1[4:0]
  BS_helper bs_helper_2 (.input_6_bit(num_1_2), .output_5_bit(RE_save1[4:0]));
  BS_helper_0__31 bs_helper_0_31_12 (.input_6_bit(num_2_2), .output_5_bit(RE_save1[9:5]));
  // Probe on RE_save1[9:5]
  // Probe on RE_save1[14:10]
  BS_helper_0__31 bs_helper_0_31_13 (.input_6_bit(num_3_2), .output_5_bit(RE_save1[14:10]));
  BS_helper_0__31 bs_helper_0_31_14 (.input_6_bit(num_4_2), .output_5_bit(RE_save1[19:15]));
  // Probe on RE_save1[19:15]
  // Probe on RE_save1[24:20]
  BS_helper_0__31 bs_helper_0_31_15 (.input_6_bit(num_5_2), .output_5_bit(RE_save1[24:20]));
  // Probe on RE_save1[29:25]
  BS_helper_0__31 bs_helper_0_31_16 (.input_6_bit(num_6_2), .output_5_bit(RE_save1[29:25]));
  BS_helper_0__31 bs_helper_0_31_17 (.input_6_bit(num_7_2), .output_5_bit(RE_save2[4:0]));
  // Probe on RE_save2[4:0]
  BS_helper_0__31 bs_helper_0_31_18 (.input_6_bit(num_8_2), .output_5_bit(RE_save2[9:5]));
  // Probe on RE_save2[9:5]
  BS_helper_0__31 bs_helper_0_31_19 (.input_6_bit(num_9_2), .output_5_bit(RE_save2[14:10]));
  // Probe on RE_save2[14:10]
  BS_helper_0__31 bs_helper_0_31_20 (.input_6_bit(num_10_2), .output_5_bit(RE_save2[19:15]));
  // Probe on RE_save2[19:15]
  BS_helper_0__31 bs_helper_0_31_21 (.input_6_bit(num_11_2), .output_5_bit(RE_save2[24:20]));
  // Probe on RE_save2[24:20]
  BS_helper_0__31 bs_helper_0_31_22 (.input_6_bit(num_12_2), .output_5_bit(RE_save2[29:25]));
  // Probe on RE_save2[29:25]
  // Probe on 5'b00010
  // Probe on 5'b00011
  // Probe on {5{1'b1}}
  // Probe on {5{1'b1}}
  // Probe on {5{1'b1}}
  // Probe on {5{1'b1}}
  // Probe on {5{1'b1}}
  // Probe on {5{1'b1}}
  // Probe on {5{1'b1}}
  // Probe on {5{1'b1}}
  // Probe on {5{1'b1}}
  // Probe on {5{1'b1}}
  Button rnd (.out(random));
  Button button (.out(L));
  Button space (.out(pause));
  LED led_2 (.in(sP));
  LED led_3 (.in(tunnel));
  Button button_2 (.out(U));
  Button button_3 (.out(R));
  Button button_4 (.out(D));
  // Probe on KB_out
  KeyBoard keyboard_1 (
    .LEFT(L), .DOWN(D), .RIGHT(R), .UP(U), ._1(_1), ._0(_0), .SPACE(pause), .out(KB_out), .CLEAR(clear),
    .INVERT(inv), .torus(tor));
  LED led_4 (.in(U));
  LED led_5 (.in(R));
  LED led_6 (.in(L));
  LED led_7 (.in(D));
  // Probe on KB_out

  // Other names for the same wires on the sheet: RE_lookAt[24:0] = {plus_2_line, plus_1_line, cur_line, minus_1_line, minus_2_line}

  // Notes on the sheet:
  //   Standard rules:
  //   0. Neighbors are nearby cells (like a king in chess)
  //   I. 3 neighbours — cell can be born
  //   II. 2 or 3 neighbours — cell continues to live
  //   III. Otherwise, the cell dies
  //   look at
  //   presets
  //   standard look at
  //   see look at
  //   birth
  //   standard birth
  //   Set up rules
  //   Standard rules
  //   inv, set 0 and set 1 work if pause set!
  //   KeyBoard
  //   save
  //   standard save
endmodule
