// Logisim project 023.main (add loadBar, ROM with code, delete unused schemes, add presets and random in main scheme, etc).circ as structural Verilog
module main (
  input  Rules_editor__below___0__or_Standard_rules__1,
  input  [4:0] minus_2_line,
  input  [5:0] num_1,
  input  [5:0] num_1_2,
  input  [4:0] minus_1_line,
  input  [5:0] num_2,
  input  [5:0] num_2_2,
  input  [4:0] cur_line,
  input  [5:0] num_3,
  input  [5:0] num_3_2,
  input  [4:0] plus_1_line,
  input  [5:0] num_4,
  input  [5:0] num_4_2,
  input  [4:0] plus_2_line,
  input  [5:0] num_5,
  input  [5:0] num_5_2,
  input  [5:0] num_6,
  input  [5:0] num_6_2,
  input  [5:0] num_7,
  input  [5:0] num_7_2,
  input  [5:0] num_8,
  input  [5:0] num_8_2,
  input  [5:0] num_9,
  input  [5:0] num_9_2,
  input  [5:0] num_10,
  input  [5:0] num_10_2,
  input  [5:0] num_11,
  input  [5:0] num_11_2,
  input  [5:0] num_12,
  input  [5:0] num_12_2
);

  wire _0, _1, cdm8_1_clear, cdm8_1_enable, clear, clock, D, inv, L, loadDone, pause, pre1, pre2, pre3, R,
       random, sP, sT, text_1_out_2, text_1_out_3, text_1_out_4, text_1_out_5, text_1_out_6, text_1_out_7,
       text_1_out_8, text_1_out_9, text_1_out_10, text_1_out_11, text_1_out_12, text_1_out_13, text_1_out_14,
       text_1_out_15, text_1_out_16, text_1_out_17, text_1_out_18, text_1_out_19, text_1_out_20,
       text_1_out_21, text_1_out_22, text_1_out_23, text_1_out_24, text_1_out_25, text_1_out_26,
       text_1_out_27, text_1_out_28, text_1_out_29, text_1_out_30, text_1_out_31, text_1_out_32,
       text_1_out_33, text_1_out_34, text_1_out_35, text_1_out_36, text_1_out_37, text_1_out_38,
       text_1_out_39, text_1_out_40, text_1_out_41, text_1_out_42, text_1_out_43, text_1_out_44,
       text_1_out_45, text_1_out_46, text_1_out_47, text_1_out_48, text_1_out_49, text_1_out_50,
       text_1_out_51, text_1_out_52, text_1_out_53, text_1_out_54, text_1_out_55, text_1_out_56,
       text_1_out_57, text_1_out_58, text_1_out_59, text_1_out_60, text_1_out_61, text_1_out_62,
       text_1_out_63, text_1_out_64, text_1_out_65, tor, tunnel, U;
  wire [1:0] cdm8_1_state, multiplexer_1_out, multiplexer_2_out, preset;
  wire [7:0] KB_out;
  wire [15:0] i, j, loadBar, matrix_1_line_0, matrix_1_line_1, matrix_1_line_2, matrix_1_line_3,
       matrix_1_line_4, matrix_1_line_5, matrix_1_line_6, matrix_1_line_7, matrix_1_line_8, matrix_1_line_9,
       matrix_1_line_10, matrix_1_line_11, matrix_1_line_12, matrix_1_line_13, matrix_1_line_14,
       matrix_1_line_15;
  wire [24:0] lookAt;
  wire [29:0] birth1, birth2, RE_birth1, RE_birth2, RE_save1, RE_save2, save1, save2;

  Multiplexer #(.width(2), .disabled(0), .enable("false")) multiplexer_1 (
    .in0(2'b00), .in1(2'b11), .out(multiplexer_1_out), .sel(pre3));
  Multiplexer #(.width(2), .disabled(0), .enable("false")) multiplexer_2 (
    .in0(multiplexer_1_out), .in1(2'b10), .out(multiplexer_2_out), .sel(pre2));
  Multiplexer #(.width(25), .enable("false")) multiplexer_3 (
    .in0({plus_2_line, plus_1_line, cur_line, minus_1_line, minus_2_line}), .in1(25'h729c0), .out(lookAt),
    .sel(Rules_editor__below___0__or_Standard_rules__1));
  Multiplexer #(.width(30), .enable("false")) multiplexer_4 (
    .in0(RE_birth1), .in1(30'h3fffffe3), .out(birth1), .sel(Rules_editor__below___0__or_Standard_rules__1));
  Multiplexer #(.width(30), .enable("false")) multiplexer_5 (
    .in0(RE_save1), .in1(30'h3ffffc62), .out(save1), .sel(Rules_editor__below___0__or_Standard_rules__1));
  Multiplexer #(.width(30), .enable("false")) multiplexer_6 (
    .in0(RE_birth2), .in1({30{1'b1}}), .out(birth2), .sel(Rules_editor__below___0__or_Standard_rules__1));
  Multiplexer #(.width(30), .enable("false")) multiplexer_7 (
    .in0(RE_save2), .in1({30{1'b1}}), .out(save2), .sel(Rules_editor__below___0__or_Standard_rules__1));
  Multiplexer #(.width(2), .disabled(0), .enable("false")) multiplexer_8 (
    .in0(multiplexer_2_out), .in1(2'b01), .out(preset), .sel(pre1));
  BS_helper bs_helper_1 (.input_6_bit(num_1), .output_5_bit(RE_birth1[4:0]));
  BS_helper_0__31 bs_helper_0_31_1 (.input_6_bit(num_2), .output_5_bit(RE_birth1[9:5]));
  BS_helper_0__31 bs_helper_0_31_2 (.input_6_bit(num_3), .output_5_bit(RE_birth1[14:10]));
  BS_helper_0__31 bs_helper_0_31_3 (.input_6_bit(num_4), .output_5_bit(RE_birth1[19:15]));
  BS_helper_0__31 bs_helper_0_31_4 (.input_6_bit(num_5), .output_5_bit(RE_birth1[24:20]));
  BS_helper_0__31 bs_helper_0_31_5 (.input_6_bit(num_6), .output_5_bit(RE_birth1[29:25]));
  BS_helper_0__31 bs_helper_0_31_6 (.input_6_bit(num_7), .output_5_bit(RE_birth2[4:0]));
  BS_helper_0__31 bs_helper_0_31_7 (.input_6_bit(num_8), .output_5_bit(RE_birth2[9:5]));
  BS_helper_0__31 bs_helper_0_31_8 (.input_6_bit(num_9), .output_5_bit(RE_birth2[14:10]));
  BS_helper_0__31 bs_helper_0_31_9 (.input_6_bit(num_10), .output_5_bit(RE_birth2[19:15]));
  BS_helper_0__31 bs_helper_0_31_10 (.input_6_bit(num_11), .output_5_bit(RE_birth2[24:20]));
  BS_helper_0__31 bs_helper_0_31_11 (.input_6_bit(num_12), .output_5_bit(RE_birth2[29:25]));
  Clock clock_1 (.out(clock));
  // Probe on RE_birth1[4:0]
  // Probe on RE_birth1[9:5]
  // Probe on RE_birth1[14:10]
  // Probe on RE_birth1[19:15]
  // Probe on RE_birth1[24:20]
  // Probe on RE_birth1[29:25]
  // Probe on RE_birth2[4:0]
  // Probe on RE_birth2[9:5]
  // Probe on RE_birth2[14:10]
  // Probe on RE_birth2[19:15]
  // Probe on RE_birth2[24:20]
  // Probe on RE_birth2[29:25]
  // Probe on 5'b00011
  // Probe on {5{1'b1}}
  // Probe on {5{1'b1}}
  // Probe on {5{1'b1}}
  // Probe on {5{1'b1}}
  // Probe on {5{1'b1}}
  // Probe on {5{1'b1}}
  // Probe on {5{1'b1}}
  // Probe on {5{1'b1}}
  // Probe on {5{1'b1}}
  // Probe on {5{1'b1}}
  // Probe on {5{1'b1}}
  _7_Segment_Display u_7_segment_display_1 (
    .g(text_1_out_20), .f(text_1_out_4), .a(text_1_out_21), .b(text_1_out_5), .e(text_1_out_52),
    .d(text_1_out_36), .c(text_1_out_53), .dp(text_1_out_37));
  _7_Segment_Display u_7_segment_display_2 (
    .g(text_1_out_18), .f(text_1_out_2), .a(text_1_out_19), .b(text_1_out_3), .e(text_1_out_50),
    .d(text_1_out_34), .c(text_1_out_51), .dp(text_1_out_35));
  DotMatrix #(.inputtype("row"), .matrixcols(16), .matrixrows(1)) dotmatrix_1 (.row0(loadBar));
  DotMatrix #(.inputtype("row"), .matrixcols(16), .matrixrows(1)) dotmatrix_2 (.row0(j));
  matrix matrix_1 (
    .clock(clock), .i(i), .LINE_15(matrix_1_line_15), .J(j), .LINE_14(matrix_1_line_14), .Torus(sT),
    .input_state(cdm8_1_state), .pause(sP), .LINE_13(matrix_1_line_13), .clear(cdm8_1_clear),
    .enable(cdm8_1_enable), .random(random), .LINE_12(matrix_1_line_12), .lookAt(lookAt), .birth1(birth1),
    .LINE_11(matrix_1_line_11), .save1(save1), .LINE_10(matrix_1_line_10), .birth2(birth2), .save2(save2),
    .LINE_9(matrix_1_line_9), .whatPreset(preset), .LINE_8(matrix_1_line_8), .LINE_7(matrix_1_line_7),
    .LINE_6(matrix_1_line_6), .LINE_5(matrix_1_line_5), .LINE_4(matrix_1_line_4), .LINE_3(matrix_1_line_3),
    .LINE_2(matrix_1_line_2), .LINE_1(matrix_1_line_1), .LINE_0(matrix_1_line_0));
  DotMatrix #(.inputtype("row"), .matrixcols(16), .matrixrows(16)) dotmatrix_3 (
    .row0(matrix_1_line_15), .row1(matrix_1_line_14), .row2(matrix_1_line_13), .row3(matrix_1_line_12),
    .row4(matrix_1_line_11), .row5(matrix_1_line_10), .row6(matrix_1_line_9), .row7(matrix_1_line_8),
    .row8(matrix_1_line_7), .row9(matrix_1_line_6), .row10(matrix_1_line_5), .row11(matrix_1_line_4),
    .row12(matrix_1_line_3), .row13(matrix_1_line_2), .row14(matrix_1_line_1), .row15(matrix_1_line_0));
  CDM8 cdm8_1 (
    .clock(clock), .KeyBoard(KB_out), .i__row(i), .j__column(j), .torus(sT), .state(cdm8_1_state),
    .pause(sP), .clear(cdm8_1_clear), .enable(cdm8_1_enable), .KB_lamp(tunnel), .loadDone(loadDone),
    .loadBar(loadBar));
  _7_Segment_Display u_7_segment_display_3 (
    .g(text_1_out_22), .f(text_1_out_6), .a(text_1_out_23), .b(text_1_out_7), .e(text_1_out_54),
    .d(text_1_out_38), .c(text_1_out_55), .dp(text_1_out_39));
  _7_Segment_Display u_7_segment_display_4 (
    .g(text_1_out_24), .f(text_1_out_8), .a(text_1_out_25), .b(text_1_out_9), .e(text_1_out_56),
    .d(text_1_out_40), .c(text_1_out_57), .dp(text_1_out_41));
  LED led_1 (.in(sT));
  Button u_pre1 (.out(pre1));
  _7_Segment_Display u_7_segment_display_5 (
    .g(text_1_out_28), .f(text_1_out_12), .a(text_1_out_29), .b(text_1_out_13), .e(text_1_out_60),
    .d(text_1_out_44), .c(text_1_out_61), .dp(text_1_out_45));
  _7_Segment_Display u_7_segment_display_6 (
    .g(text_1_out_26), .f(text_1_out_10), .a(text_1_out_27), .b(text_1_out_11), .e(text_1_out_58),
    .d(text_1_out_42), .c(text_1_out_59), .dp(text_1_out_43));
  Button u_inv (.out(inv));
  Button u_tor (.out(tor));
  Button u_clear (.out(clear));
  Button u_pre2 (.out(pre2));
  Button u_pre3 (.out(pre3));
  BS_helper bs_helper_2 (.input_6_bit(num_1_2), .output_5_bit(RE_save1[4:0]));
  // Probe on RE_save1[4:0]
  // Probe on RE_save1[9:5]
  BS_helper_0__31 bs_helper_0_31_12 (.input_6_bit(num_2_2), .output_5_bit(RE_save1[9:5]));
  // Probe on RE_save1[14:10]
  BS_helper_0__31 bs_helper_0_31_13 (.input_6_bit(num_3_2), .output_5_bit(RE_save1[14:10]));
  // Probe on RE_save1[19:15]
  BS_helper_0__31 bs_helper_0_31_14 (.input_6_bit(num_4_2), .output_5_bit(RE_save1[19:15]));
  // Probe on RE_save1[24:20]
  BS_helper_0__31 bs_helper_0_31_15 (.input_6_bit(num_5_2), .output_5_bit(RE_save1[24:20]));
  // Probe on RE_save1[29:25]
  BS_helper_0__31 bs_helper_0_31_16 (.input_6_bit(num_6_2), .output_5_bit(RE_save1[29:25]));
  // Probe on RE_save2[4:0]
  BS_helper_0__31 bs_helper_0_31_17 (.input_6_bit(num_7_2), .output_5_bit(RE_save2[4:0]));
  BS_helper_0__31 bs_helper_0_31_18 (.input_6_bit(num_8_2), .output_5_bit(RE_save2[9:5]));
  // Probe on RE_save2[9:5]
  // Probe on RE_save2[14:10]
  BS_helper_0__31 bs_helper_0_31_19 (.input_6_bit(num_9_2), .output_5_bit(RE_save2[14:10]));
  // Probe on RE_save2[19:15]
  BS_helper_0__31 bs_helper_0_31_20 (.input_6_bit(num_10_2), .output_5_bit(RE_save2[19:15]));
  BS_helper_0__31 bs_helper_0_31_21 (.input_6_bit(num_11_2), .output_5_bit(RE_save2[24:20]));
  // Probe on RE_save2[24:20]
  // Probe on RE_save2[29:25]
  BS_helper_0__31 bs_helper_0_31_22 (.input_6_bit(num_12_2), .output_5_bit(RE_save2[29:25]));
  // Probe on 5'b00010
  // Probe on 5'b00011
  // Probe on {5{1'b1}}
  // Probe on {5{1'b1}}
  // Probe on {5{1'b1}}
  // Probe on {5{1'b1}}
  // Probe on {5{1'b1}}
  // Probe on {5{1'b1}}
  // Probe on {5{1'b1}}
  // Probe on {5{1'b1}}
  // Probe on {5{1'b1}}
  // Probe on {5{1'b1}}
  _7_Segment_Display u_7_segment_display_7 (
    .g(text_1_out_30), .f(text_1_out_14), .a(text_1_out_31), .b(text_1_out_15), .e(text_1_out_62),
    .d(text_1_out_46), .c(text_1_out_63), .dp(text_1_out_47));
  _7_Segment_Display u_7_segment_display_8 (
    .g(text_1_out_32), .f(text_1_out_16), .a(text_1_out_33), .b(text_1_out_17), .e(text_1_out_64),
    .d(text_1_out_48), .c(text_1_out_65), .dp(text_1_out_49));
  DotMatrix #(.inputtype("row"), .matrixcols(1), .matrixrows(16)) dotmatrix_4 (
    .row0(i[15]), .row1(i[14]), .row2(i[13]), .row3(i[12]), .row4(i[11]), .row5(i[10]), .row6(i[9]),
    .row7(i[8]), .row8(i[7]), .row9(i[6]), .row10(i[5]), .row11(i[4]), .row12(i[3]), .row13(i[2]),
    .row14(i[1]), .row15(i[0]));
  Button u__1 (.out(_1));
  Button u__0 (.out(_0));
  Button rnd (.out(random));
  LED led_2 (.in(sP));
  Button space (.out(pause));
  text text_1 (
    .in_1(loadDone), .out_18(text_1_out_18), .out_2(text_1_out_2), .out_19(text_1_out_19),
    .out_3(text_1_out_3), .out_20(text_1_out_20), .out_4(text_1_out_4), .out_21(text_1_out_21),
    .out_5(text_1_out_5), .out_22(text_1_out_22), .out_6(text_1_out_6), .out_23(text_1_out_23),
    .out_7(text_1_out_7), .out_24(text_1_out_24), .out_8(text_1_out_8), .out_25(text_1_out_25),
    .out_9(text_1_out_9), .out_26(text_1_out_26), .out_10(text_1_out_10), .out_27(text_1_out_27),
    .out_11(text_1_out_11), .out_28(text_1_out_28), .out_12(text_1_out_12), .out_29(text_1_out_29),
    .out_13(text_1_out_13), .out_30(text_1_out_30), .out_14(text_1_out_14), .out_31(text_1_out_31),
    .out_15(text_1_out_15), .out_50(text_1_out_50), .out_34(text_1_out_34), .out_51(text_1_out_51),
    .out_35(text_1_out_35), .out_52(text_1_out_52), .out_36(text_1_out_36), .out_53(text_1_out_53),
    .out_37(text_1_out_37), .out_54(text_1_out_54), .out_38(text_1_out_38), .out_55(text_1_out_55),
    .out_39(text_1_out_39), .out_56(text_1_out_56), .out_40(text_1_out_40), .out_57(text_1_out_57),
    .out_41(text_1_out_41), .out_58(text_1_out_58), .out_42(text_1_out_42), .out_59(text_1_out_59),
    .out_43(text_1_out_43), .out_60(text_1_out_60), .out_44(text_1_out_44), .out_61(text_1_out_61),
    .out_45(text_1_out_45), .out_62(text_1_out_62), .out_46(text_1_out_46), .out_63(text_1_out_63),
    .out_47(text_1_out_47), .out_16(text_1_out_16), .out_17(text_1_out_17), .out_32(text_1_out_32),
    .out_33(text_1_out_33), .out_48(text_1_out_48), .out_49(text_1_out_49), .out_64(text_1_out_64),
    .out_65(text_1_out_65));
  LED led_3 (.in(tunnel));
  Button button (.out(U));
  Button button_2 (.out(R));
  Button button_3 (.out(L));
  Button button_4 (.out(D));
  LED led_4 (.in(U));
  LED led_5 (.in(L));
  LED led_6 (.in(D));
  // Probe on KB_out
  KeyBoard keyboard_1 (
    .LEFT(L), .DOWN(D), .RIGHT(R), .UP(U), ._1(_1), ._0(_0), .SPACE(pause), .out(KB_out), .CLEAR(clear),
    .INVERT(inv), .torus(tor));
  LED led_7 (.in(R));

  // Other names for the same wires on the sheet: RE_lookAt[24:0] = {plus_2_line, plus_1_line, cur_line, minus_1_line, minus_2_line}

  // Notes on the sheet:
  //   Standard rules:
  //   I. 3 neighbours — cell can be born
  //   II. 2 or 3 neighbours — cell continues to live
  //   III. Otherwise, the cell dies
  //   look at
  //   presets
  //   look at
  //   0. Neighbors are nearby cells (like a king in chess)
  //   birth
  //   birth
  //   Set up rules
  //   Standard rules
  //   save
  //   save
  //   KeyBoard
  //   random by Logisim
endmodule

module CDM8 (
  input  clock,
  input  [7:0] KeyBoard,
  output KB_lamp,
  output [15:0] i__row,
  output [15:0] j__column,
  output torus,
  output [1:0] state,
  output pause,
  output clear,
  output enable,
  output [15:0] loadBar,
  output loadDone
);

  wire _0xFD, _0xFF, adr____0xF8_2_out, adr____0xF8_out, adr____0xFA_out, adr____0xFC_out, adr____0xFE_out,
       and_1_out, and_2_out, and_6_out, and_7_out, and_8_out, and_9_out, and_10_out, and_11_out,
       comparator_3_eq, load_1_Done, mem, noRAM, not_1_out, not_2_out, not_3_out, not_4_out, not_5_out,
       not_6_out, or_1_out, or_2_out, RAM, read;
  wire [6:5] state_t;
  wire [7:0] addressBus, cdm_8_1_data_out, cdm_8_1_pc, cdm_8_1_ps, cdm_8_1_r0, cdm_8_1_r1, cdm_8_1_r2,
       cdm_8_1_r3, cdm_8_1_sp, controlled_buffer_1_out, controlled_buffer_3_out, counter_2_q, counter_3_q,
       dataBus, loadAddress, loadData, multiplexer_1_out, RAMDataBus;
  wire [15:0] j, toRegi, toRegj;

  // Probe on cdm_8_1_r0
  // Probe on cdm_8_1_r3
  // Probe on cdm_8_1_r1
  // Probe on cdm_8_1_r2
  and and_1 (and_1_out, load_1_Done, clock);
  reverse16Bits reverse16bits_1 (.in(j), .out(j__column));
  // Probe on cdm_8_1_sp
  // Probe on cdm_8_1_pc
  CdM_8 cdm_8_1 (
    .R0(cdm_8_1_r0), .R1(cdm_8_1_r1), .mem(mem), .R2(cdm_8_1_r2), .load_st_prime(read), .R3(cdm_8_1_r3),
    .addr(addressBus), .PC(cdm_8_1_pc), .SP(cdm_8_1_sp), .data_out(cdm_8_1_data_out),
    .data_in(controlled_buffer_1_out), .PS(cdm_8_1_ps), .clk(and_1_out));  // open: data_code_prime, page, IAck, IRQ, vector, shadow
  assign controlled_buffer_1_out = read ? dataBus : 8'bz;  // Controlled_Buffer controlled_buffer_1
  // Probe on cdm_8_1_ps
  assign dataBus = not_1_out ? cdm_8_1_data_out : 8'bz;  // Controlled_Buffer controlled_buffer_2
  not not_1 (not_1_out, read);
  // Probe on dataBus
  // Probe on addressBus
  Multiplexer #(.width(8), .enable("false")) multiplexer_1 (
    .in0(loadAddress), .in1(addressBus), .out(multiplexer_1_out), .sel(load_1_Done));
  and and_2 (and_2_out, load_1_Done, read);
  and adr____0xF8 (adr____0xF8_out, addressBus[3], addressBus[4], addressBus[5], addressBus[6], addressBus[7]);
  not not_2 (not_2_out, load_1_Done);
  assign controlled_buffer_3_out = not_2_out ? loadData : 8'bz;  // Controlled_Buffer controlled_buffer_3
  RAM ram_1 (
    .addr(multiplexer_1_out), .data(controlled_buffer_3_out), .sel(RAM), .clk(clock), .ld(and_2_out));  // open: clr
  and and_3 (RAM, mem, ~adr____0xF8_out);  // AND_Gate
  and and_4 (noRAM, adr____0xF8_out, mem);
  and and_5 (KB_lamp, mem, adr____0xF8_2_out);
  and adr____0xF8_2 (adr____0xF8_2_out, ~addressBus[0], ~addressBus[1], ~addressBus[2], noRAM);  // AND_Gate
  and adr____0xFA (adr____0xFA_out, ~addressBus[0], addressBus[1], ~addressBus[2], noRAM);  // AND_Gate
  and adr____0xFC (adr____0xFC_out, ~addressBus[0], ~addressBus[1], addressBus[2], noRAM);  // AND_Gate
  and adr____0xFD (_0xFD, addressBus[0], ~addressBus[1], noRAM);  // AND_Gate
  and adr____0xFE (adr____0xFE_out, ~addressBus[0], addressBus[1], addressBus[2], noRAM);  // AND_Gate
  and adr____0xFF (_0xFF, addressBus[0], addressBus[1], addressBus[2], noRAM);
  assign RAMDataBus = and_6_out ? controlled_buffer_3_out : 8'bz;  // Controlled_Buffer controlled_buffer_4
  and and_6 (and_6_out, load_1_Done, read);
  assign controlled_buffer_3_out = and_7_out ? dataBus : 8'bz;  // Controlled_Buffer controlled_buffer_5
  and and_7 (and_7_out, ~read, load_1_Done);  // AND_Gate
  and and_8 (and_8_out, adr____0xFA_out, ~read);  // AND_Gate
  or or_1 (or_1_out, adr____0xFC_out, _0xFD);
  and and_9 (and_9_out, or_1_out, ~read);  // AND_Gate
  or or_2 (or_2_out, adr____0xFE_out, _0xFF);
  and and_10 (and_10_out, or_2_out, ~read);  // AND_Gate
  Multiplexer #(.width(8)) multiplexer_2 (
    .in0(RAMDataBus), .in1(KeyBoard), .out(dataBus), .sel(adr____0xF8_2_out), .en(read));
  Register register_1 (
    .D(dataBus), .en(and_8_out), .Q({enable, state_t, clear, pause, state, torus}), .clk(clock));  // open: clr
  Register #(.width(16)) register_2 (.D(toRegi), .en(and_9_out), .Q(i__row), .clk(clock));  // open: clr
  Register #(.width(16), .trigger("falling")) register_3 (
    .D(toRegj), .en(and_10_out), .Q(j), .clk(clock));  // open: clr
  // Probe on dataBus
  // Probe on dataBus
  not not_3 (not_3_out, load_1_Done);
  // Probe on toRegi
  Multiplexer #(.width(16), .enable("false")) multiplexer_3 (
    .in0({dataBus, i__row[7:0]}), .in1({i__row[15:8], dataBus}), .out(toRegi), .sel(_0xFD));
  // Probe on toRegj
  Multiplexer #(.width(16), .enable("false")) multiplexer_4 (
    .in0({dataBus, j[7:0]}), .in1({j[15:8], dataBus}), .out(toRegj), .sel(_0xFF));
  ROM rom_1 (.addr(loadAddress), .data(loadData), .sel(not_3_out));
  Counter #(.max('hee), .ongoal("stay"), .trigger("falling")) counter_1 (
    .count(not_4_out), .Q(loadAddress), .clk(clock));  // open: load, D, carry, clr
  not not_4 (not_4_out, load_1_Done);
  Counter #(.max('h1f), .ongoal("stay"), .trigger("falling")) counter_2 (
    .count(and_11_out), .Q(counter_2_q), .clk(clock));  // open: load, D, carry, clr
  and and_11 (and_11_out, ~loadDone, load_1_Done);  // AND_Gate
  Counter #(.max('hf), .trigger("falling")) counter_3 (
    .count(not_5_out), .Q(counter_3_q), .clk(clock));  // open: load, D, carry, clr
  not not_5 (not_5_out, loadDone);
  not not_6 (not_6_out, not_6_out);
  Comparator #(.mode("unsigned")) comparator_1 (.a(loadAddress), .b(8'hee), .eq(load_1_Done));  // open: gt, lt
  Comparator #(.mode("unsigned")) comparator_2 (.a(counter_2_q), .b(8'h1f), .eq(loadDone));  // open: gt, lt
  Comparator comparator_3 (.a(counter_3_q), .b(8'hf), .eq(comparator_3_eq));  // open: gt, lt
  Register #(.width(16)) register_4 (
    .D({1'b1, loadBar[15:1]}), .en(1'b1), .Q(loadBar), .clk(comparator_3_eq));  // open: clr

  // Other names for the same wires on the sheet: i[15:0] = i__row; KB_out[7:0] = KeyBoard;
  //   state_t (some bits) = {enable, clear, pause, state, torus}

  // Notes on the sheet:
  //   input
  //   output
  //   CDM8 + memory
  //   store KeyBoard's data to CPU
  //   if the "read" option is disabled (↑), plexer won't work
  //   load STATE (from CPU)
  //   load i-cursor (need x2 operations)
  //   load j-cursor (need x2 operations)
  //   load i-cursor (high part) from CPU
  //   load i-cursor (low part) from CPU
  //   load j-cursor (high part) from CPU
  //   load j-cursor (low part) from CPU
  //   The game code
  //   progress bar counters
  //   while (code copying)
  //   while (init game)
  //   while (game is loading)
  //   copying or init
  //   contents of rom_1 (hex, n*v repeats v):
  //   cd f0 d1 0 d2 1 d0 fc a1 8c a2 d3 f5 ae 8c a1 8c a2 d3 f7 ae d0 fa d1 8 a1 d0 f2 a1 3f e1 ad d2 f8
  //   b9 5 e0 ab d3 f2 bc d2 7f 42 ae d0 fa a2 d0 f 74 e8 6d e1 41 bd d0 1 61 ad d3 fa ad ee 6b d0 4 74 eb
  //   58 e1 50 d0 f6 d1 ff d6 ae ee 56 d0 f4 d1 fd d6 ae ee 6b d0 2 74 e1 65 d0 f5 d1 fc d6 c4 ee 6b d0 f7
  //   d1 fe d6 c4 ee a1 d0 40 74 e3 8a e1 80 d0 f2 b0 d1 10 51 d3 fa ad ac ee 88 bc d1 8 64 ac d1 fa a4 ee
  //   a1 d0 20 74 eb 9d e1 97 d3 4 d6 e0 ee 9b d3 6 d6 e0 ee a1 d3 2 d6 e0 d0 f2 b3 d1 80 5d a1 d0 fa a1
  //   ee 1d d4 b3 f e5 b3 d7 8c b2 7e e9 bb 97 ee bd 96 2f a2 88 a3 a6 89 a7 d7 b2 d3 1 7b e1 cb d7 88 b3
  //   7e e9 d8 7b 93 e1 d6 d2 80 ee d9 92 a3 8c a2 a7 8d a6 d7 d2 f2 b8 d1 f9 41 5d d2 fa a9 a8 d7
  //   copying is done
  //   init is done
  //   (game loaded)
endmodule

module KeyBoard (
  input  LEFT,
  input  DOWN,
  input  torus,
  input  RIGHT,
  input  UP,
  input  _1,
  input  INVERT,
  input  _0,
  input  CLEAR,
  input  SPACE,
  output [7:0] out
);

  wire [2:0] or_5_out;
  wire [3:0] arrows, or_1_out;

  or or_1 (or_1_out[0], LEFT, torus);
  or or_2 (or_1_out[1], DOWN, torus);
  or or_3 (or_1_out[2], RIGHT, torus);
  or or_4 (or_1_out[3], UP, torus);
  Multiplexer #(.select(4), .width(4)) multiplexer_1 (
    .in0(4'b0000), .in1(4'b0001), .in2(4'b0010), .in3(4'b0010), .in4(4'b0100), .in5(4'b0100), .in6(4'b0100),
    .in7(4'b0100), .in8(4'b1000), .in9(4'b1000), .in10(4'b1000), .in11(4'b1000), .in12(4'b1000),
    .in13(4'b1000), .in14(4'b1000), .in15(4'b1111), .out(arrows), .sel(or_1_out));  // open: en
  or or_5 (or_5_out[0], arrows[0], arrows[1], arrows[2], arrows[3]);
  // Probe on 2'b11
  or or_6 (or_5_out[1], _1, INVERT);
  or or_7 (or_5_out[2], INVERT, _0);
  // Probe on 2'b10
  // Probe on or_5_out[0]
  // Probe on 2'b01
  // Probe on 2'b00
  Multiplexer #(.select(5), .width(8)) multiplexer_2 (
    .in0({8{1'b0}}), .in1({4'b0000, arrows}), .in2(8'h30), .in3(8'h30), .in4(8'h20), .in5(8'h20),
    .in6(8'h10), .in7(8'h10), .in8(8'h40), .in9(8'h40), .in10(8'h40), .in11(8'h40), .in12(8'h40),
    .in13(8'h40), .in14(8'h40), .in15(8'h40), .in16(8'h80), .in17(8'h80), .in18(8'h80), .in19(8'h80),
    .in20(8'h80), .in21(8'h80), .in22(8'h80), .in23(8'h80), .in24(8'h80), .in25(8'h80), .in26(8'h80),
    .in27(8'h80), .in28(8'h80), .in29(8'h80), .in30(8'h80), .in31(8'h80), .out(out),
    .sel({SPACE, CLEAR, or_5_out}));  // open: en
  // Probe on 2'b00

  // Notes on the sheet:
  //   1 (set alive)
  //   state = 11
  //   0 (set dead)
  //   state = 10
  //   invert cell
  //   state = 01
  //   clear field
  //   state = 00
  //   space (pause)
  //   state = 00
endmodule

module matrix (
  input  clock,
  input  [15:0] i,
  input  [15:0] J,
  input  Torus,
  input  [1:0] input_state,
  input  pause,
  input  clear,
  input  enable,
  input  random,
  input  [24:0] lookAt,
  input  [29:0] birth1,
  input  [29:0] save1,
  input  [29:0] birth2,
  input  [29:0] save2,
  input  [1:0] whatPreset,
  output [15:0] LINE_15,
  output [15:0] LINE_14,
  output [15:0] LINE_13,
  output [15:0] LINE_12,
  output [15:0] LINE_11,
  output [15:0] LINE_10,
  output [15:0] LINE_9,
  output [15:0] LINE_8,
  output [15:0] LINE_7,
  output [15:0] LINE_6,
  output [15:0] LINE_5,
  output [15:0] LINE_4,
  output [15:0] LINE_3,
  output [15:0] LINE_2,
  output [15:0] LINE_1,
  output [15:0] LINE_0
);

  wire loadPreset;
  wire [15:0] and_1_out, and_2_out, and_3_out, and_4_out, and_5_out, and_6_out, line_1__0_line__out__1_2,
       line_1__0_line__out__2_2, line_2__0_line__out__1, line_2__0_line__out__1_2, line_2__0_line__out__2_2,
       line_3__0_line__out__1, line_3__0_line__out__1_2, line_3__0_line__out__2, line_3__0_line__out__2_2,
       line_4__0_line__out__1, line_4__0_line__out__1_2, line_4__0_line__out__2, line_4__0_line__out__2_2,
       line_5__0_line__out__1, line_5__0_line__out__1_2, line_5__0_line__out__2, line_5__0_line__out__2_2,
       line_6__0_line__out__1, line_6__0_line__out__1_2, line_6__0_line__out__2, line_6__0_line__out__2_2,
       line_7__0_line__out__1, line_7__0_line__out__1_2, line_7__0_line__out__2, line_7__0_line__out__2_2,
       line_8__0_line__out__1, line_8__0_line__out__1_2, line_8__0_line__out__2, line_8__0_line__out__2_2,
       line_9__0_line__out__1, line_9__0_line__out__1_2, line_9__0_line__out__2, line_9__0_line__out__2_2,
       line_10__0_line__out__1, line_10__0_line__out__1_2, line_10__0_line__out__2,
       line_10__0_line__out__2_2, line_11__0_line__out__1, line_11__0_line__out__1_2,
       line_11__0_line__out__2, line_11__0_line__out__2_2, line_12__0_line__out__1,
       line_12__0_line__out__1_2, line_12__0_line__out__2, line_12__0_line__out__2_2,
       line_13__0_line__out__1, line_13__0_line__out__1_2, line_13__0_line__out__2,
       line_13__0_line__out__2_2, line_14__0_line__out__1, line_14__0_line__out__1_2,
       line_14__0_line__out__2, line_14__0_line__out__2_2, line_15__0_line__out__1,
       line_15__0_line__out__1_2, line_15__0_line__out__2, line_16__0_line__out__1, minus_01, minus_01_star,
       minus_02, plus_16, plus_16_star, plus_17, presetLine0, presetLine1, presetLine2, presetLine3,
       presetLine4, presetLine5, presetLine6, presetLine7, presetLine8, presetLine9, presetLineA,
       presetLineB, presetLineC, presetLineD, presetLineE, presetLineF;

  Pull_Resistor pull_resistor_1 (.node(input_state[1]));
  Pull_Resistor pull_resistor_2 (.node(Torus));
  Pull_Resistor pull_resistor_3 (.node(input_state[0]));
  Pull_Resistor #(.pull(1)) pull_resistor_4 (.node(pause));
  Pull_Resistor pull_resistor_5 (.node(clear));
  Pull_Resistor #(.pull(1)) pull_resistor_6 (.node(enable));
  Pull_Resistor pull_resistor_7 (.node(random));
  Multiplexer #(.select(2), .width(16), .enable("false")) multiplexer_1 (
    .in0({16{1'b0}}), .in1({16{1'b0}}), .in2(16'hc0), .in3(16'hfe7f), .out(presetLine0), .sel(whatPreset));
  Multiplexer #(.select(2), .width(16), .enable("false")) multiplexer_2 (
    .in0({16{1'b0}}), .in1(16'h6db6), .in2(16'h2c0), .in3(16'ha245), .out(presetLine1), .sel(whatPreset));
  Multiplexer #(.select(2), .width(16), .enable("false")) multiplexer_3 (
    .in0({16{1'b0}}), .in1(16'h7ffe), .in2(16'h7c0), .in3(16'he667), .out(presetLine2), .sel(whatPreset));
  Multiplexer #(.select(2), .width(16), .enable("false")) multiplexer_4 (
    .in0({16{1'b0}}), .in1(16'h2004), .in2(16'hdc0), .in3(16'h8c31), .out(presetLine3), .sel(whatPreset));
  Multiplexer #(.select(2), .width(16), .enable("false")) multiplexer_5 (
    .in0({16{1'b0}}), .in1(16'h2004), .in2(16'h18c0), .in3(16'h9819), .out(presetLine4), .sel(whatPreset));
  Multiplexer #(.select(2), .width(16), .enable("false")) multiplexer_6 (
    .in0({16{1'b0}}), .in1(16'h2664), .in2(16'h3060), .in3(16'hb00d), .out(presetLine5), .sel(whatPreset));
  Multiplexer #(.select(2), .width(16), .enable("false")) multiplexer_7 (
    .in0({16{1'b0}}), .in1(16'h2664), .in2(16'h3fe0), .in3(16'he007), .out(presetLine6), .sel(whatPreset));
  Multiplexer #(.select(2), .width(16), .enable("false")) multiplexer_8 (
    .in0({16{1'b0}}), .in1(16'h2004), .in2(16'h2020), .in3({16{1'b0}}), .out(presetLine7), .sel(whatPreset));
  Multiplexer #(.select(2), .width(16), .enable("false")) multiplexer_9 (
    .in0({16{1'b0}}), .in1(16'h2004), .in2(16'h2fa0), .in3({16{1'b0}}), .out(presetLine8), .sel(whatPreset));
  Multiplexer #(.select(2), .width(16), .enable("false")) multiplexer_10 (
    .in0({16{1'b0}}), .in1(16'h2604), .in2(16'h2aa0), .in3(16'he007), .out(presetLine9), .sel(whatPreset));
  Multiplexer #(.select(2), .width(16), .enable("false")) multiplexer_11 (
    .in0({16{1'b0}}), .in1(16'h27e4), .in2(16'h2fbc), .in3(16'hb00d), .out(presetLineA), .sel(whatPreset));
  Multiplexer #(.select(2), .width(16), .enable("false")) multiplexer_12 (
    .in0({16{1'b0}}), .in1(16'h23c4), .in2(16'h2aa4), .in3(16'h9819), .out(presetLineB), .sel(whatPreset));
  Multiplexer #(.select(2), .width(16), .enable("false")) multiplexer_13 (
    .in0({16{1'b0}}), .in1(16'h2004), .in2(16'h2fac), .in3(16'h8c31), .out(presetLineC), .sel(whatPreset));
  Multiplexer #(.select(2), .width(16), .enable("false")) multiplexer_14 (
    .in0({16{1'b0}}), .in1(16'h3ffc), .in2(16'h2024), .in3(16'he667), .out(presetLineD), .sel(whatPreset));
  Multiplexer #(.select(2), .width(16), .enable("false")) multiplexer_15 (
    .in0({16{1'b0}}), .in1({16{1'b0}}), .in2(16'h3ffc), .in3(16'ha245), .out(presetLineE), .sel(whatPreset));
  Multiplexer #(.select(2), .width(16), .enable("false")) multiplexer_16 (
    .in0({16{1'b0}}), .in1({16{1'b0}}), .in2({16{1'b0}}), .in3(16'hfe7f), .out(presetLineF), .sel(whatPreset));
  or or_1 (loadPreset, whatPreset[0], whatPreset[1]);
  assign and_1_out = plus_17 & {16{Torus}};  // AND_Gate and_1, 16 bits wide
  assign and_2_out = plus_16 & {16{Torus}};  // AND_Gate and_2, 16 bits wide
  assign and_3_out = minus_02 & {16{Torus}};  // AND_Gate and_3, 16 bits wide
  assign and_4_out = {16{Torus}} & minus_01;  // AND_Gate and_4, 16 bits wide
  assign and_5_out = plus_16_star & {16{Torus}};  // AND_Gate and_5, 16 bits wide
  assign and_6_out = {16{Torus}} & minus_01_star;  // AND_Gate and_6, 16 bits wide
  line u_line_1 (
    ._0_line__out__2(minus_02), .J(J), .minus_2_line(and_1_out), .minus_1_line(and_5_out),
    ._1_line(line_2__0_line__out__1), ._2_line(line_3__0_line__out__2), ._0_line__out__1(minus_01_star),
    .display(LINE_15), ._0_line__out__1_2(line_1__0_line__out__1_2),
    ._0_line__out__2_2(line_1__0_line__out__2_2), .I(i[15]), .Torus(Torus), .input_state(input_state),
    .clock(clock), .pause(pause), .clear(clear), .enable(enable), .random(random), .lookAt(lookAt),
    .birth1(birth1), .save1(save1), .birth2(birth2), .save2(save2), .preset(presetLine0),
    .loadPreset(loadPreset));
  line u_line_2 (
    ._0_line__out__2(minus_01), .J(J), .minus_2_line(and_2_out), .minus_1_line(line_1__0_line__out__1_2),
    ._1_line(line_3__0_line__out__1), ._2_line(line_4__0_line__out__2),
    ._0_line__out__1(line_2__0_line__out__1), .display(LINE_14),
    ._0_line__out__1_2(line_2__0_line__out__1_2), ._0_line__out__2_2(line_2__0_line__out__2_2), .I(i[14]),
    .Torus(Torus), .input_state(input_state), .clock(clock), .pause(pause), .clear(clear), .enable(enable),
    .random(random), .lookAt(lookAt), .birth1(birth1), .save1(save1), .birth2(birth2), .save2(save2),
    .preset(presetLine1), .loadPreset(loadPreset));
  line u_line_3 (
    ._0_line__out__2(line_3__0_line__out__2), .J(J), .minus_2_line(line_1__0_line__out__2_2),
    .minus_1_line(line_2__0_line__out__1_2), ._1_line(line_4__0_line__out__1),
    ._2_line(line_5__0_line__out__2), ._0_line__out__1(line_3__0_line__out__1), .display(LINE_13),
    ._0_line__out__1_2(line_3__0_line__out__1_2), ._0_line__out__2_2(line_3__0_line__out__2_2), .I(i[13]),
    .Torus(Torus), .input_state(input_state), .clock(clock), .pause(pause), .clear(clear), .enable(enable),
    .random(random), .lookAt(lookAt), .birth1(birth1), .save1(save1), .birth2(birth2), .save2(save2),
    .preset(presetLine2), .loadPreset(loadPreset));
  line u_line_4 (
    ._0_line__out__2(line_4__0_line__out__2), .J(J), .minus_2_line(line_2__0_line__out__2_2),
    .minus_1_line(line_3__0_line__out__1_2), ._1_line(line_5__0_line__out__1),
    ._2_line(line_6__0_line__out__2), ._0_line__out__1(line_4__0_line__out__1), .display(LINE_12),
    ._0_line__out__1_2(line_4__0_line__out__1_2), ._0_line__out__2_2(line_4__0_line__out__2_2), .I(i[12]),
    .Torus(Torus), .input_state(input_state), .clock(clock), .pause(pause), .clear(clear), .enable(enable),
    .random(random), .lookAt(lookAt), .birth1(birth1), .save1(save1), .birth2(birth2), .save2(save2),
    .preset(presetLine3), .loadPreset(loadPreset));
  line u_line_5 (
    ._0_line__out__2(line_5__0_line__out__2), .J(J), .minus_2_line(line_3__0_line__out__2_2),
    .minus_1_line(line_4__0_line__out__1_2), ._1_line(line_6__0_line__out__1),
    ._2_line(line_7__0_line__out__2), ._0_line__out__1(line_5__0_line__out__1), .display(LINE_11),
    ._0_line__out__1_2(line_5__0_line__out__1_2), ._0_line__out__2_2(line_5__0_line__out__2_2), .I(i[11]),
    .Torus(Torus), .input_state(input_state), .clock(clock), .pause(pause), .clear(clear), .enable(enable),
    .random(random), .lookAt(lookAt), .birth1(birth1), .save1(save1), .birth2(birth2), .save2(save2),
    .preset(presetLine4), .loadPreset(loadPreset));
  line u_line_6 (
    ._0_line__out__2(line_6__0_line__out__2), .J(J), .minus_2_line(line_4__0_line__out__2_2),
    .minus_1_line(line_5__0_line__out__1_2), ._1_line(line_7__0_line__out__1),
    ._2_line(line_8__0_line__out__2), ._0_line__out__1(line_6__0_line__out__1), .display(LINE_10),
    ._0_line__out__1_2(line_6__0_line__out__1_2), ._0_line__out__2_2(line_6__0_line__out__2_2), .I(i[10]),
    .Torus(Torus), .input_state(input_state), .clock(clock), .pause(pause), .clear(clear), .enable(enable),
    .random(random), .lookAt(lookAt), .birth1(birth1), .save1(save1), .birth2(birth2), .save2(save2),
    .preset(presetLine5), .loadPreset(loadPreset));
  line u_line_7 (
    ._0_line__out__2(line_7__0_line__out__2), .J(J), .minus_2_line(line_5__0_line__out__2_2),
    .minus_1_line(line_6__0_line__out__1_2), ._1_line(line_8__0_line__out__1),
    ._2_line(line_9__0_line__out__2), ._0_line__out__1(line_7__0_line__out__1), .display(LINE_9),
    ._0_line__out__1_2(line_7__0_line__out__1_2), ._0_line__out__2_2(line_7__0_line__out__2_2), .I(i[9]),
    .Torus(Torus), .input_state(input_state), .clock(clock), .pause(pause), .clear(clear), .enable(enable),
    .random(random), .lookAt(lookAt), .birth1(birth1), .save1(save1), .birth2(birth2), .save2(save2),
    .preset(presetLine6), .loadPreset(loadPreset));
  line u_line_8 (
    ._0_line__out__2(line_8__0_line__out__2), .J(J), .minus_2_line(line_6__0_line__out__2_2),
    .minus_1_line(line_7__0_line__out__1_2), ._1_line(line_9__0_line__out__1),
    ._2_line(line_10__0_line__out__2), ._0_line__out__1(line_8__0_line__out__1), .display(LINE_8),
    ._0_line__out__1_2(line_8__0_line__out__1_2), ._0_line__out__2_2(line_8__0_line__out__2_2), .I(i[8]),
    .Torus(Torus), .input_state(input_state), .clock(clock), .pause(pause), .clear(clear), .enable(enable),
    .random(random), .lookAt(lookAt), .birth1(birth1), .save1(save1), .birth2(birth2), .save2(save2),
    .preset(presetLine7), .loadPreset(loadPreset));
  line u_line_9 (
    ._0_line__out__2(line_9__0_line__out__2), .J(J), .minus_2_line(line_7__0_line__out__2_2),
    .minus_1_line(line_8__0_line__out__1_2), ._1_line(line_10__0_line__out__1),
    ._2_line(line_11__0_line__out__2), ._0_line__out__1(line_9__0_line__out__1), .display(LINE_7),
    ._0_line__out__1_2(line_9__0_line__out__1_2), ._0_line__out__2_2(line_9__0_line__out__2_2), .I(i[7]),
    .Torus(Torus), .input_state(input_state), .clock(clock), .pause(pause), .clear(clear), .enable(enable),
    .random(random), .lookAt(lookAt), .birth1(birth1), .save1(save1), .birth2(birth2), .save2(save2),
    .preset(presetLine8), .loadPreset(loadPreset));
  line u_line_10 (
    ._0_line__out__2(line_10__0_line__out__2), .J(J), .minus_2_line(line_8__0_line__out__2_2),
    .minus_1_line(line_9__0_line__out__1_2), ._1_line(line_11__0_line__out__1),
    ._2_line(line_12__0_line__out__2), ._0_line__out__1(line_10__0_line__out__1), .display(LINE_6),
    ._0_line__out__1_2(line_10__0_line__out__1_2), ._0_line__out__2_2(line_10__0_line__out__2_2), .I(i[6]),
    .Torus(Torus), .input_state(input_state), .clock(clock), .pause(pause), .clear(clear), .enable(enable),
    .random(random), .lookAt(lookAt), .birth1(birth1), .save1(save1), .birth2(birth2), .save2(save2),
    .preset(presetLine9), .loadPreset(loadPreset));
  line u_line_11 (
    ._0_line__out__2(line_11__0_line__out__2), .J(J), .minus_2_line(line_9__0_line__out__2_2),
    .minus_1_line(line_10__0_line__out__1_2), ._1_line(line_12__0_line__out__1),
    ._2_line(line_13__0_line__out__2), ._0_line__out__1(line_11__0_line__out__1), .display(LINE_5),
    ._0_line__out__1_2(line_11__0_line__out__1_2), ._0_line__out__2_2(line_11__0_line__out__2_2), .I(i[5]),
    .Torus(Torus), .input_state(input_state), .clock(clock), .pause(pause), .clear(clear), .enable(enable),
    .random(random), .lookAt(lookAt), .birth1(birth1), .save1(save1), .birth2(birth2), .save2(save2),
    .preset(presetLineA), .loadPreset(loadPreset));
  line u_line_12 (
    ._0_line__out__2(line_12__0_line__out__2), .J(J), .minus_2_line(line_10__0_line__out__2_2),
    .minus_1_line(line_11__0_line__out__1_2), ._1_line(line_13__0_line__out__1),
    ._2_line(line_14__0_line__out__2), ._0_line__out__1(line_12__0_line__out__1), .display(LINE_4),
    ._0_line__out__1_2(line_12__0_line__out__1_2), ._0_line__out__2_2(line_12__0_line__out__2_2), .I(i[4]),
    .Torus(Torus), .input_state(input_state), .clock(clock), .pause(pause), .clear(clear), .enable(enable),
    .random(random), .lookAt(lookAt), .birth1(birth1), .save1(save1), .birth2(birth2), .save2(save2),
    .preset(presetLineB), .loadPreset(loadPreset));
  line u_line_13 (
    ._0_line__out__2(line_13__0_line__out__2), .J(J), .minus_2_line(line_11__0_line__out__2_2),
    .minus_1_line(line_12__0_line__out__1_2), ._1_line(line_14__0_line__out__1),
    ._2_line(line_15__0_line__out__2), ._0_line__out__1(line_13__0_line__out__1), .display(LINE_3),
    ._0_line__out__1_2(line_13__0_line__out__1_2), ._0_line__out__2_2(line_13__0_line__out__2_2), .I(i[3]),
    .Torus(Torus), .input_state(input_state), .clock(clock), .pause(pause), .clear(clear), .enable(enable),
    .random(random), .lookAt(lookAt), .birth1(birth1), .save1(save1), .birth2(birth2), .save2(save2),
    .preset(presetLineC), .loadPreset(loadPreset));
  line u_line_14 (
    ._0_line__out__2(line_14__0_line__out__2), .J(J), .minus_2_line(line_12__0_line__out__2_2),
    .minus_1_line(line_13__0_line__out__1_2), ._1_line(line_15__0_line__out__1),
    ._0_line__out__1(line_14__0_line__out__1), .display(LINE_2),
    ._0_line__out__1_2(line_14__0_line__out__1_2), ._0_line__out__2_2(line_14__0_line__out__2_2), .I(i[2]),
    .Torus(Torus), .input_state(input_state), .clock(clock), .pause(pause), .clear(clear), .enable(enable),
    .random(random), .lookAt(lookAt), .birth1(birth1), .save1(save1), .birth2(birth2), .save2(save2),
    .preset(presetLineD), .loadPreset(loadPreset));  // open: _2_line
  line u_line_15 (
    ._0_line__out__2(line_15__0_line__out__2), .J(J), .minus_2_line(line_13__0_line__out__2_2),
    .minus_1_line(line_14__0_line__out__1_2), ._1_line(line_16__0_line__out__1), ._2_line(and_4_out),
    ._0_line__out__1(line_15__0_line__out__1), .display(LINE_1),
    ._0_line__out__1_2(line_15__0_line__out__1_2), ._0_line__out__2_2(plus_16), .I(i[1]), .Torus(Torus),
    .input_state(input_state), .clock(clock), .pause(pause), .clear(clear), .enable(enable), .random(random),
    .lookAt(lookAt), .birth1(birth1), .save1(save1), .birth2(birth2), .save2(save2), .preset(presetLineE),
    .loadPreset(loadPreset));
  line line_16 (
    .J(J), .minus_2_line(line_14__0_line__out__2_2), .minus_1_line(line_15__0_line__out__1_2),
    ._1_line(and_6_out), ._2_line(and_3_out), ._0_line__out__1(line_16__0_line__out__1), .display(LINE_0),
    ._0_line__out__1_2(plus_16_star), ._0_line__out__2_2(plus_17), .I(i[0]), .Torus(Torus),
    .input_state(input_state), .clock(clock), .pause(pause), .clear(clear), .enable(enable), .random(random),
    .lookAt(lookAt), .birth1(birth1), .save1(save1), .birth2(birth2), .save2(save2), .preset(presetLineF),
    .loadPreset(loadPreset));  // open: _0_line__out__2

  // Other names for the same wires on the sheet: B1[29:0] = birth1; B2[29:0] = birth2; S1[29:0] = save1;
  //   S2[29:0] = save2; state[1:0] = input_state; torus16[15:0] = {16{Torus}}

  // Notes on the sheet:
  //   birth1: pull=down
  //   lookAt: pull=down
  //   LINE_6: pull=down
  //   save2: pull=down
  //   LINE_5: pull=down
  //   LINE_1: pull=down
  //   LINE_8: pull=down
  //   LINE_15: pull=down
  //   LINE_11: pull=down
  //   LINE_4: pull=down
  //   birth2: pull=down
  //   LINE_13: pull=down
  //   LINE_12: pull=down
  //   LINE_7: pull=down
  //   LINE_9: pull=down
  //   LINE_2: pull=down
  //   LINE_0: pull=down
  //   LINE_14: pull=down
  //   LINE_10: pull=down
  //   LINE_3: pull=down
  //   save1: pull=down
  //   preset 1
  //   00 — old
  //   01 — invert
  //   10 — set DEAD
  //   11 — set ALIVE
endmodule

module line (
  input  [15:0] J,
  input  [15:0] minus_2_line,
  input  [15:0] minus_1_line,
  input  [15:0] _1_line,
  input  [15:0] _2_line,
  input  I,
  input  Torus,
  input  [1:0] input_state,
  input  clock,
  input  pause,
  input  clear,
  input  enable,
  input  random,
  input  [24:0] lookAt,
  input  [29:0] birth1,
  input  [29:0] save1,
  input  [29:0] birth2,
  input  [29:0] save2,
  input  [15:0] preset,
  input  loadPreset,
  output [15:0] _0_line__out__2,
  output [15:0] _0_line__out__1,
  output [15:0] display,
  output [15:0] _0_line__out__1_2,
  output [15:0] _0_line__out__2_2
);

  wire minus_01_01_t, minus_01_02_t, minus_01_16, minus_01_17, minus_02_01_t, minus_02_02_t, minus_02_16,
       minus_02_17, or_1_out, plus_00_00new, plus_00_01_t, plus_00_01new, plus_00_02_t, plus_00_02new,
       plus_00_03new, plus_00_04new, plus_00_05new, plus_00_06new, plus_00_07new, plus_00_08new,
       plus_00_09new, plus_00_10new, plus_00_11new, plus_00_12new, plus_00_13new, plus_00_14new,
       plus_00_15new, plus_00_16, plus_00_17, plus_01_01_t, plus_01_02_t, plus_01_16, plus_01_17,
       plus_02_01_t, plus_02_02_t, plus_02_16, plus_02_17;
  wire [1:0] state_helper_1_output_state, state_helper_2_output_state, state_helper_3_output_state,
       state_helper_4_output_state, state_helper_5_output_state, state_helper_6_output_state,
       state_helper_7_output_state, state_helper_8_output_state, state_helper_9_output_state,
       state_helper_10_output_state, state_helper_11_output_state, state_helper_12_output_state,
       state_helper_13_output_state, state_helper_14_output_state, state_helper_15_output_state,
       state_helper_16_output_state;
  wire [15:0] multiplexer_1_out, multiplexer_2_out, random_1_out;
  wire [24:0] neighbours_1_neighbours, neighbours_2_neighbours, neighbours_3_neighbours,
       neighbours_4_neighbours, neighbours_5_neighbours, neighbours_6_neighbours, neighbours_7_neighbours,
       neighbours_8_neighbours, neighbours_9_neighbours, neighbours_10_neighbours, neighbours_11_neighbours,
       neighbours_12_neighbours, neighbours_13_neighbours, neighbours_14_neighbours,
       neighbours_15_neighbours, neighbours_16_neighbours;

  Pull_Resistor pull_resistor_1 (.node(preset[10]));
  Pull_Resistor pull_resistor_2 (.node(preset[12]));
  Pull_Resistor pull_resistor_3 (.node(preset[14]));
  Pull_Resistor pull_resistor_4 (.node(preset[13]));
  Pull_Resistor pull_resistor_5 (.node(preset[11]));
  Pull_Resistor pull_resistor_6 (.node(preset[15]));
  Pull_Resistor pull_resistor_7 (.node(preset[2]));
  Pull_Resistor pull_resistor_8 (.node(preset[7]));
  Pull_Resistor pull_resistor_9 (.node(preset[9]));
  Pull_Resistor pull_resistor_10 (.node(preset[5]));
  Pull_Resistor pull_resistor_11 (.node(preset[3]));
  Pull_Resistor pull_resistor_12 (.node(preset[4]));
  Pull_Resistor pull_resistor_13 (.node(preset[8]));
  Pull_Resistor pull_resistor_14 (.node(preset[6]));
  Pull_Resistor pull_resistor_15 (.node(preset[1]));
  Pull_Resistor pull_resistor_16 (.node(preset[0]));
  neighbours neighbours_1 (
    .minus_02_02(minus_02_02_t), .minus_02_01(minus_02_01_t), .minus_02_00(minus_2_line[0]),
    .minus_02_01_2(minus_2_line[1]), .minus_02_02_2(minus_2_line[2]), .minus_01_02(minus_01_02_t),
    .minus_01_01(minus_01_01_t), .minus_01_00(minus_1_line[0]), .minus_01_01_2(minus_1_line[1]),
    .minus_01_02_2(minus_1_line[2]), .plus_00_02(plus_00_02_t), .plus_00_01(plus_00_01_t),
    .plus_00_00(_0_line__out__1[0]), .neighbours(neighbours_1_neighbours), .plus_00_01_2(_0_line__out__1[1]),
    .plus_00_02_2(_0_line__out__1[2]), .plus_01_02(plus_01_02_t), .plus_01_01(plus_01_01_t),
    .plus_01_00(_1_line[0]), .plus_01_01_2(_1_line[1]), .plus_01_02_2(_1_line[2]), .plus_02_02(plus_02_02_t),
    .plus_02_01(plus_02_01_t), .plus_02_00(_2_line[0]), .plus_02_01_2(_2_line[1]), .plus_02_02_2(_2_line[2]));
  Random #(.width(16)) random_1 (.clk(clock), .next(random), .out(random_1_out));  // open: clr
  and and_1 (minus_02_16, minus_2_line[0], Torus);
  and and_2 (minus_02_17, minus_2_line[1], Torus);
  and and_3 (minus_02_01_t, minus_2_line[15], Torus);
  and and_4 (minus_02_02_t, minus_2_line[14], Torus);
  alive alive_1 (
    .neighbours(neighbours_1_neighbours), .look_at(lookAt), .B1___birth(birth1), .S1___save(save1),
    .alive(plus_00_00new), .pause(pause), .input_state(state_helper_1_output_state));  // open: B2___birth, S2___save
  STATE_helper state_helper_1 (.input_state(input_state), .output_state(state_helper_1_output_state), .i(I), .j(J[0]));
  Multiplexer #(.width(16), .enable("false")) multiplexer_1 (
    .in0({plus_00_15new, plus_00_14new, plus_00_13new, plus_00_12new, plus_00_11new, plus_00_10new, plus_00_09new, plus_00_08new, plus_00_07new, plus_00_06new, plus_00_05new, plus_00_04new, plus_00_03new, plus_00_02new, plus_00_01new, plus_00_00new}),
    .in1(random_1_out), .out(multiplexer_1_out), .sel(random));
  Multiplexer #(.width(16), .enable("false")) multiplexer_2 (
    .in0(multiplexer_1_out), .in1(preset), .out(multiplexer_2_out), .sel(loadPreset));
  or or_1 (or_1_out, pause, enable);
  and and_5 (minus_01_16, minus_1_line[0], Torus);
  and and_6 (minus_01_17, minus_1_line[1], Torus);
  and and_7 (minus_01_01_t, minus_1_line[15], Torus);
  and and_8 (minus_01_02_t, minus_1_line[14], Torus);
  neighbours neighbours_2 (
    .minus_02_02(minus_02_01_t), .minus_02_01(minus_2_line[0]), .minus_02_00(minus_2_line[1]),
    .minus_02_01_2(minus_2_line[2]), .minus_02_02_2(minus_2_line[3]), .minus_01_02(minus_01_01_t),
    .minus_01_01(minus_1_line[0]), .minus_01_00(minus_1_line[1]), .minus_01_01_2(minus_1_line[2]),
    .minus_01_02_2(minus_1_line[3]), .plus_00_02(plus_00_01_t), .plus_00_01(_0_line__out__1[0]),
    .plus_00_00(_0_line__out__1[1]), .neighbours(neighbours_2_neighbours), .plus_00_01_2(_0_line__out__1[2]),
    .plus_00_02_2(_0_line__out__1[3]), .plus_01_02(plus_01_01_t), .plus_01_01(_1_line[0]),
    .plus_01_00(_1_line[1]), .plus_01_01_2(_1_line[2]), .plus_01_02_2(_1_line[3]), .plus_02_02(plus_02_01_t),
    .plus_02_01(_2_line[0]), .plus_02_00(_2_line[1]), .plus_02_01_2(_2_line[2]), .plus_02_02_2(_2_line[3]));
  Register #(.width(16), .trigger("falling")) register_1 (
    .D(multiplexer_2_out), .en(or_1_out), .Q(_0_line__out__1), .clk(clock), .clr(clear));
  alive alive_2 (
    .neighbours(neighbours_2_neighbours), .look_at(lookAt), .B1___birth(birth1), .S1___save(save1),
    .alive(plus_00_01new), .pause(pause), .input_state(state_helper_2_output_state));  // open: B2___birth, S2___save
  STATE_helper state_helper_2 (.input_state(input_state), .output_state(state_helper_2_output_state), .i(I), .j(J[1]));
  and and_9 (plus_01_16, _1_line[0], Torus);
  and and_10 (plus_01_17, _1_line[1], Torus);
  and and_11 (plus_01_01_t, _1_line[15], Torus);
  and and_12 (plus_01_02_t, _1_line[14], Torus);
  and and_13 (plus_02_16, _2_line[0], Torus);
  and and_14 (plus_02_17, _2_line[1], Torus);
  and and_15 (plus_02_01_t, _2_line[15], Torus);
  and and_16 (plus_02_02_t, _2_line[14], Torus);
  neighbours neighbours_3 (
    .minus_02_02(minus_2_line[0]), .minus_02_01(minus_2_line[1]), .minus_02_00(minus_2_line[2]),
    .minus_02_01_2(minus_2_line[3]), .minus_02_02_2(minus_2_line[4]), .minus_01_02(minus_1_line[0]),
    .minus_01_01(minus_1_line[1]), .minus_01_00(minus_1_line[2]), .minus_01_01_2(minus_1_line[3]),
    .minus_01_02_2(minus_1_line[4]), .plus_00_02(_0_line__out__1[0]), .plus_00_01(_0_line__out__1[1]),
    .plus_00_00(_0_line__out__1[2]), .neighbours(neighbours_3_neighbours), .plus_00_01_2(_0_line__out__1[3]),
    .plus_00_02_2(_0_line__out__1[4]), .plus_01_02(_1_line[0]), .plus_01_01(_1_line[1]),
    .plus_01_00(_1_line[2]), .plus_01_01_2(_1_line[3]), .plus_01_02_2(_1_line[4]), .plus_02_02(_2_line[0]),
    .plus_02_01(_2_line[1]), .plus_02_00(_2_line[2]), .plus_02_01_2(_2_line[3]), .plus_02_02_2(_2_line[4]));
  alive alive_3 (
    .neighbours(neighbours_3_neighbours), .look_at(lookAt), .B1___birth(birth1), .S1___save(save1),
    .alive(plus_00_02new), .pause(pause), .input_state(state_helper_3_output_state));  // open: B2___birth, S2___save
  STATE_helper state_helper_3 (.input_state(input_state), .output_state(state_helper_3_output_state), .i(I), .j(J[2]));
  and and_17 (plus_00_16, _0_line__out__1[0], Torus);
  and and_18 (plus_00_17, _0_line__out__1[1], Torus);
  and and_19 (plus_00_01_t, _0_line__out__1[15], Torus);
  and and_20 (plus_00_02_t, _0_line__out__1[14], Torus);
  neighbours neighbours_4 (
    .minus_02_02(minus_2_line[1]), .minus_02_01(minus_2_line[2]), .minus_02_00(minus_2_line[3]),
    .minus_02_01_2(minus_2_line[4]), .minus_02_02_2(minus_2_line[5]), .minus_01_02(minus_1_line[1]),
    .minus_01_01(minus_1_line[2]), .minus_01_00(minus_1_line[3]), .minus_01_01_2(minus_1_line[4]),
    .minus_01_02_2(minus_1_line[5]), .plus_00_02(_0_line__out__1[1]), .plus_00_01(_0_line__out__1[2]),
    .plus_00_00(_0_line__out__1[3]), .neighbours(neighbours_4_neighbours), .plus_00_01_2(_0_line__out__1[4]),
    .plus_00_02_2(_0_line__out__1[5]), .plus_01_02(_1_line[1]), .plus_01_01(_1_line[2]),
    .plus_01_00(_1_line[3]), .plus_01_01_2(_1_line[4]), .plus_01_02_2(_1_line[5]), .plus_02_02(_2_line[1]),
    .plus_02_01(_2_line[2]), .plus_02_00(_2_line[3]), .plus_02_01_2(_2_line[4]), .plus_02_02_2(_2_line[5]));
  alive alive_4 (
    .neighbours(neighbours_4_neighbours), .look_at(lookAt), .B1___birth(birth1), .S1___save(save1),
    .alive(plus_00_03new), .pause(pause), .input_state(state_helper_4_output_state));  // open: B2___birth, S2___save
  STATE_helper state_helper_4 (.input_state(input_state), .output_state(state_helper_4_output_state), .i(I), .j(J[3]));
  neighbours neighbours_5 (
    .minus_02_02(minus_2_line[2]), .minus_02_01(minus_2_line[3]), .minus_02_00(minus_2_line[4]),
    .minus_02_01_2(minus_2_line[5]), .minus_02_02_2(minus_2_line[6]), .minus_01_02(minus_1_line[2]),
    .minus_01_01(minus_1_line[3]), .minus_01_00(minus_1_line[4]), .minus_01_01_2(minus_1_line[5]),
    .minus_01_02_2(minus_1_line[6]), .plus_00_02(_0_line__out__1[2]), .plus_00_01(_0_line__out__1[3]),
    .plus_00_00(_0_line__out__1[4]), .neighbours(neighbours_5_neighbours), .plus_00_01_2(_0_line__out__1[5]),
    .plus_00_02_2(_0_line__out__1[6]), .plus_01_02(_1_line[2]), .plus_01_01(_1_line[3]),
    .plus_01_00(_1_line[4]), .plus_01_01_2(_1_line[5]), .plus_01_02_2(_1_line[6]), .plus_02_02(_2_line[2]),
    .plus_02_01(_2_line[3]), .plus_02_00(_2_line[4]), .plus_02_01_2(_2_line[5]), .plus_02_02_2(_2_line[6]));
  alive alive_5 (
    .neighbours(neighbours_5_neighbours), .look_at(lookAt), .B1___birth(birth1), .S1___save(save1),
    .alive(plus_00_04new), .pause(pause), .input_state(state_helper_5_output_state));  // open: B2___birth, S2___save
  STATE_helper state_helper_5 (.input_state(input_state), .output_state(state_helper_5_output_state), .i(I), .j(J[4]));
  neighbours neighbours_6 (
    .minus_02_02(minus_2_line[3]), .minus_02_01(minus_2_line[4]), .minus_02_00(minus_2_line[5]),
    .minus_02_01_2(minus_2_line[6]), .minus_02_02_2(minus_2_line[7]), .minus_01_02(minus_1_line[3]),
    .minus_01_01(minus_1_line[4]), .minus_01_00(minus_1_line[5]), .minus_01_01_2(minus_1_line[6]),
    .minus_01_02_2(minus_1_line[7]), .plus_00_02(_0_line__out__1[3]), .plus_00_01(_0_line__out__1[4]),
    .plus_00_00(_0_line__out__1[5]), .neighbours(neighbours_6_neighbours), .plus_00_01_2(_0_line__out__1[6]),
    .plus_00_02_2(_0_line__out__1[7]), .plus_01_02(_1_line[3]), .plus_01_01(_1_line[4]),
    .plus_01_00(_1_line[5]), .plus_01_01_2(_1_line[6]), .plus_01_02_2(_1_line[7]), .plus_02_02(_2_line[3]),
    .plus_02_01(_2_line[4]), .plus_02_00(_2_line[5]), .plus_02_01_2(_2_line[6]), .plus_02_02_2(_2_line[7]));
  alive alive_6 (
    .neighbours(neighbours_6_neighbours), .look_at(lookAt), .B1___birth(birth1), .S1___save(save1),
    .alive(plus_00_05new), .pause(pause), .input_state(state_helper_6_output_state));  // open: B2___birth, S2___save
  STATE_helper state_helper_6 (.input_state(input_state), .output_state(state_helper_6_output_state), .i(I), .j(J[5]));
  neighbours neighbours_7 (
    .minus_02_02(minus_2_line[4]), .minus_02_01(minus_2_line[5]), .minus_02_00(minus_2_line[6]),
    .minus_02_01_2(minus_2_line[7]), .minus_02_02_2(minus_2_line[8]), .minus_01_02(minus_1_line[4]),
    .minus_01_01(minus_1_line[5]), .minus_01_00(minus_1_line[6]), .minus_01_01_2(minus_1_line[7]),
    .minus_01_02_2(minus_1_line[8]), .plus_00_02(_0_line__out__1[4]), .plus_00_01(_0_line__out__1[5]),
    .plus_00_00(_0_line__out__1[6]), .neighbours(neighbours_7_neighbours), .plus_00_01_2(_0_line__out__1[7]),
    .plus_00_02_2(_0_line__out__1[8]), .plus_01_02(_1_line[4]), .plus_01_01(_1_line[5]),
    .plus_01_00(_1_line[6]), .plus_01_01_2(_1_line[7]), .plus_01_02_2(_1_line[8]), .plus_02_02(_2_line[4]),
    .plus_02_01(_2_line[5]), .plus_02_00(_2_line[6]), .plus_02_01_2(_2_line[7]), .plus_02_02_2(_2_line[8]));
  alive alive_7 (
    .neighbours(neighbours_7_neighbours), .look_at(lookAt), .B1___birth(birth1), .S1___save(save1),
    .alive(plus_00_06new), .pause(pause), .input_state(state_helper_7_output_state));  // open: B2___birth, S2___save
  STATE_helper state_helper_7 (.input_state(input_state), .output_state(state_helper_7_output_state), .i(I), .j(J[6]));
  neighbours neighbours_8 (
    .minus_02_02(minus_2_line[5]), .minus_02_01(minus_2_line[6]), .minus_02_00(minus_2_line[7]),
    .minus_02_01_2(minus_2_line[8]), .minus_02_02_2(minus_2_line[9]), .minus_01_02(minus_1_line[5]),
    .minus_01_01(minus_1_line[6]), .minus_01_00(minus_1_line[7]), .minus_01_01_2(minus_1_line[8]),
    .minus_01_02_2(minus_1_line[9]), .plus_00_02(_0_line__out__1[5]), .plus_00_01(_0_line__out__1[6]),
    .plus_00_00(_0_line__out__1[7]), .neighbours(neighbours_8_neighbours), .plus_00_01_2(_0_line__out__1[8]),
    .plus_00_02_2(_0_line__out__1[9]), .plus_01_02(_1_line[5]), .plus_01_01(_1_line[6]),
    .plus_01_00(_1_line[7]), .plus_01_01_2(_1_line[8]), .plus_01_02_2(_1_line[9]), .plus_02_02(_2_line[5]),
    .plus_02_01(_2_line[6]), .plus_02_00(_2_line[7]), .plus_02_01_2(_2_line[8]), .plus_02_02_2(_2_line[9]));
  alive alive_8 (
    .neighbours(neighbours_8_neighbours), .look_at(lookAt), .B1___birth(birth1), .S1___save(save1),
    .alive(plus_00_07new), .pause(pause), .input_state(state_helper_8_output_state));  // open: B2___birth, S2___save
  STATE_helper state_helper_8 (.input_state(input_state), .output_state(state_helper_8_output_state), .i(I), .j(J[7]));
  neighbours neighbours_9 (
    .minus_02_02(minus_2_line[6]), .minus_02_01(minus_2_line[7]), .minus_02_00(minus_2_line[8]),
    .minus_02_01_2(minus_2_line[9]), .minus_02_02_2(minus_2_line[10]), .minus_01_02(minus_1_line[6]),
    .minus_01_01(minus_1_line[7]), .minus_01_00(minus_1_line[8]), .minus_01_01_2(minus_1_line[9]),
    .minus_01_02_2(minus_1_line[10]), .plus_00_02(_0_line__out__1[6]), .plus_00_01(_0_line__out__1[7]),
    .plus_00_00(_0_line__out__1[8]), .neighbours(neighbours_9_neighbours), .plus_00_01_2(_0_line__out__1[9]),
    .plus_00_02_2(_0_line__out__1[10]), .plus_01_02(_1_line[6]), .plus_01_01(_1_line[7]),
    .plus_01_00(_1_line[8]), .plus_01_01_2(_1_line[9]), .plus_01_02_2(_1_line[10]), .plus_02_02(_2_line[6]),
    .plus_02_01(_2_line[7]), .plus_02_00(_2_line[8]), .plus_02_01_2(_2_line[9]), .plus_02_02_2(_2_line[10]));
  alive alive_9 (
    .neighbours(neighbours_9_neighbours), .look_at(lookAt), .B1___birth(birth1), .S1___save(save1),
    .alive(plus_00_08new), .pause(pause), .input_state(state_helper_9_output_state));  // open: B2___birth, S2___save
  STATE_helper state_helper_9 (.input_state(input_state), .output_state(state_helper_9_output_state), .i(I), .j(J[8]));
  neighbours neighbours_10 (
    .minus_02_02(minus_2_line[7]), .minus_02_01(minus_2_line[8]), .minus_02_00(minus_2_line[9]),
    .minus_02_01_2(minus_2_line[10]), .minus_02_02_2(minus_2_line[11]), .minus_01_02(minus_1_line[7]),
    .minus_01_01(minus_1_line[8]), .minus_01_00(minus_1_line[9]), .minus_01_01_2(minus_1_line[10]),
    .minus_01_02_2(minus_1_line[11]), .plus_00_02(_0_line__out__1[7]), .plus_00_01(_0_line__out__1[8]),
    .plus_00_00(_0_line__out__1[9]), .neighbours(neighbours_10_neighbours),
    .plus_00_01_2(_0_line__out__1[10]), .plus_00_02_2(_0_line__out__1[11]), .plus_01_02(_1_line[7]),
    .plus_01_01(_1_line[8]), .plus_01_00(_1_line[9]), .plus_01_01_2(_1_line[10]), .plus_01_02_2(_1_line[11]),
    .plus_02_02(_2_line[7]), .plus_02_01(_2_line[8]), .plus_02_00(_2_line[9]), .plus_02_01_2(_2_line[10]),
    .plus_02_02_2(_2_line[11]));
  alive alive_10 (
    .neighbours(neighbours_10_neighbours), .look_at(lookAt), .B1___birth(birth1), .S1___save(save1),
    .alive(plus_00_09new), .pause(pause), .input_state(state_helper_10_output_state));  // open: B2___birth, S2___save
  STATE_helper state_helper_10 (
    .input_state(input_state), .output_state(state_helper_10_output_state), .i(I), .j(J[9]));
  neighbours neighbours_11 (
    .minus_02_02(minus_2_line[8]), .minus_02_01(minus_2_line[9]), .minus_02_00(minus_2_line[10]),
    .minus_02_01_2(minus_2_line[11]), .minus_02_02_2(minus_2_line[12]), .minus_01_02(minus_1_line[8]),
    .minus_01_01(minus_1_line[9]), .minus_01_00(minus_1_line[10]), .minus_01_01_2(minus_1_line[11]),
    .minus_01_02_2(minus_1_line[12]), .plus_00_02(_0_line__out__1[8]), .plus_00_01(_0_line__out__1[9]),
    .plus_00_00(_0_line__out__1[10]), .neighbours(neighbours_11_neighbours),
    .plus_00_01_2(_0_line__out__1[11]), .plus_00_02_2(_0_line__out__1[12]), .plus_01_02(_1_line[8]),
    .plus_01_01(_1_line[9]), .plus_01_00(_1_line[10]), .plus_01_01_2(_1_line[11]),
    .plus_01_02_2(_1_line[12]), .plus_02_02(_2_line[8]), .plus_02_01(_2_line[9]), .plus_02_00(_2_line[10]),
    .plus_02_01_2(_2_line[11]), .plus_02_02_2(_2_line[12]));
  alive alive_11 (
    .neighbours(neighbours_11_neighbours), .look_at(lookAt), .B1___birth(birth1), .S1___save(save1),
    .alive(plus_00_10new), .pause(pause), .input_state(state_helper_11_output_state));  // open: B2___birth, S2___save
  STATE_helper state_helper_11 (
    .input_state(input_state), .output_state(state_helper_11_output_state), .i(I), .j(J[10]));
  neighbours neighbours_12 (
    .minus_02_02(minus_2_line[9]), .minus_02_01(minus_2_line[10]), .minus_02_00(minus_2_line[11]),
    .minus_02_01_2(minus_2_line[12]), .minus_02_02_2(minus_2_line[13]), .minus_01_02(minus_1_line[9]),
    .minus_01_01(minus_1_line[10]), .minus_01_00(minus_1_line[11]), .minus_01_01_2(minus_1_line[12]),
    .minus_01_02_2(minus_1_line[13]), .plus_00_02(_0_line__out__1[9]), .plus_00_01(_0_line__out__1[10]),
    .plus_00_00(_0_line__out__1[11]), .neighbours(neighbours_12_neighbours),
    .plus_00_01_2(_0_line__out__1[12]), .plus_00_02_2(_0_line__out__1[13]), .plus_01_02(_1_line[9]),
    .plus_01_01(_1_line[10]), .plus_01_00(_1_line[11]), .plus_01_01_2(_1_line[12]),
    .plus_01_02_2(_1_line[13]), .plus_02_02(_2_line[9]), .plus_02_01(_2_line[10]), .plus_02_00(_2_line[11]),
    .plus_02_01_2(_2_line[12]), .plus_02_02_2(_2_line[13]));
  alive alive_12 (
    .neighbours(neighbours_12_neighbours), .look_at(lookAt), .B1___birth(birth1), .S1___save(save1),
    .alive(plus_00_11new), .pause(pause), .input_state(state_helper_12_output_state));  // open: B2___birth, S2___save
  STATE_helper state_helper_12 (
    .input_state(input_state), .output_state(state_helper_12_output_state), .i(I), .j(J[11]));
  neighbours neighbours_13 (
    .minus_02_02(minus_2_line[10]), .minus_02_01(minus_2_line[11]), .minus_02_00(minus_2_line[12]),
    .minus_02_01_2(minus_2_line[13]), .minus_02_02_2(minus_2_line[14]), .minus_01_02(minus_1_line[10]),
    .minus_01_01(minus_1_line[11]), .minus_01_00(minus_1_line[12]), .minus_01_01_2(minus_1_line[13]),
    .minus_01_02_2(minus_1_line[14]), .plus_00_02(_0_line__out__1[10]), .plus_00_01(_0_line__out__1[11]),
    .plus_00_00(_0_line__out__1[12]), .neighbours(neighbours_13_neighbours),
    .plus_00_01_2(_0_line__out__1[13]), .plus_00_02_2(_0_line__out__1[14]), .plus_01_02(_1_line[10]),
    .plus_01_01(_1_line[11]), .plus_01_00(_1_line[12]), .plus_01_01_2(_1_line[13]),
    .plus_01_02_2(_1_line[14]), .plus_02_02(_2_line[10]), .plus_02_01(_2_line[11]), .plus_02_00(_2_line[12]),
    .plus_02_01_2(_2_line[13]), .plus_02_02_2(_2_line[14]));
  alive alive_13 (
    .neighbours(neighbours_13_neighbours), .look_at(lookAt), .B1___birth(birth1), .S1___save(save1),
    .alive(plus_00_12new), .pause(pause), .input_state(state_helper_13_output_state));  // open: B2___birth, S2___save
  STATE_helper state_helper_13 (
    .input_state(input_state), .output_state(state_helper_13_output_state), .i(I), .j(J[12]));
  neighbours neighbours_14 (
    .minus_02_02(minus_2_line[11]), .minus_02_01(minus_2_line[12]), .minus_02_00(minus_2_line[13]),
    .minus_02_01_2(minus_2_line[14]), .minus_02_02_2(minus_2_line[15]), .minus_01_02(minus_1_line[11]),
    .minus_01_01(minus_1_line[12]), .minus_01_00(minus_1_line[13]), .minus_01_01_2(minus_1_line[14]),
    .minus_01_02_2(minus_1_line[15]), .plus_00_02(_0_line__out__1[11]), .plus_00_01(_0_line__out__1[12]),
    .plus_00_00(_0_line__out__1[13]), .neighbours(neighbours_14_neighbours),
    .plus_00_01_2(_0_line__out__1[14]), .plus_00_02_2(_0_line__out__1[15]), .plus_01_02(_1_line[11]),
    .plus_01_01(_1_line[12]), .plus_01_00(_1_line[13]), .plus_01_01_2(_1_line[14]),
    .plus_01_02_2(_1_line[15]), .plus_02_02(_2_line[11]), .plus_02_01(_2_line[12]), .plus_02_00(_2_line[13]),
    .plus_02_01_2(_2_line[14]), .plus_02_02_2(_2_line[15]));
  alive alive_14 (
    .neighbours(neighbours_14_neighbours), .look_at(lookAt), .B1___birth(birth1), .S1___save(save1),
    .alive(plus_00_13new), .pause(pause), .input_state(state_helper_14_output_state));  // open: B2___birth, S2___save
  STATE_helper state_helper_14 (
    .input_state(input_state), .output_state(state_helper_14_output_state), .i(I), .j(J[13]));
  neighbours neighbours_15 (
    .minus_02_02(minus_2_line[12]), .minus_02_01(minus_2_line[13]), .minus_02_00(minus_2_line[14]),
    .minus_02_01_2(minus_2_line[15]), .minus_02_02_2(minus_02_16), .minus_01_02(minus_1_line[12]),
    .minus_01_01(minus_1_line[13]), .minus_01_00(minus_1_line[14]), .minus_01_01_2(minus_1_line[15]),
    .minus_01_02_2(minus_01_16), .plus_00_02(_0_line__out__1[12]), .plus_00_01(_0_line__out__1[13]),
    .plus_00_00(_0_line__out__1[14]), .neighbours(neighbours_15_neighbours),
    .plus_00_01_2(_0_line__out__1[15]), .plus_00_02_2(plus_00_16), .plus_01_02(_1_line[12]),
    .plus_01_01(_1_line[13]), .plus_01_00(_1_line[14]), .plus_01_01_2(_1_line[15]),
    .plus_01_02_2(plus_01_16), .plus_02_02(_2_line[12]), .plus_02_01(_2_line[13]), .plus_02_00(_2_line[14]),
    .plus_02_01_2(_2_line[15]), .plus_02_02_2(plus_02_16));
  alive alive_15 (
    .neighbours(neighbours_15_neighbours), .look_at(lookAt), .B1___birth(birth1), .S1___save(save1),
    .alive(plus_00_14new), .pause(pause), .input_state(state_helper_15_output_state));  // open: B2___birth, S2___save
  STATE_helper state_helper_15 (
    .input_state(input_state), .output_state(state_helper_15_output_state), .i(I), .j(J[14]));
  neighbours neighbours_16 (
    .minus_02_02(minus_2_line[13]), .minus_02_01(minus_2_line[14]), .minus_02_00(minus_2_line[15]),
    .minus_02_01_2(minus_02_16), .minus_02_02_2(minus_02_17), .minus_01_02(minus_1_line[13]),
    .minus_01_01(minus_1_line[14]), .minus_01_00(minus_1_line[15]), .minus_01_01_2(minus_01_16),
    .minus_01_02_2(minus_01_17), .plus_00_02(_0_line__out__1[13]), .plus_00_01(_0_line__out__1[14]),
    .plus_00_00(_0_line__out__1[15]), .neighbours(neighbours_16_neighbours), .plus_00_01_2(plus_00_16),
    .plus_00_02_2(plus_00_17), .plus_01_02(_1_line[13]), .plus_01_01(_1_line[14]), .plus_01_00(_1_line[15]),
    .plus_01_01_2(plus_01_16), .plus_01_02_2(plus_01_17), .plus_02_02(_2_line[13]), .plus_02_01(_2_line[14]),
    .plus_02_00(_2_line[15]), .plus_02_01_2(plus_02_16), .plus_02_02_2(plus_02_17));
  alive alive_16 (
    .neighbours(neighbours_16_neighbours), .look_at(lookAt), .B1___birth(birth1), .S1___save(save1),
    .alive(plus_00_15new), .pause(pause), .input_state(state_helper_16_output_state));  // open: B2___birth, S2___save
  STATE_helper state_helper_16 (
    .input_state(input_state), .output_state(state_helper_16_output_state), .i(I), .j(J[15]));

  assign _0_line__out__1_2 = _0_line__out__1;
  assign _0_line__out__2 = _0_line__out__1;
  assign _0_line__out__2_2 = _0_line__out__1;
  assign display = _0_line__out__1;

  // Other names for the same wires on the sheet: plus_01_00 = _1_line[0]; plus_01_01 = _1_line[1];
  //   plus_01_02 = _1_line[2]; plus_01_03 = _1_line[3]; plus_01_04 = _1_line[4]; plus_01_05 = _1_line[5];
  //   plus_01_06 = _1_line[6]; plus_01_07 = _1_line[7]; plus_01_08 = _1_line[8]; plus_01_09 = _1_line[9];
  //   plus_01_10 = _1_line[10]; plus_01_11 = _1_line[11]; plus_01_12 = _1_line[12]; plus_01_13 = _1_line[13];
  //   plus_01_14 = _1_line[14]; plus_01_15 = _1_line[15]; plus_02_00 = _2_line[0]; plus_02_01 = _2_line[1];
  //   plus_02_02 = _2_line[2]; plus_02_03 = _2_line[3]; plus_02_04 = _2_line[4]; plus_02_05 = _2_line[5];
  //   plus_02_06 = _2_line[6]; plus_02_07 = _2_line[7]; plus_02_08 = _2_line[8]; plus_02_09 = _2_line[9];
  //   plus_02_10 = _2_line[10]; plus_02_11 = _2_line[11]; plus_02_12 = _2_line[12]; plus_02_13 = _2_line[13];
  //   plus_02_14 = _2_line[14]; plus_02_15 = _2_line[15]; birth[29:0] = birth1; plus_00_00 = _0_line__out__1[0];
  //   plus_00_01 = _0_line__out__1[1]; plus_00_02 = _0_line__out__1[2]; plus_00_03 = _0_line__out__1[3];
  //   plus_00_04 = _0_line__out__1[4]; plus_00_05 = _0_line__out__1[5]; plus_00_06 = _0_line__out__1[6];
  //   plus_00_07 = _0_line__out__1[7]; plus_00_08 = _0_line__out__1[8]; plus_00_09 = _0_line__out__1[9];
  //   plus_00_10 = _0_line__out__1[10]; plus_00_11 = _0_line__out__1[11]; plus_00_12 = _0_line__out__1[12];
  //   plus_00_13 = _0_line__out__1[13]; plus_00_14 = _0_line__out__1[14]; plus_00_15 = _0_line__out__1[15];
  //   minus_01_00 = minus_1_line[0]; minus_01_01 = minus_1_line[1]; minus_01_02 = minus_1_line[2];
  //   minus_01_03 = minus_1_line[3]; minus_01_04 = minus_1_line[4]; minus_01_05 = minus_1_line[5];
  //   minus_01_06 = minus_1_line[6]; minus_01_07 = minus_1_line[7]; minus_01_08 = minus_1_line[8];
  //   minus_01_09 = minus_1_line[9]; minus_01_10 = minus_1_line[10]; minus_01_11 = minus_1_line[11];
  //   minus_01_12 = minus_1_line[12]; minus_01_13 = minus_1_line[13]; minus_01_14 = minus_1_line[14];
  //   minus_01_15 = minus_1_line[15]; minus_02_00 = minus_2_line[0]; minus_02_01 = minus_2_line[1];
  //   minus_02_02 = minus_2_line[2]; minus_02_03 = minus_2_line[3]; minus_02_04 = minus_2_line[4];
  //   minus_02_05 = minus_2_line[5]; minus_02_06 = minus_2_line[6]; minus_02_07 = minus_2_line[7];
  //   minus_02_08 = minus_2_line[8]; minus_02_09 = minus_2_line[9]; minus_02_10 = minus_2_line[10];
  //   minus_02_11 = minus_2_line[11]; minus_02_12 = minus_2_line[12]; minus_02_13 = minus_2_line[13];
  //   minus_02_14 = minus_2_line[14]; minus_02_15 = minus_2_line[15]; save[29:0] = save1; state[1:0] = input_state

  // Notes on the sheet:
  //   save1: pull=down
  //   birth2: pull=down
  //   pause: pull=down
  //   lookAt: pull=down
  //   birth1: pull=down
  //   clock: pull=down
  //   save2: pull=down
  //   clear: pull=down
  //   enable: pull=down
  //   if the game is paused, there will be no
  //   further iterations, but cursor can work
endmodule

module alive (
  input  [24:0] neighbours,
  input  [24:0] look_at,
  input  pause,
  input  [1:0] input_state,
  input  [29:0] B1___birth,
  input  [29:0] B2___birth,
  input  [29:0] S1___save,
  input  [29:0] S2___save,
  output alive
);

  wire can_birth_out_14, can_save_out_14, multiplexer_1_out, multiplexer_2_out, xor_1_out;
  wire [4:0] newCnt;
  wire [24:0] and_1_out;

  assign and_1_out = neighbours & look_at;  // AND_Gate and_1, 25 bits wide
  // Probe on newCnt
  BitAdder #(.width(25)) bitadder_1 (.in0(and_1_out), .out(newCnt));
  OR12 can_birth (
    ._1(B1___birth[4:0]), ._2(B1___birth[9:5]), ._3(B1___birth[14:10]), ._4(B1___birth[19:15]),
    ._5(B1___birth[24:20]), ._6(B1___birth[29:25]), ._7(B2___birth[4:0]), ._8(B2___birth[9:5]),
    ._9(B2___birth[14:10]), ._10(B2___birth[19:15]), ._11(B2___birth[24:20]), ._12(B2___birth[29:25]),
    .newCnt(newCnt), .out_14(can_birth_out_14));
  Multiplexer #(.disabled(0)) multiplexer_1 (
    .in0(can_birth_out_14), .in1(can_save_out_14), .out(multiplexer_1_out), .sel(neighbours[12]));  // open: en
  OR12 can_save (
    ._1(S1___save[4:0]), ._2(S1___save[9:5]), ._3(S1___save[14:10]), ._4(S1___save[19:15]),
    ._5(S1___save[24:20]), ._6(S1___save[29:25]), ._7(S2___save[4:0]), ._8(S2___save[9:5]),
    ._9(S2___save[14:10]), ._10(S2___save[19:15]), ._11(S2___save[24:20]), ._12(S2___save[29:25]),
    .newCnt(newCnt), .out_14(can_save_out_14));
  xor xor_1 (xor_1_out, neighbours[12], input_state[0]);
  Multiplexer #(.disabled(0)) multiplexer_2 (
    .in0(xor_1_out), .in1(input_state[0]), .out(multiplexer_2_out), .sel(input_state[1]));  // open: en
  Pull_Resistor pull_resistor_1 (.node(alive));
  Multiplexer #(.disabled(0)) multiplexer_3 (
    .in0(multiplexer_1_out), .in1(multiplexer_2_out), .out(alive), .sel(pause));  // open: en

  // Other names for the same wires on the sheet: B1[4:0] = B1___birth[4:0]; B2[4:0] = B1___birth[9:5];
  //   B3[4:0] = B1___birth[14:10]; B4[4:0] = B1___birth[19:15]; B5[4:0] = B1___birth[24:20];
  //   B6[4:0] = B1___birth[29:25]; B7[4:0] = B2___birth[4:0]; B8[4:0] = B2___birth[9:5]; B9[4:0] = B2___birth[14:10];
  //   B10[4:0] = B2___birth[19:15]; B11[4:0] = B2___birth[24:20]; B12[4:0] = B2___birth[29:25]; cur = neighbours[12];
  //   S1[4:0] = S1___save[4:0]; S2[4:0] = S1___save[9:5]; S3[4:0] = S1___save[14:10]; S4[4:0] = S1___save[19:15];
  //   S5[4:0] = S1___save[24:20]; S6[4:0] = S1___save[29:25]; S7[4:0] = S2___save[4:0]; S8[4:0] = S2___save[9:5];
  //   S9[4:0] = S2___save[14:10]; S10[4:0] = S2___save[19:15]; S11[4:0] = S2___save[24:20];
  //   S12[4:0] = S2___save[29:25]

  // Notes on the sheet:
  //   S2___save: pull=up
  //   S1___save: pull=up
  //   B2___birth: pull=up
  //   neighbours: pull=down
  //   input_state: pull=down
  //   B1___birth: pull=up
  //   look_at: pull=down
  //   floating → 0
  //   floating → 0
  //   number of neighbours
  //   ▒ — neighbours
  //   ▓ — current cell
  //   ▒ ▒ ▒ ▒ ▒
  //   ▒ ▒ ▒ ▒ ▒
  //   ▒ ▒ ▓ ▒ ▒
  //   ▒ ▒ ▒ ▒ ▒
  //   ▒ ▒ ▒ ▒ ▒
  //   birth rules
  //   save rules
  //   if cur cell is dead (= 0) try birth ↑
  //   alive (= 1) — try save ↓
  //   old or invert
  //   new: 0 or 1
  //   new iteration
  //   by state
  //   00 — old
  //   01 — invert
  //   10 — set DEAD
  //   11 — set ALIVE
endmodule

module neighbours (
  input  minus_02_02,
  input  minus_02_01,
  input  minus_02_00,
  input  minus_02_01_2,
  input  minus_02_02_2,
  input  minus_01_02,
  input  minus_01_01,
  input  minus_01_00,
  input  minus_01_01_2,
  input  minus_01_02_2,
  input  plus_00_02,
  input  plus_00_01,
  input  plus_00_00,
  input  plus_00_01_2,
  input  plus_00_02_2,
  input  plus_01_02,
  input  plus_01_01,
  input  plus_01_00,
  input  plus_01_01_2,
  input  plus_01_02_2,
  input  plus_02_02,
  input  plus_02_01,
  input  plus_02_00,
  input  plus_02_01_2,
  input  plus_02_02_2,
  output [24:0] neighbours
);


  assign neighbours = {plus_02_02_2, plus_02_01_2, plus_02_00, plus_02_01, plus_02_02, plus_01_02_2, plus_01_01_2, plus_01_00, plus_01_01, plus_01_02, plus_00_02_2, plus_00_01_2, plus_00_00, plus_00_01, plus_00_02, minus_01_02_2, minus_01_01_2, minus_01_00, minus_01_01, minus_01_02, minus_02_02_2, minus_02_01_2, minus_02_00, minus_02_01, minus_02_02};
endmodule

module BS_helper (
  input  [5:0] input_6_bit,
  output [4:0] output_5_bit
);

  Multiplexer #(.width(5)) multiplexer_1 (
    .in0(input_6_bit[4:0]), .in1({5{1'b1}}), .out(output_5_bit), .sel(input_6_bit[5]));  // open: en
endmodule

// BS-0->31
module BS_helper_0__31 (
  input  [5:0] input_6_bit,
  output [4:0] output_5_bit
);

  wire nor_1_out, or_1_out;

  nor nor_1 (nor_1_out, input_6_bit[4], input_6_bit[3], input_6_bit[2], input_6_bit[1], input_6_bit[0]);
  or or_1 (or_1_out, nor_1_out, input_6_bit[5]);
  Multiplexer #(.width(5)) multiplexer_1 (
    .in0(input_6_bit[4:0]), .in1({5{1'b1}}), .out(output_5_bit), .sel(or_1_out));  // open: en
endmodule

module STATE_helper (
  input  [1:0] input_state,
  input  i,
  input  j,
  output [1:0] output_state
);

  wire [1:1] and_2_out;

  assign output_state = input_state & {2{and_2_out[1]}};  // AND_Gate and_1, 2 bits wide
  and and_2 (and_2_out[1], i, j);

  // Notes on the sheet:
  //   i: pull=down
  //   j: pull=down
  //   if cursor there, out = input state. Otherwise out = 00
endmodule

module reverse16Bits (
  input  [15:0] in,
  output [15:0] out
);


  assign out = {in[0], in[1], in[2], in[3], in[4], in[5], in[6], in[7], in[8], in[9], in[10], in[11], in[12], in[13], in[14], in[15]};

  // Notes on the sheet:
  //   in: pull=down
  //   out: pull=down
endmodule

// newCnt == _?
module OR12 (
  input  [4:0] newCnt,
  input  [4:0] _1,
  input  [4:0] _2,
  input  [4:0] _3,
  input  [4:0] _4,
  input  [4:0] _5,
  input  [4:0] _6,
  input  [4:0] _7,
  input  [4:0] _8,
  input  [4:0] _9,
  input  [4:0] _10,
  input  [4:0] _11,
  input  [4:0] _12,
  output out_14
);

  wire comparator_1_eq, comparator_2_eq, comparator_3_eq, comparator_4_eq, comparator_5_eq, comparator_6_eq,
       comparator_7_eq, comparator_8_eq, comparator_9_eq, comparator_10_eq, comparator_11_eq,
       comparator_12_eq;

  Comparator #(.width(5), .mode("unsigned")) comparator_1 (.a(newCnt), .b(_1), .eq(comparator_1_eq));  // open: gt, lt
  Comparator #(.width(5), .mode("unsigned")) comparator_2 (.a(newCnt), .b(_2), .eq(comparator_2_eq));  // open: gt, lt
  Comparator #(.width(5), .mode("unsigned")) comparator_3 (.a(newCnt), .b(_3), .eq(comparator_3_eq));  // open: gt, lt
  Comparator #(.width(5), .mode("unsigned")) comparator_4 (.a(newCnt), .b(_4), .eq(comparator_4_eq));  // open: gt, lt
  Comparator #(.width(5), .mode("unsigned")) comparator_5 (.a(newCnt), .b(_5), .eq(comparator_5_eq));  // open: gt, lt
  Comparator #(.width(5), .mode("unsigned")) comparator_6 (.a(newCnt), .b(_6), .eq(comparator_6_eq));  // open: gt, lt
  Comparator #(.width(5), .mode("unsigned")) comparator_7 (.a(newCnt), .b(_7), .eq(comparator_7_eq));  // open: gt, lt
  Comparator #(.width(5), .mode("unsigned")) comparator_8 (.a(newCnt), .b(_8), .eq(comparator_8_eq));  // open: gt, lt
  Comparator #(.width(5), .mode("unsigned")) comparator_9 (.a(newCnt), .b(_9), .eq(comparator_9_eq));  // open: gt, lt
  Comparator #(.width(5), .mode("unsigned")) comparator_10 (
    .a(newCnt), .b(_10), .eq(comparator_10_eq));  // open: gt, lt
  Comparator #(.width(5), .mode("unsigned")) comparator_11 (
    .a(newCnt), .b(_11), .eq(comparator_11_eq));  // open: gt, lt
  Comparator #(.width(5), .mode("unsigned")) comparator_12 (
    .a(newCnt), .b(_12), .eq(comparator_12_eq));  // open: gt, lt
  or can_cell (out_14, comparator_1_eq, comparator_2_eq, comparator_3_eq, comparator_4_eq, comparator_5_eq, comparator_6_eq, comparator_7_eq, comparator_8_eq, comparator_9_eq, comparator_10_eq, comparator_11_eq, comparator_12_eq);

  // Notes on the sheet:
  //   _8: pull=down
  //   _3: pull=down
  //   _6: pull=down
  //   _5: pull=down
  //   _10: pull=down
  //   _12: pull=down
  //   _7: pull=down
  //   _11: pull=down
  //   _1: pull=down
  //   _4: pull=down
  //   newCnt: pull=down
  //   _2: pull=down
  //   _9: pull=down
endmodule

module text (
  input  in_1,
  output out_2,
  output out_3,
  output out_4,
  output out_5,
  output out_6,
  output out_7,
  output out_8,
  output out_9,
  output out_10,
  output out_11,
  output out_12,
  output out_13,
  output out_14,
  output out_15,
  output out_16,
  output out_17,
  output out_18,
  output out_19,
  output out_20,
  output out_21,
  output out_22,
  output out_23,
  output out_24,
  output out_25,
  output out_26,
  output out_27,
  output out_28,
  output out_29,
  output out_30,
  output out_31,
  output out_32,
  output out_33,
  output out_34,
  output out_35,
  output out_36,
  output out_37,
  output out_38,
  output out_39,
  output out_40,
  output out_41,
  output out_42,
  output out_43,
  output out_44,
  output out_45,
  output out_46,
  output out_47,
  output out_48,
  output out_49,
  output out_50,
  output out_51,
  output out_52,
  output out_53,
  output out_54,
  output out_55,
  output out_56,
  output out_57,
  output out_58,
  output out_59,
  output out_60,
  output out_61,
  output out_62,
  output out_63,
  output out_64,
  output out_65
);

  Multiplexer #(.width(4), .disabled(0), .enable("false")) multiplexer_1 (
    .in0(4'b0100), .in1(4'b1111), .out({out_18, out_2, out_19, out_3}), .sel(in_1));
  Multiplexer #(.width(4), .disabled(0), .enable("false")) multiplexer_2 (
    .in0(4'b1100), .in1(4'b1000), .out({out_50, out_34, out_51, out_35}), .sel(in_1));
  Multiplexer #(.width(4), .disabled(0), .enable("false")) multiplexer_3 (
    .in0(4'b0111), .in1(4'b0100), .out({out_20, out_4, out_21, out_5}), .sel(in_1));
  Multiplexer #(.width(4), .disabled(0), .enable("false")) multiplexer_4 (
    .in0(4'b1110), .in1(4'b1100), .out({out_52, out_36, out_53, out_37}), .sel(in_1));
  Multiplexer #(.width(4), .disabled(0), .enable("false")) multiplexer_5 (
    .in0(4'b1111), .in1(4'b1111), .out({out_22, out_6, out_23, out_7}), .sel(in_1));
  Multiplexer #(.width(4), .disabled(0), .enable("false")) multiplexer_6 (
    .in0(4'b1010), .in1(4'b1010), .out({out_54, out_38, out_55, out_39}), .sel(in_1));
  Multiplexer #(.width(4), .disabled(0), .enable("false")) multiplexer_7 (
    .in0(4'b1001), .in1(4'b1101), .out({out_24, out_8, out_25, out_9}), .sel(in_1));
  Multiplexer #(.width(4), .disabled(0), .enable("false")) multiplexer_8 (
    .in0(4'b1110), .in1(4'b0110), .out({out_56, out_40, out_57, out_41}), .sel(in_1));
  Multiplexer #(.width(4), .disabled(0), .enable("false")) multiplexer_9 (
    .in0(4'b0001), .in1(4'b0000), .out({out_26, out_10, out_27, out_11}), .sel(in_1));
  Multiplexer #(.width(4), .disabled(0), .enable("false")) multiplexer_10 (
    .in0(4'b0010), .in1(4'b0000), .out({out_58, out_42, out_59, out_43}), .sel(in_1));
  Multiplexer #(.width(4), .disabled(0), .enable("false")) multiplexer_11 (
    .in0(4'b1000), .in1(4'b0001), .out({out_28, out_12, out_29, out_13}), .sel(in_1));
  Multiplexer #(.width(4), .disabled(0), .enable("false")) multiplexer_12 (
    .in0(4'b1010), .in1(4'b0010), .out({out_60, out_44, out_61, out_45}), .sel(in_1));
  Multiplexer #(.width(4), .disabled(0), .enable("false")) multiplexer_13 (
    .in0(4'b0110), .in1(4'b1100), .out({out_30, out_14, out_31, out_15}), .sel(in_1));
  Multiplexer #(.width(4), .disabled(0), .enable("false")) multiplexer_14 (
    .in0(4'b1110), .in1(4'b1100), .out({out_62, out_46, out_63, out_47}), .sel(in_1));
  Multiplexer #(.width(4), .disabled(0), .enable("false")) multiplexer_15 (
    .in0(4'b0000), .in1(4'b0001), .out({out_32, out_16, out_33, out_17}), .sel(in_1));
  Multiplexer #(.width(4), .disabled(0), .enable("false")) multiplexer_16 (
    .in0(4'b0101), .in1(4'b0011), .out({out_64, out_48, out_65, out_49}), .sel(in_1));

  // Notes on the sheet:
  //   in_1: pull=up
endmodule
