// Logisim project Buttons.circ as structural Verilog: 1 circuit, main circuit Buttons
module Buttons (
  input  in_1,
  input  in_2,
  input  in_3,
  input  in_4,
  output [3:0] out_5,
  output out_6
);

  or or_1 (out_6, in_1, in_2, in_3, in_4);

  assign out_5 = {in_4, in_3, in_2, in_1};
endmodule
