// Logisim project NSU-2023-T04L1e03.circ as structural Verilog: 1 circuit, main circuit mycircuit
module mycircuit (
  input  A,
  input  B,
  input  C,
  output R
);

  wire or_1_out;

  or or_1 (or_1_out, B, C);
  not not_1 (R, or_1_out);
endmodule
