// Logisim project NSU-2023-T04L1e05.circ as structural Verilog: 1 circuit, main circuit mycircuit
module mycircuit (
  input  A,
  input  B,
  input  C,
  output R
);

  wire and_1_out;

  and and_1 (and_1_out, A, B, C);
  not not_1 (R, and_1_out);
endmodule
