// Logisim project NSU-2023-T04L1e07.circ as structural Verilog: 1 circuit, main circuit mycircuit
module mycircuit (
  input  A,
  input  B,
  input  C,
  output R
);

  wire and_1_out, and_2_out, not_1_out, not_2_out, not_3_out;

  not not_1 (not_1_out, B);
  and and_1 (and_1_out, C, not_1_out, A);
  not not_2 (not_2_out, A);
  and and_2 (and_2_out, not_2_out, B, not_3_out);
  not not_3 (not_3_out, C);
  or or_1 (R, and_1_out, and_2_out);
endmodule
