// Logisim project NSU-2023-T04L3e01.circ as structural Verilog: 1 circuit, main circuit formula
module formula (
  input  A,
  input  B,
  input  C,
  output R
);

  wire transistor_1_out, transistor_3_out;

  Transistor transistor_1 (.in(1'b1), .out(transistor_1_out), .gate(A));
  Transistor transistor_2 (.in(1'b1), .out(transistor_1_out), .gate(B));
  Transistor transistor_3 (.in(transistor_1_out), .out(transistor_3_out), .gate(B));
  Transistor transistor_4 (.in(transistor_3_out), .out(R), .gate(A));
  Transistor transistor_5 (.in(transistor_1_out), .out(R), .gate(C));
  Pull_Resistor pull_resistor_1 (.node(R));
endmodule
