// Logisim project NSU-2023-T05L3e02.circ as structural Verilog: 1 circuit, main circuit cmp
module cmp (
  input  [7:0] A,
  input  [7:0] B,
  output Gt,
  output Eq
);

  wire and_2_out, and_7_out, nand_1_out, not_2_out, not_3_out, not_5_out, or_2_out, or_3_out;
  wire [7:0] and_1_out, and_3_out, and_4_out, and_5_out, not_1_out, xor_1_out, xor_2_out;
  wire [7:1] or_1_out;
  wire [7:7] or_1_out_2;

  assign not_1_out = ~B;  // NOT_Gate not_1, 8 bits wide
  assign and_1_out = {and_1_out[6:0], 1'b1} & not_1_out;  // AND_Gate and_1, 8 bits wide
  assign xor_1_out = not_1_out ^ {and_1_out[6:0], 1'b1};  // XOR_Gate xor_1, 8 bits wide
  not not_2 (not_2_out, B[7]);
  nand nand_1 (nand_1_out, not_3_out, B[7]);
  and and_2 (and_2_out, A[7], not_2_out);
  not not_3 (not_3_out, A[7]);
  assign and_3_out = A & xor_1_out;  // AND_Gate and_3, 8 bits wide
  assign and_4_out = xor_1_out & {or_1_out, 1'b0};  // AND_Gate and_4, 8 bits wide
  assign and_5_out = A & {or_1_out, 1'b0};  // AND_Gate and_5, 8 bits wide
  assign {or_1_out_2[7], or_1_out} = and_3_out | and_4_out | and_5_out;  // OR_Gate or_1, 8 bits wide
  and and_6 (Gt, nand_1_out, or_2_out);
  or or_2 (or_2_out, and_2_out, and_7_out);
  and and_7 (and_7_out, not_5_out, or_3_out);
  not not_4 (Eq, or_3_out);
  not not_5 (not_5_out, xor_2_out[7]);
  assign xor_2_out = A ^ {or_1_out, 1'b0} ^ xor_1_out;  // XOR_Gate xor_2, 8 bits wide
  or or_3 (or_3_out, xor_2_out[0], xor_2_out[1], xor_2_out[2], xor_2_out[3], xor_2_out[4], xor_2_out[5], xor_2_out[6], xor_2_out[7]);

  // Notes on the sheet:
  //   A: pull=up
endmodule
