// Logisim project input-controller.circ as structural Verilog: 1 circuit, main circuit input_controller
module input_controller (
  input  [15:0] data__start___0,
  input  [15:0] data__from_memory,
  input  [15:0] data__start___1,
  input  read_write,
  input  [15:0] data__start___2,
  input  memory__proc,
  input  [15:0] data__start___3,
  input  clock,
  input  [15:0] data__start___4,
  input  [15:0] address,
  input  [15:0] data__start___5,
  input  [11:0] start_address,
  input  [15:0] data__start___6,
  input  [15:0] data__start___7,
  input  [15:0] data__start___8,
  input  [15:0] data__start___9,
  input  [15:0] data__start___10,
  input  [15:0] data__start___11,
  input  [15:0] data__start___12,
  input  [15:0] data__start___13,
  input  [15:0] data__start___14,
  input  [15:0] data__start___15,
  output memory__device,
  output [15:0] data__out
);

  wire and_2_out, and_3_out, and_4_out, and_5_out, and_6_out, and_7_out, not_1_out;
  wire [11:0] xnor_1_out;
  wire [15:0] multiplexer_1_out;

  and and_1 (memory__device, memory__proc, not_1_out);
  not not_1 (not_1_out, and_6_out);
  assign xnor_1_out = ~(address[15:4] ^ start_address);  // XNOR_Gate xnor_1, 12 bits wide
  and and_2 (and_2_out, and_3_out, and_4_out, and_5_out, and_7_out);
  assign data__from_memory = and_6_out ? multiplexer_1_out : 16'bz;  // Controlled_Buffer controlled_buffer_1
  and and_3 (and_3_out, xnor_1_out[11], xnor_1_out[10], xnor_1_out[9]);
  and and_4 (and_4_out, xnor_1_out[8], xnor_1_out[7], xnor_1_out[6]);
  and and_5 (and_5_out, xnor_1_out[5], xnor_1_out[4], xnor_1_out[3]);
  and and_6 (and_6_out, read_write, clock, and_2_out);
  Multiplexer #(.select(4), .width(16)) multiplexer_1 (
    .in0(data__start___0), .in1(data__start___1), .in2(data__start___2), .in3(data__start___3),
    .in4(data__start___4), .in5(data__start___5), .in6(data__start___6), .in7(data__start___7),
    .in8(data__start___8), .in9(data__start___9), .in10(data__start___10), .in11(data__start___11),
    .in12(data__start___12), .in13(data__start___13), .in14(data__start___14), .in15(data__start___15),
    .out(multiplexer_1_out), .sel(address[3:0]), .en(1'b1));
  and and_7 (and_7_out, xnor_1_out[2], xnor_1_out[1], xnor_1_out[0]);
  Pull_Resistor pull_resistor_1 (.node(data__start___0));
  Pull_Resistor pull_resistor_2 (.node(data__start___1));
  Pull_Resistor pull_resistor_3 (.node(data__start___2));
  Pull_Resistor pull_resistor_4 (.node(data__start___3));
  Pull_Resistor pull_resistor_5 (.node(data__start___4));
  Pull_Resistor pull_resistor_6 (.node(data__start___5));
  Pull_Resistor pull_resistor_7 (.node(data__start___6));
  Pull_Resistor pull_resistor_8 (.node(data__start___7));
  Pull_Resistor pull_resistor_9 (.node(data__start___8));
  Pull_Resistor pull_resistor_10 (.node(data__start___9));
  Pull_Resistor pull_resistor_11 (.node(data__start___10));
  Pull_Resistor pull_resistor_12 (.node(data__start___11));
  Pull_Resistor pull_resistor_13 (.node(data__start___12));
  Pull_Resistor pull_resistor_14 (.node(data__start___13));
  Pull_Resistor pull_resistor_15 (.node(data__start___14));
  Pull_Resistor pull_resistor_16 (.node(data__start___15));

  assign data__out = data__from_memory;

  // Other names for the same wires on the sheet: read_wrt = read_write; s00[15:0] = data__start___0;
  //   s01[15:0] = data__start___1; s02[15:0] = data__start___2; s03[15:0] = data__start___3;
  //   s04[15:0] = data__start___4; s05[15:0] = data__start___5; s06[15:0] = data__start___6;
  //   s07[15:0] = data__start___7; s08[15:0] = data__start___8; s09[15:0] = data__start___9;
  //   s10[15:0] = data__start___10; s11[15:0] = data__start___11; s12[15:0] = data__start___12;
  //   s13[15:0] = data__start___13; s14[15:0] = data__start___14; s15[15:0] = data__start___15
endmodule
